// Logisim project 单周期中断嵌套_硬件堆栈.circ as structural Verilog: 19 circuits, main circuit ◇单周期MIPS+多级中断
module \单周期MIPS_多级中断  (
  input  IR1,
  input  IR2,
  input  IR3,
  output RegWrite,
  output MemWrite,
  output [31:0] PC,
  output [31:0] IR,
  output [31:0] RDin,
  output [31:0] MDin,
  output [31:0] LedData
);

  wire and_3_out, and_4_out, and_5_out, and_6_out, CLK, comparator_1_eq, comparator_2_eq, d_ff_1_q, d_ff_2_q,
       d_ff_3_q, demultiplexer_1_out1, demultiplexer_1_out2, demultiplexer_1_out3, ERET, Go, I_Branch, IR1_t,
       IR2_t, IR3_t, IRA, IRB, IRC, LHU, MFC0, mips_alu_1_equal, MTC0, multiplexer_1_out, multiplexer_10_out,
       multiplexer_11_out, multiplexer_14_out, multiplexer_17_out, not_1_out, not_2_out, not_3_out,
       not_4_out, not_5_out, or_4_out, or_5_out, or_6_out, or_7_out, or_8_out, priority_encoder_1_en_out,
       priority_encoder_1_gs, SignedExt, stop, W1, W2, W3, \中断CPU , \中断使能_q , \单周期硬布线控制器_1_alu_src ,
       \单周期硬布线控制器_1_beq , \单周期硬布线控制器_1_bgez , \单周期硬布线控制器_1_bne , \单周期硬布线控制器_1_jal , \单周期硬布线控制器_1_jmp ,
       \单周期硬布线控制器_1_jr , \单周期硬布线控制器_1_memtoreg , \单周期硬布线控制器_1_regdst , \单周期硬布线控制器_1_shamtsrc ,
       \单周期硬布线控制器_1_syscall ;
  wire [1:0] multiplexer_6_out, \n2位硬件堆栈_1_dataout , priority_encoder_1_out, register_1_q;
  wire [2:0] IR1_q;
  wire [3:0] \单周期硬布线控制器_1_alu_op ;
  wire [4:0] mips_regifile_1_r1, multiplexer_8_out, multiplexer_12_out, multiplexer_13_out,
       multiplexer_15_out, multiplexer_20_out;
  wire [15:0] multiplexer_23_out, \总周期数 , \无条件分支数 , \条件分支成功数 ;
  wire [31:0] adder_1_out, adder_2_out, bit_extender_1_out, bit_extender_2_out, mips_alu_1_result,
       multiplexer_2_out, multiplexer_3_out, multiplexer_4_out, multiplexer_5_out, multiplexer_7_out,
       multiplexer_19_out, multiplexer_21_out, multiplexer_22_out, newPC, ram_1_data, \硬件堆栈_1_dataout ;
  wire [31:2] multiplexer_9_out;
  wire [31:5] mips_regifile_1_r1_2;
  wire [31:30] multiplexer_9_out_2;

  Clock #(.highDuration(1), .lowDuration(1)) clock_1 (.out(CLK));
  Button _1 (.out(IRA));
  Button _2 (.out(IRB));
  Button _3 (.out(IRC));
  not not_1 (not_1_out, stop);
  Multiplexer #(.select(1), .width(1), .disabled("Z"), .enable("false")) multiplexer_1 (
    .in0(not_1_out), .in1(stop), .out(multiplexer_1_out), .sel(Go));
  Button \u_继续运行  (.out(Go));
  LED #(.active("true")) led_1 (.in(W1));
  LED #(.active("true")) led_2 (.in(W2));
  LED #(.active("true")) led_3 (.in(W3));
  Counter #(.width(16), .max('hffff), .ongoal("wrap"), .trigger("rising"), .behavior("new")) counter_1 (
    .load(1'b0), .D({16{1'b0}}), .count(multiplexer_1_out), .Q(\总周期数 ), .clk(CLK), .preset(1'b0), .down(1'b0));  // open: carry, clr
  or or_1 (W1, IR1_q[0], d_ff_1_q);
  or or_2 (W2, IR1_q[1], d_ff_2_q);
  or or_3 (W3, IR1_q[2], d_ff_3_q);
  Hex_Digit_Display hex_digit_display_1 (.value(LedData[31:28]));  // open: dp
  Counter #(.width(16), .max('hffff), .ongoal("wrap"), .trigger("rising"), .behavior("new")) counter_2 (
    .load(1'b0), .D({16{1'b0}}), .count(or_7_out), .Q(\无条件分支数 ), .clk(CLK), .preset(1'b0), .down(1'b0));  // open: carry, clr
  Register #(.width(32), .trigger("rising"), .Select("low")) u_PC (
    .D(newPC), .en(multiplexer_1_out), .Q(PC), .clk(CLK));  // open: clr
  D_Flip_Flop #(.trigger("rising"), .Pre_Clr_Positions("LEGACY"), .NegatePresetClear("false"), .enable("true"), .NewFFLayout("false")) d_ff_1 (
    .clk(IR1_t), .D(1'b1), .Q(d_ff_1_q), .reset(IR1_q[0]));  // open: Qn, preset, en
  D_Flip_Flop #(.trigger("rising"), .Pre_Clr_Positions("LEGACY"), .NegatePresetClear("false"), .enable("true"), .NewFFLayout("false")) d_ff_2 (
    .clk(IR2_t), .D(1'b1), .Q(d_ff_2_q), .reset(IR1_q[1]));  // open: Qn, preset, en
  D_Flip_Flop #(.trigger("rising"), .Pre_Clr_Positions("LEGACY"), .NegatePresetClear("false"), .enable("true"), .NewFFLayout("false")) d_ff_3 (
    .clk(IR3_t), .D(1'b1), .Q(d_ff_3_q), .reset(IR1_q[2]));  // open: Qn, preset, en
  Hex_Digit_Display hex_digit_display_2 (.value(LedData[23:20]));  // open: dp
  Hex_Digit_Display hex_digit_display_3 (.value(LedData[27:24]));  // open: dp
  or or_4 (or_4_out, d_ff_1_q, IR1_q[0]);
  or or_5 (or_5_out, d_ff_2_q, IR1_q[1]);
  or or_6 (or_6_out, d_ff_3_q, IR1_q[2]);
  Hex_Digit_Display hex_digit_display_4 (.value(LedData[19:16]));  // open: dp
  Hex_Digit_Display hex_digit_display_5 (.value(LedData[15:12]));  // open: dp
  or or_7 (or_7_out, \单周期硬布线控制器_1_jmp , \单周期硬布线控制器_1_jr );
  Adder #(.width(32)) adder_1 (.a(PC), .b(32'h4), .out(adder_1_out), .cin(1'b0));  // open: cout
  Hex_Digit_Display hex_digit_display_6 (.value(LedData[7:4]));  // open: dp
  Hex_Digit_Display hex_digit_display_7 (.value(LedData[11:8]));  // open: dp
  // Probe on \总周期数 
  Multiplexer #(.select(1), .width(32), .disabled(0), .enable("false")) multiplexer_2 (
    .in0(adder_1_out), .in1({mips_regifile_1_r1_2, mips_regifile_1_r1}), .out(multiplexer_2_out),
    .sel(\单周期硬布线控制器_1_jr ));
  Multiplexer #(.select(1), .width(32), .disabled(0), .enable("false")) multiplexer_3 (
    .in0(multiplexer_2_out), .in1(adder_2_out), .out(multiplexer_3_out), .sel(I_Branch));
  Adder #(.width(32)) adder_2 (
    .a(adder_1_out), .b({multiplexer_9_out, 2'b00}), .out(adder_2_out), .cin(1'b0));  // open: cout
  \硬件堆栈  \u_硬件堆栈_1  (.data(multiplexer_5_out), .clk(CLK), .enable(\中断CPU ), .dataOut(\硬件堆栈_1_dataout ), .eret(ERET));
  D_Flip_Flop #(.trigger("rising"), .Pre_Clr_Positions("LEGACY"), .NegatePresetClear("false"), .enable("true"), .NewFFLayout("false")) u_IR1 (
    .clk(CLK), .D(or_4_out), .Q(IR1_q[0]), .reset(demultiplexer_1_out1));  // open: Qn, preset, en
  D_Flip_Flop #(.trigger("rising"), .Pre_Clr_Positions("LEGACY"), .NegatePresetClear("false"), .enable("true"), .NewFFLayout("false")) u_IR2 (
    .clk(CLK), .D(or_5_out), .Q(IR1_q[1]), .reset(demultiplexer_1_out2));  // open: Qn, preset, en
  D_Flip_Flop #(.trigger("rising"), .Pre_Clr_Positions("LEGACY"), .NegatePresetClear("false"), .enable("true"), .NewFFLayout("false")) u_IR3 (
    .clk(CLK), .D(or_6_out), .Q(IR1_q[2]), .reset(demultiplexer_1_out3));  // open: Qn, preset, en
  Hex_Digit_Display hex_digit_display_8 (.value(LedData[3:0]));  // open: dp
  Multiplexer #(.select(1), .width(32), .disabled("Z"), .enable("false")) multiplexer_4 (
    .in0(multiplexer_3_out), .in1({adder_1_out[31:28], IR[25:0], 2'b00}), .out(multiplexer_4_out),
    .sel(\单周期硬布线控制器_1_jmp ));
  // Mips_Probe mips_probe_1: pin names not known; wires that end beside it: IR
  Multiplexer #(.select(1), .width(32), .disabled("Z"), .enable("false")) multiplexer_5 (
    .in0(multiplexer_4_out), .in1(\硬件堆栈_1_dataout ), .out(multiplexer_5_out), .sel(ERET));
  not not_2 (not_2_out, priority_encoder_1_en_out);
  Priority_Encoder #(.select(2), .disabled("Z")) priority_encoder_1 (
    .in0(1'b0), .in1(IR1_q[0]), .in2(IR1_q[1]), .in3(IR1_q[2]), .out(priority_encoder_1_out),
    .gs(priority_encoder_1_gs), .en_out(priority_encoder_1_en_out), .en_in(1'b1));
  Multiplexer #(.select(1), .width(2), .disabled("Z"), .enable("false")) multiplexer_6 (
    .in0(2'b00), .in1(priority_encoder_1_out), .out(multiplexer_6_out), .sel(priority_encoder_1_gs));
  or or_8 (or_8_out, ERET, \中断CPU );
  or or_9 (IR1_t, IR1, IRA);
  ROM #(.addrWidth(10), .dataWidth(32), .Select("high")) rom_1 (.addr(PC[11:2]), .data(IR), .sel(1'b1));
  \_2位硬件堆栈  \u_2位硬件堆栈_1  (
    .data(multiplexer_6_out), .enable(or_8_out), .pop(ERET), .clk(CLK), .dataOut(\n2位硬件堆栈_1_dataout ));
  or or_10 (IR2_t, IR2, IRB);
  // Probe on priority_encoder_1_out
  Multiplexer #(.select(2), .width(32), .disabled("Z"), .enable("false")) multiplexer_7 (
    .in1(32'h30ac), .in2(32'h3158), .in3(32'h3204), .out(multiplexer_7_out), .sel(priority_encoder_1_out));  // open: in0
  Register #(.width(2), .trigger("rising"), .Select("low")) register_1 (
    .D(\n2位硬件堆栈_1_dataout ), .Q(register_1_q), .clk(CLK));  // open: en, clr
  Demultiplexer #(.select(2), .width(1), .tristate("false"), .disabled("Z"), .enable("false")) demultiplexer_1 (
    .out1(demultiplexer_1_out1), .out2(demultiplexer_1_out2), .out3(demultiplexer_1_out3), .in(ERET),
    .sel(register_1_q));  // open: out0
  \单周期硬布线控制器  \u_单周期硬布线控制器_1  (
    .Func(IR[5:0]), .OP(IR[31:26]), .ALU_OP(\单周期硬布线控制器_1_alu_op ), .MemToReg(\单周期硬布线控制器_1_memtoreg ),
    .MemWrite(MemWrite), .ALU_SRC(\单周期硬布线控制器_1_alu_src ), .SysCALL(\单周期硬布线控制器_1_syscall ),
    .SignedExt(SignedExt), .RegDst(\单周期硬布线控制器_1_regdst ), .JR(\单周期硬布线控制器_1_jr ), .JMP(\单周期硬布线控制器_1_jmp ),
    .Beq(\单周期硬布线控制器_1_beq ), .JAL(\单周期硬布线控制器_1_jal ), .Bne(\单周期硬布线控制器_1_bne ),
    .ShamtSrc(\单周期硬布线控制器_1_shamtsrc ), .LHU(LHU), .BGEZ(\单周期硬布线控制器_1_bgez ), .ERET(ERET), .CPsrc(IR[25:21]),
    .MFC0(MFC0), .MTC0(MTC0), .RegWrite(RegWrite));  // open: COP0
  Multiplexer #(.select(1), .width(5), .disabled("Z"), .enable("false")) multiplexer_8 (
    .in0(IR[25:21]), .in1(5'b00010), .out(multiplexer_8_out), .sel(\单周期硬布线控制器_1_syscall ));
  assign bit_extender_1_out = {{16{1'b0}}, IR[15:0]};  // Bit_Extender bit_extender_1
  Multiplexer #(.select(1), .width(32), .disabled("Z"), .enable("false")) multiplexer_9 (
    .in0(bit_extender_1_out), .in1(bit_extender_2_out), .out({multiplexer_9_out_2, multiplexer_9_out}),
    .sel(SignedExt));
  assign bit_extender_2_out = {{16{IR[15]}}, IR[15:0]};  // Bit_Extender bit_extender_2
  Multiplexer #(.select(1), .width(1), .disabled("Z"), .enable("false")) multiplexer_10 (
    .in0(\中断使能_q ), .in1(1'b1), .out(multiplexer_10_out), .sel(\中断CPU ));
  Multiplexer #(.select(1), .width(1), .disabled("Z"), .enable("false")) multiplexer_11 (
    .in0(multiplexer_10_out), .in1(1'b0), .out(multiplexer_11_out), .sel(ERET));
  or or_11 (IR3_t, IR3, IRC);
  Multiplexer #(.select(1), .width(5), .disabled(0), .enable("false")) multiplexer_12 (
    .in0(IR[20:16]), .in1(5'b00100), .out(multiplexer_12_out), .sel(\单周期硬布线控制器_1_syscall ));
  Multiplexer #(.select(1), .width(5), .disabled(0), .enable("false")) multiplexer_13 (
    .in0(IR[20:16]), .in1(IR[15:11]), .out(multiplexer_13_out), .sel(\单周期硬布线控制器_1_regdst ));
  Multiplexer #(.select(1), .width(1), .disabled("Z"), .enable("false")) multiplexer_14 (
    .in0(multiplexer_11_out), .in1(1'b1), .out(multiplexer_14_out), .sel(MTC0));
  Multiplexer #(.select(1), .width(5), .disabled(0), .enable("false")) multiplexer_15 (
    .in0(multiplexer_13_out), .in1({5{1'b1}}), .out(multiplexer_15_out), .sel(\单周期硬布线控制器_1_jal ));
  Multiplexer #(.select(1), .width(32), .disabled(0), .enable("false")) multiplexer_16 (
    .in0(multiplexer_21_out), .in1(adder_1_out), .out(RDin), .sel(\单周期硬布线控制器_1_jal ));
  Multiplexer #(.select(1), .width(1), .disabled("Z"), .enable("false")) multiplexer_17 (
    .in0(multiplexer_14_out), .in1(1'b0), .out(multiplexer_17_out), .sel(MFC0));
  Comparator #(.width(2), .mode("twosComplement")) comparator_1 (
    .a(multiplexer_6_out), .b(\n2位硬件堆栈_1_dataout ), .eq(comparator_1_eq));  // open: gt, lt
  Register #(.width(1), .trigger("rising"), .Select("low")) \u_中断使能  (
    .D(multiplexer_17_out), .Q(\中断使能_q ), .clk(CLK));  // open: en, clr
  Multiplexer #(.select(1), .width(32), .disabled("Z"), .enable("false")) multiplexer_18 (
    .in0(multiplexer_5_out), .in1(multiplexer_7_out), .out(newPC), .sel(\中断CPU ));
  and and_1 (\中断CPU , not_2_out, ~\中断使能_q , ~comparator_1_eq);  // AND_Gate
  MIPS_Regifile mips_regifile_1 (
    .Din(RDin), .Clk(CLK), .R1({mips_regifile_1_r1_2, mips_regifile_1_r1}), .R2(MDin), .WE(RegWrite),
    .W_num(multiplexer_15_out), .R1_num(multiplexer_8_out), .R2_num(multiplexer_12_out));
  not not_3 (not_3_out, comparator_2_eq);
  Comparator #(.width(32), .mode("twosComplement")) comparator_2 (
    .a(32'h22), .b({mips_regifile_1_r1_2, mips_regifile_1_r1}), .eq(comparator_2_eq));  // open: gt, lt
  and and_2 (stop, \单周期硬布线控制器_1_syscall , not_3_out);
  and and_3 (and_3_out, \单周期硬布线控制器_1_syscall , comparator_2_eq);
  Register #(.width(32), .trigger("rising"), .Select("low")) register_2 (
    .D(MDin), .en(and_3_out), .Q(LedData), .clk(CLK));  // open: clr
  Multiplexer #(.select(1), .width(32), .disabled(0), .enable("false")) multiplexer_19 (
    .in0(MDin), .in1({multiplexer_9_out_2, multiplexer_9_out}), .out(multiplexer_19_out),
    .sel(\单周期硬布线控制器_1_alu_src ));
  not not_4 (not_4_out, mips_regifile_1_r1_2[31]);
  Multiplexer #(.select(1), .width(5), .disabled("Z"), .enable("false")) multiplexer_20 (
    .in0(IR[10:6]), .in1(mips_regifile_1_r1), .out(multiplexer_20_out), .sel(\单周期硬布线控制器_1_shamtsrc ));
  not not_5 (not_5_out, mips_alu_1_equal);
  MIPS_ALU mips_alu_1 (
    .X({mips_regifile_1_r1_2, mips_regifile_1_r1}), .Y(multiplexer_19_out), .AluOP(\单周期硬布线控制器_1_alu_op ),
    .Equal(mips_alu_1_equal), .Result(mips_alu_1_result), .shamt(multiplexer_20_out));  // open: Result_2
  Multiplexer #(.select(1), .width(32), .disabled("Z"), .enable("false")) multiplexer_21 (
    .in0(mips_alu_1_result), .in1(multiplexer_22_out), .out(multiplexer_21_out), .sel(\单周期硬布线控制器_1_memtoreg ));
  and and_4 (and_4_out, \单周期硬布线控制器_1_bgez , not_4_out);
  and and_5 (and_5_out, \单周期硬布线控制器_1_beq , mips_alu_1_equal);
  and and_6 (and_6_out, \单周期硬布线控制器_1_bne , not_5_out);
  or or_12 (I_Branch, and_4_out, and_5_out, and_6_out);
  RAM #(.addrWidth(10), .dataWidth(32), .bus("separate"), .Select("high")) ram_1 (
    .addr(mips_alu_1_result[11:2]), .din(MDin), .data(ram_1_data), .str(MemWrite), .sel(1'b1), .clk(CLK),
    .ld(\单周期硬布线控制器_1_memtoreg ));  // open: clr
  Multiplexer #(.select(1), .width(32), .disabled("Z"), .enable("false")) multiplexer_22 (
    .in0(ram_1_data), .in1({{16{1'b0}}, multiplexer_23_out}), .out(multiplexer_22_out), .sel(LHU));
  Counter #(.width(16), .max('hffff), .ongoal("wrap"), .trigger("rising"), .behavior("new")) counter_3 (
    .load(1'b0), .D({16{1'b0}}), .count(I_Branch), .Q(\条件分支成功数 ), .clk(CLK), .preset(1'b0), .down(1'b0));  // open: carry, clr
  Multiplexer #(.select(1), .width(16), .disabled("Z"), .enable("false")) multiplexer_23 (
    .in0(ram_1_data[15:0]), .in1(ram_1_data[31:16]), .out(multiplexer_23_out), .sel(mips_alu_1_result[1]));

  // Other names for the same wires on the sheet: rd[4:0] = IR[15:11]

  // Notes on the sheet:
  //   中断源
  //   中断等待指示
  //   总复位信号应将除ROM以外所有存储组件全部清零
  //   数码管输出
  //   数码管输出应该用寄存器锁存，否则显示数据只能一闪而过
  //   指令存储器
  //   指令字
  //   contents of rom_1 (hex, n*v repeats v):
  //   201d07d0 20100001 109fc0 139fc3 8021 2012000c 24160008 26100001 3210000f 20080008 20090001 139900
  //   2709825 132020 20020022 c 1094022 1500fff9 22100001 2018000f 2188024 108700 20080008 20090001 139902
  //   2709825 132021 20020022 c 1094022 1500fff9 108702 2c9b022 12c00001 8000c07 4020 1084027 84400
  //   3508ffff 82021 20020022 c 8000c01 afa20000 23bd0004 afa40000 23bd0004 afb00000 23bd0004 afb30000
  //   23bd0004 afb40000 23bd0004 afb50000 23bd0004 afb60000 23bd0004 40000000 20160001 20140003 20150001
  //   168020 108100 2149825 132020 20020022 c 1600fffa 295a022 1680fff7 40800000 23bdfffc 8fb60000
  //   23bdfffc 8fb50000 23bdfffc 8fb40000 23bdfffc 8fb30000 23bdfffc 8fb00000 23bdfffc 8fa40000 23bdfffc
  //   8fa20000 42000018 afa20000 23bd0004 afa40000 23bd0004 afb00000 23bd0004 afb30000 23bd0004 afb40000
  //   23bd0004 afb50000 23bd0004 afb60000 23bd0004 40000000 20160002 20140003 20150001 168020 108100
  //   2149825 132020 20020022 c 1600fffa 295a022 1680fff7 40800000 23bdfffc 8fb60000 23bdfffc 8fb50000
  //   23bdfffc 8fb40000 23bdfffc 8fb30000 23bdfffc 8fb00000 23bdfffc 8fa40000 23bdfffc 8fa20000 42000018
  //   afa20000 23bd0004 afa40000 23bd0004 afb00000 23bd0004 afb30000 23bd0004 afb40000 23bd0004 afb50000
  //   23bd0004 afb60000 23bd0004 40000000 20160003 20140003 20150001 168020 108100 2149825 132020 20020022
  //   c 1600fffa 295a022 1680fff7 40800000 23bdfffc 8fb60000 23bdfffc 8fb50000 23bdfffc 8fb40000 23bdfffc
  //   8fb30000 23bdfffc 8fb00000 23bdfffc 8fa40000 23bdfffc 8fa20000 42000018
  //   JMP
  //   JR
  //   OP
  //   Func
  //   OP
  //   Func
  //   rs
  //   rt
  //   rd
  //   shamt
  //   BGEZ
  //   Beq
  //   Bne
  //   MemToReg
  //   MemWrite
  //   AluOP
  //   AluSrcB
  //   RegWrite
  //   JAL
  //   RegDst
  //   ShamtSrc
  //   Syscall
  //   为方便自动评测，需要输出PC，IR，寄存器堆写如数据RDin
  //   RAM写使能MemWrite、RAM写入数据MDin等信号
endmodule

// 单周期硬布线控制器
module \单周期硬布线控制器  (
  input  [5:0] OP,
  input  [5:0] Func,
  input  [4:0] CPsrc,
  output [3:0] ALU_OP,
  output MemToReg,
  output MemWrite,
  output ALU_SRC,
  output RegWrite,
  output SysCALL,
  output SignedExt,
  output RegDst,
  output Beq,
  output Bne,
  output JR,
  output JMP,
  output JAL,
  output ShamtSrc,
  output LHU,
  output BGEZ,
  output ERET,
  output COP0,
  output MFC0,
  output MTC0
);

  wire not_1_out;

  \运算控制器自动生成  \u_运算控制器自动生成_1  (
    .OP0(OP[0]), .OP1(OP[1]), .OP2(OP[2]), .OP3(OP[3]), .OP4(OP[4]), .OP5(OP[5]), .F0(Func[0]), .F1(Func[1]),
    .F2(Func[2]), .F3(Func[3]), .F4(Func[4]), .F5(Func[5]), .S0(ALU_OP[0]), .S1(ALU_OP[1]), .S2(ALU_OP[2]),
    .S3(ALU_OP[3]));
  \控制信号自动生成  \u_控制信号自动生成_1  (
    .OP0(OP[0]), .OP1(OP[1]), .OP2(OP[2]), .OP3(OP[3]), .OP4(OP[4]), .OP5(OP[5]), .F0(Func[0]), .F1(Func[1]),
    .F2(Func[2]), .F3(Func[3]), .F4(Func[4]), .F5(Func[5]), .MemToReg(MemToReg), .MemWrite(MemWrite),
    .ALU_SRC(ALU_SRC), .RegWrite(RegWrite), .SysCALL(SysCALL), .SignedExt(SignedExt), .RegDst(RegDst),
    .BEQ(Beq), .BNE(Bne), .JR(JR), .JUMP(JMP), .JAL(JAL), .ShamtSrc(ShamtSrc), .LHU(LHU), .BGEZ(BGEZ),
    .ERET(ERET), .COP0(COP0));
  not not_1 (not_1_out, CPsrc[2]);
  and and_1 (MFC0, COP0, not_1_out);
  and and_2 (MTC0, COP0, CPsrc[2]);

  // Other names for the same wires on the sheet: OP_CODE[5:0] = OP

  // Notes on the sheet:
  //   运算器控制器，根据指令生成运算器功能选择信号
  //   控制信号生成，产生数据通路需要的其他控制信号
endmodule

// 运算器控制器
module \运算控制器自动生成  (
  input  OP0,
  input  OP1,
  input  OP2,
  input  OP3,
  input  OP4,
  input  OP5,
  input  F0,
  input  F1,
  input  F2,
  input  F3,
  input  F4,
  input  F5,
  output S0,
  output S1,
  output S2,
  output S3
);

  wire and_1_out, and_2_out, and_3_out, and_4_out, and_5_out, and_6_out, and_7_out, and_8_out, and_9_out,
       and_10_out, and_11_out, and_12_out, and_13_out, and_14_out, and_15_out, and_16_out, and_17_out,
       and_18_out, and_19_out, and_20_out, and_21_out, and_22_out, and_23_out, and_24_out, and_25_out,
       and_26_out, and_27_out, and_28_out, and_29_out, and_30_out, and_31_out, and_32_out, and_33_out,
       and_34_out, and_35_out, and_36_out, and_37_out, and_38_out, and_39_out, and_40_out, and_41_out,
       and_42_out, and_43_out, not_1_out, not_2_out, not_3_out, not_4_out, not_5_out, not_6_out, not_7_out,
       not_8_out, not_9_out, not_10_out, not_11_out, not_12_out, not_13_out, not_14_out, not_15_out,
       not_16_out, not_17_out, not_18_out, not_19_out, not_20_out, not_21_out, not_22_out, not_23_out,
       not_24_out, not_25_out, not_26_out, not_27_out, not_28_out, not_29_out, not_30_out, not_31_out,
       not_32_out, not_33_out, not_34_out, not_35_out, not_36_out, not_37_out, not_38_out, not_39_out,
       not_40_out, not_41_out, not_42_out, not_43_out, not_44_out, not_45_out, not_46_out, not_47_out,
       not_48_out, not_49_out, not_50_out, not_51_out, not_52_out, not_53_out, not_54_out, not_55_out,
       not_56_out, not_57_out, not_58_out, not_59_out, not_60_out, not_61_out, not_62_out, not_63_out,
       not_64_out, not_65_out, not_66_out, not_67_out, not_68_out, not_69_out, not_70_out, not_71_out,
       not_72_out, not_73_out, not_74_out, not_75_out, not_76_out, not_77_out, not_78_out, not_79_out,
       not_80_out, not_81_out, not_82_out, not_83_out, not_84_out, not_85_out, not_86_out, not_87_out,
       not_88_out, not_89_out, not_90_out, not_91_out, not_92_out, not_93_out, not_94_out, not_95_out,
       not_96_out, not_97_out, not_98_out, not_99_out, not_100_out, not_101_out, not_102_out, not_103_out,
       not_104_out, not_105_out, not_106_out, not_107_out, not_108_out, not_109_out, not_110_out,
       not_111_out, not_112_out, not_113_out, not_114_out, not_115_out, not_116_out, not_117_out,
       not_118_out, not_119_out, not_120_out, not_121_out, not_122_out, not_123_out, not_124_out,
       not_125_out, not_126_out, not_127_out, not_128_out, not_129_out, not_130_out, not_131_out,
       not_132_out, not_133_out, not_134_out, not_135_out, not_136_out, not_137_out, not_138_out,
       not_139_out, not_140_out, not_141_out, not_142_out, not_143_out, not_144_out, not_145_out,
       not_146_out, not_147_out, not_148_out, not_149_out, not_150_out, not_151_out, not_152_out,
       not_153_out, not_154_out, not_155_out, not_156_out, not_157_out, not_158_out, not_159_out,
       not_160_out, not_161_out, not_162_out, not_163_out, not_164_out, not_165_out, not_166_out,
       not_167_out, not_168_out, not_169_out, not_170_out, not_171_out, not_172_out, not_173_out,
       not_174_out, not_175_out, not_176_out, not_177_out, not_178_out, not_179_out, not_180_out,
       not_181_out, not_182_out, not_183_out, not_184_out, not_185_out, not_186_out, not_187_out,
       not_188_out, not_189_out, not_190_out, not_191_out, not_192_out, not_193_out, not_194_out,
       not_195_out, not_196_out, not_197_out, not_198_out, not_199_out, not_200_out, not_201_out,
       not_202_out, not_203_out, not_204_out, not_205_out, not_206_out, not_207_out, not_208_out,
       not_209_out, not_210_out, not_211_out, not_212_out, not_213_out, not_214_out, not_215_out,
       not_216_out, not_217_out, not_218_out, not_219_out, not_220_out, not_221_out, not_222_out,
       not_223_out, not_224_out, not_225_out, not_226_out, not_227_out, not_228_out, not_229_out,
       not_230_out, not_231_out, not_232_out, not_233_out, not_234_out, not_235_out, not_236_out,
       not_237_out, not_238_out, not_239_out, not_240_out, not_241_out, not_242_out, not_243_out,
       not_244_out, not_245_out, not_246_out, not_247_out, not_248_out, not_249_out, not_250_out,
       not_251_out, not_252_out, not_253_out, not_254_out, not_255_out, not_256_out, not_257_out,
       not_258_out, not_259_out, not_260_out, not_261_out, not_262_out, not_263_out, not_264_out,
       not_265_out, not_266_out, not_267_out, not_268_out, not_269_out, not_270_out, not_271_out,
       not_272_out, not_273_out, not_274_out, not_275_out, not_276_out, not_277_out, not_278_out,
       not_279_out, not_280_out, not_281_out, not_282_out, not_283_out, not_284_out, not_285_out,
       not_286_out, not_287_out, not_288_out;

  not not_1 (not_1_out, OP5);
  not not_2 (not_2_out, OP4);
  not not_3 (not_3_out, OP3);
  not not_4 (not_4_out, OP2);
  not not_5 (not_5_out, OP1);
  not not_6 (not_6_out, OP0);
  not not_7 (not_7_out, F5);
  not not_8 (not_8_out, F4);
  not not_9 (not_9_out, F3);
  not not_10 (not_10_out, F2);
  not not_11 (not_11_out, OP5);
  not not_12 (not_12_out, OP4);
  not not_13 (not_13_out, OP3);
  not not_14 (not_14_out, OP2);
  not not_15 (not_15_out, OP1);
  not not_16 (not_16_out, OP0);
  not not_17 (not_17_out, F4);
  not not_18 (not_18_out, F3);
  not not_19 (not_19_out, F2);
  not not_20 (not_20_out, F1);
  not not_21 (not_21_out, F0);
  not not_22 (not_22_out, OP5);
  not not_23 (not_23_out, OP4);
  not not_24 (not_24_out, OP3);
  not not_25 (not_25_out, OP2);
  not not_26 (not_26_out, OP1);
  not not_27 (not_27_out, OP0);
  not not_28 (not_28_out, F4);
  not not_29 (not_29_out, F3);
  not not_30 (not_30_out, F2);
  not not_31 (not_31_out, F1);
  not not_32 (not_32_out, OP5);
  not not_33 (not_33_out, OP4);
  not not_34 (not_34_out, OP3);
  not not_35 (not_35_out, OP2);
  not not_36 (not_36_out, OP1);
  not not_37 (not_37_out, OP0);
  not not_38 (not_38_out, F4);
  not not_39 (not_39_out, F3);
  not not_40 (not_40_out, F1);
  not not_41 (not_41_out, F0);
  not not_42 (not_42_out, OP5);
  not not_43 (not_43_out, OP4);
  not not_44 (not_44_out, OP3);
  not not_45 (not_45_out, OP2);
  not not_46 (not_46_out, OP1);
  not not_47 (not_47_out, OP0);
  not not_48 (not_48_out, F4);
  not not_49 (not_49_out, F2);
  not not_50 (not_50_out, F0);
  not not_51 (not_51_out, OP5);
  not not_52 (not_52_out, OP4);
  not not_53 (not_53_out, OP3);
  not not_54 (not_54_out, OP1);
  not not_55 (not_55_out, OP0);
  not not_56 (not_56_out, OP5);
  not not_57 (not_57_out, OP4);
  not not_58 (not_58_out, OP3);
  not not_59 (not_59_out, OP1);
  not not_60 (not_60_out, OP5);
  not not_61 (not_61_out, OP4);
  not not_62 (not_62_out, OP2);
  not not_63 (not_63_out, OP1);
  not not_64 (not_64_out, OP0);
  not not_65 (not_65_out, OP5);
  not not_66 (not_66_out, OP4);
  not not_67 (not_67_out, OP1);
  not not_68 (not_68_out, OP0);
  not not_69 (not_69_out, OP5);
  not not_70 (not_70_out, OP4);
  not not_71 (not_71_out, OP2);
  not not_72 (not_72_out, OP1);
  not not_73 (not_73_out, OP5);
  not not_74 (not_74_out, OP4);
  not not_75 (not_75_out, OP2);
  not not_76 (not_76_out, OP0);
  not not_77 (not_77_out, OP4);
  not not_78 (not_78_out, OP3);
  not not_79 (not_79_out, OP2);
  not not_80 (not_80_out, OP4);
  not not_81 (not_81_out, OP2);
  not not_82 (not_82_out, OP5);
  not not_83 (not_83_out, OP4);
  not not_84 (not_84_out, OP3);
  not not_85 (not_85_out, OP2);
  not not_86 (not_86_out, OP1);
  not not_87 (not_87_out, OP0);
  not not_88 (not_88_out, F4);
  not not_89 (not_89_out, F3);
  not not_90 (not_90_out, F0);
  not not_91 (not_91_out, OP4);
  not not_92 (not_92_out, OP3);
  not not_93 (not_93_out, OP1);
  not not_94 (not_94_out, OP5);
  not not_95 (not_95_out, OP4);
  not not_96 (not_96_out, OP3);
  not not_97 (not_97_out, OP2);
  not not_98 (not_98_out, OP1);
  not not_99 (not_99_out, OP0);
  not not_100 (not_100_out, F5);
  not not_101 (not_101_out, F4);
  not not_102 (not_102_out, F3);
  not not_103 (not_103_out, F2);
  not not_104 (not_104_out, F0);
  not not_105 (not_105_out, OP5);
  not not_106 (not_106_out, OP4);
  not not_107 (not_107_out, OP3);
  not not_108 (not_108_out, OP2);
  not not_109 (not_109_out, OP1);
  not not_110 (not_110_out, OP0);
  not not_111 (not_111_out, F4);
  not not_112 (not_112_out, F3);
  not not_113 (not_113_out, F2);
  not not_114 (not_114_out, F0);
  not not_115 (not_115_out, OP5);
  not not_116 (not_116_out, OP4);
  not not_117 (not_117_out, OP3);
  not not_118 (not_118_out, OP2);
  not not_119 (not_119_out, OP1);
  not not_120 (not_120_out, OP0);
  not not_121 (not_121_out, F4);
  not not_122 (not_122_out, F3);
  not not_123 (not_123_out, F1);
  not not_124 (not_124_out, F0);
  not not_125 (not_125_out, OP5);
  not not_126 (not_126_out, OP4);
  not not_127 (not_127_out, OP3);
  not not_128 (not_128_out, OP2);
  not not_129 (not_129_out, OP1);
  not not_130 (not_130_out, OP0);
  not not_131 (not_131_out, F4);
  not not_132 (not_132_out, F3);
  not not_133 (not_133_out, OP5);
  not not_134 (not_134_out, OP4);
  not not_135 (not_135_out, OP3);
  not not_136 (not_136_out, OP2);
  not not_137 (not_137_out, OP1);
  not not_138 (not_138_out, OP0);
  not not_139 (not_139_out, F4);
  not not_140 (not_140_out, F2);
  not not_141 (not_141_out, F0);
  not not_142 (not_142_out, OP5);
  not not_143 (not_143_out, OP4);
  not not_144 (not_144_out, OP1);
  not not_145 (not_145_out, OP0);
  not not_146 (not_146_out, OP5);
  not not_147 (not_147_out, OP4);
  not not_148 (not_148_out, OP2);
  not not_149 (not_149_out, OP0);
  not not_150 (not_150_out, OP5);
  not not_151 (not_151_out, OP4);
  not not_152 (not_152_out, OP3);
  not not_153 (not_153_out, OP2);
  not not_154 (not_154_out, OP1);
  not not_155 (not_155_out, OP0);
  not not_156 (not_156_out, F5);
  not not_157 (not_157_out, F4);
  not not_158 (not_158_out, F3);
  not not_159 (not_159_out, F0);
  not not_160 (not_160_out, OP5);
  not not_161 (not_161_out, OP4);
  not not_162 (not_162_out, OP3);
  not not_163 (not_163_out, OP2);
  not not_164 (not_164_out, OP1);
  not not_165 (not_165_out, OP0);
  not not_166 (not_166_out, F4);
  not not_167 (not_167_out, F3);
  not not_168 (not_168_out, F2);
  not not_169 (not_169_out, F1);
  not not_170 (not_170_out, F0);
  not not_171 (not_171_out, OP5);
  not not_172 (not_172_out, OP4);
  not not_173 (not_173_out, OP3);
  not not_174 (not_174_out, OP2);
  not not_175 (not_175_out, OP1);
  not not_176 (not_176_out, OP0);
  not not_177 (not_177_out, F4);
  not not_178 (not_178_out, F3);
  not not_179 (not_179_out, F2);
  not not_180 (not_180_out, F1);
  not not_181 (not_181_out, OP5);
  not not_182 (not_182_out, OP4);
  not not_183 (not_183_out, OP3);
  not not_184 (not_184_out, OP2);
  not not_185 (not_185_out, OP1);
  not not_186 (not_186_out, OP0);
  not not_187 (not_187_out, F4);
  not not_188 (not_188_out, F3);
  not not_189 (not_189_out, F2);
  not not_190 (not_190_out, F0);
  not not_191 (not_191_out, OP5);
  not not_192 (not_192_out, OP4);
  not not_193 (not_193_out, OP3);
  not not_194 (not_194_out, OP2);
  not not_195 (not_195_out, OP1);
  not not_196 (not_196_out, OP0);
  not not_197 (not_197_out, F4);
  not not_198 (not_198_out, F3);
  not not_199 (not_199_out, F1);
  not not_200 (not_200_out, F0);
  not not_201 (not_201_out, OP5);
  not not_202 (not_202_out, OP4);
  not not_203 (not_203_out, OP3);
  not not_204 (not_204_out, OP2);
  not not_205 (not_205_out, OP1);
  not not_206 (not_206_out, OP0);
  not not_207 (not_207_out, F4);
  not not_208 (not_208_out, F2);
  not not_209 (not_209_out, OP5);
  not not_210 (not_210_out, OP4);
  not not_211 (not_211_out, OP3);
  not not_212 (not_212_out, OP1);
  not not_213 (not_213_out, OP0);
  not not_214 (not_214_out, OP5);
  not not_215 (not_215_out, OP4);
  not not_216 (not_216_out, OP3);
  not not_217 (not_217_out, OP1);
  not not_218 (not_218_out, OP5);
  not not_219 (not_219_out, OP4);
  not not_220 (not_220_out, OP2);
  not not_221 (not_221_out, OP1);
  not not_222 (not_222_out, OP0);
  not not_223 (not_223_out, OP5);
  not not_224 (not_224_out, OP4);
  not not_225 (not_225_out, OP1);
  not not_226 (not_226_out, OP0);
  not not_227 (not_227_out, OP5);
  not not_228 (not_228_out, OP4);
  not not_229 (not_229_out, OP2);
  not not_230 (not_230_out, OP1);
  not not_231 (not_231_out, OP4);
  not not_232 (not_232_out, OP3);
  not not_233 (not_233_out, OP2);
  not not_234 (not_234_out, OP4);
  not not_235 (not_235_out, OP2);
  not not_236 (not_236_out, OP4);
  not not_237 (not_237_out, OP3);
  not not_238 (not_238_out, OP1);
  not not_239 (not_239_out, OP5);
  not not_240 (not_240_out, OP4);
  not not_241 (not_241_out, OP3);
  not not_242 (not_242_out, OP2);
  not not_243 (not_243_out, OP1);
  not not_244 (not_244_out, OP0);
  not not_245 (not_245_out, F4);
  not not_246 (not_246_out, F3);
  not not_247 (not_247_out, F1);
  not not_248 (not_248_out, OP5);
  not not_249 (not_249_out, OP4);
  not not_250 (not_250_out, OP3);
  not not_251 (not_251_out, OP2);
  not not_252 (not_252_out, OP1);
  not not_253 (not_253_out, OP0);
  not not_254 (not_254_out, F4);
  not not_255 (not_255_out, F3);
  not not_256 (not_256_out, OP5);
  not not_257 (not_257_out, OP4);
  not not_258 (not_258_out, OP3);
  not not_259 (not_259_out, OP2);
  not not_260 (not_260_out, OP1);
  not not_261 (not_261_out, OP0);
  not not_262 (not_262_out, F4);
  not not_263 (not_263_out, F2);
  not not_264 (not_264_out, F0);
  not not_265 (not_265_out, OP5);
  not not_266 (not_266_out, OP4);
  not not_267 (not_267_out, OP3);
  not not_268 (not_268_out, OP2);
  not not_269 (not_269_out, OP1);
  not not_270 (not_270_out, OP0);
  not not_271 (not_271_out, F4);
  not not_272 (not_272_out, F2);
  not not_273 (not_273_out, OP5);
  not not_274 (not_274_out, OP4);
  not not_275 (not_275_out, OP2);
  not not_276 (not_276_out, OP0);
  not not_277 (not_277_out, OP5);
  not not_278 (not_278_out, OP4);
  not not_279 (not_279_out, OP1);
  not not_280 (not_280_out, OP5);
  not not_281 (not_281_out, OP4);
  not not_282 (not_282_out, OP3);
  not not_283 (not_283_out, OP2);
  not not_284 (not_284_out, OP1);
  not not_285 (not_285_out, OP0);
  not not_286 (not_286_out, F4);
  not not_287 (not_287_out, F3);
  not not_288 (not_288_out, F0);
  and and_1 (and_1_out, not_1_out, not_2_out, not_3_out, not_4_out, not_5_out, not_6_out, not_7_out, not_8_out, not_9_out, not_10_out, F1, F0);
  and and_2 (and_2_out, not_11_out, not_12_out, not_13_out, not_14_out, not_15_out, not_16_out, F5, not_17_out, not_18_out, not_19_out, not_20_out, not_21_out);
  and and_3 (and_3_out, not_22_out, not_23_out, not_24_out, not_25_out, not_26_out, not_27_out, F5, not_28_out, not_29_out, not_30_out, not_31_out, F0);
  and and_4 (and_4_out, not_32_out, not_33_out, not_34_out, not_35_out, not_36_out, not_37_out, F5, not_38_out, not_39_out, F2, not_40_out, not_41_out);
  and and_5 (and_5_out, not_42_out, not_43_out, not_44_out, not_45_out, not_46_out, not_47_out, F5, not_48_out, F3, not_49_out, F1, not_50_out);
  and and_6 (and_6_out, not_51_out, not_52_out, not_53_out, OP2, not_54_out, not_55_out);
  and and_7 (and_7_out, not_56_out, not_57_out, not_58_out, OP2, not_59_out, OP0);
  and and_8 (and_8_out, not_60_out, not_61_out, OP3, not_62_out, not_63_out, not_64_out);
  and and_9 (and_9_out, not_65_out, not_66_out, OP3, OP2, not_67_out, not_68_out);
  and and_10 (and_10_out, not_69_out, not_70_out, OP3, not_71_out, not_72_out, OP0);
  and and_11 (and_11_out, not_73_out, not_74_out, OP3, not_75_out, OP1, not_76_out);
  and and_12 (and_12_out, OP5, not_77_out, not_78_out, not_79_out, OP1, OP0);
  and and_13 (and_13_out, OP5, not_80_out, OP3, not_81_out, OP1, OP0);
  and and_14 (and_14_out, not_82_out, not_83_out, not_84_out, not_85_out, not_86_out, not_87_out, F5, not_88_out, not_89_out, F2, F1, not_90_out);
  and and_15 (and_15_out, OP5, not_91_out, not_92_out, OP2, not_93_out, OP0);
  and and_16 (and_16_out, not_94_out, not_95_out, not_96_out, not_97_out, not_98_out, not_99_out, not_100_out, not_101_out, not_102_out, not_103_out, F1, not_104_out);
  and and_17 (and_17_out, not_105_out, not_106_out, not_107_out, not_108_out, not_109_out, not_110_out, F5, not_111_out, not_112_out, not_113_out, F1, not_114_out);
  and and_18 (and_18_out, not_115_out, not_116_out, not_117_out, not_118_out, not_119_out, not_120_out, F5, not_121_out, not_122_out, F2, not_123_out, not_124_out);
  and and_19 (and_19_out, not_125_out, not_126_out, not_127_out, not_128_out, not_129_out, not_130_out, F5, not_131_out, not_132_out, F2, F1, F0);
  and and_20 (and_20_out, not_133_out, not_134_out, not_135_out, not_136_out, not_137_out, not_138_out, F5, not_139_out, F3, not_140_out, F1, not_141_out);
  and and_21 (and_21_out, not_142_out, not_143_out, OP3, OP2, not_144_out, not_145_out);
  and and_22 (and_22_out, not_146_out, not_147_out, OP3, not_148_out, OP1, not_149_out);
  and and_23 (and_23_out, not_150_out, not_151_out, not_152_out, not_153_out, not_154_out, not_155_out, not_156_out, not_157_out, not_158_out, F2, F1, not_159_out);
  and and_24 (and_24_out, not_160_out, not_161_out, not_162_out, not_163_out, not_164_out, not_165_out, F5, not_166_out, not_167_out, not_168_out, not_169_out, not_170_out);
  and and_25 (and_25_out, not_171_out, not_172_out, not_173_out, not_174_out, not_175_out, not_176_out, F5, not_177_out, not_178_out, not_179_out, not_180_out, F0);
  and and_26 (and_26_out, not_181_out, not_182_out, not_183_out, not_184_out, not_185_out, not_186_out, F5, not_187_out, not_188_out, not_189_out, F1, not_190_out);
  and and_27 (and_27_out, not_191_out, not_192_out, not_193_out, not_194_out, not_195_out, not_196_out, F5, not_197_out, not_198_out, F2, not_199_out, not_200_out);
  and and_28 (and_28_out, not_201_out, not_202_out, not_203_out, not_204_out, not_205_out, not_206_out, F5, not_207_out, F3, not_208_out, F1, F0);
  and and_29 (and_29_out, not_209_out, not_210_out, not_211_out, OP2, not_212_out, not_213_out);
  and and_30 (and_30_out, not_214_out, not_215_out, not_216_out, OP2, not_217_out, OP0);
  and and_31 (and_31_out, not_218_out, not_219_out, OP3, not_220_out, not_221_out, not_222_out);
  and and_32 (and_32_out, not_223_out, not_224_out, OP3, OP2, not_225_out, not_226_out);
  and and_33 (and_33_out, not_227_out, not_228_out, OP3, not_229_out, not_230_out, OP0);
  and and_34 (and_34_out, OP5, not_231_out, not_232_out, not_233_out, OP1, OP0);
  and and_35 (and_35_out, OP5, not_234_out, OP3, not_235_out, OP1, OP0);
  and and_36 (and_36_out, OP5, not_236_out, not_237_out, OP2, not_238_out, OP0);
  and and_37 (and_37_out, not_239_out, not_240_out, not_241_out, not_242_out, not_243_out, not_244_out, F5, not_245_out, not_246_out, F2, not_247_out, F0);
  and and_38 (and_38_out, not_248_out, not_249_out, not_250_out, not_251_out, not_252_out, not_253_out, F5, not_254_out, not_255_out, F2, F1, F0);
  and and_39 (and_39_out, not_256_out, not_257_out, not_258_out, not_259_out, not_260_out, not_261_out, F5, not_262_out, F3, not_263_out, F1, not_264_out);
  and and_40 (and_40_out, not_265_out, not_266_out, not_267_out, not_268_out, not_269_out, not_270_out, F5, not_271_out, F3, not_272_out, F1, F0);
  and and_41 (and_41_out, not_273_out, not_274_out, OP3, not_275_out, OP1, not_276_out);
  and and_42 (and_42_out, not_277_out, not_278_out, OP3, OP2, not_279_out, OP0);
  and and_43 (and_43_out, not_280_out, not_281_out, not_282_out, not_283_out, not_284_out, not_285_out, F5, not_286_out, not_287_out, F2, F1, not_288_out);
  or or_1 (S1, and_16_out, and_17_out, and_18_out, and_19_out, and_20_out, and_21_out, and_22_out, and_23_out);
  or or_2 (S3, and_37_out, and_38_out, and_39_out, and_40_out, and_41_out, and_42_out, and_43_out);
  or or_3 (S0, and_1_out, and_2_out, and_3_out, and_4_out, and_5_out, and_6_out, and_7_out, and_8_out, and_9_out, and_10_out, and_11_out, and_12_out, and_13_out, and_14_out, and_15_out);
  or or_4 (S2, and_24_out, and_25_out, and_26_out, and_27_out, and_28_out, and_29_out, and_30_out, and_31_out, and_32_out, and_33_out, and_34_out, and_35_out, and_36_out);
endmodule

// 控制信号生成
module \控制信号自动生成  (
  input  OP0,
  input  OP1,
  input  OP2,
  input  OP3,
  input  OP4,
  input  OP5,
  input  F0,
  input  F1,
  input  F2,
  input  F3,
  input  F4,
  input  F5,
  output MemToReg,
  output MemWrite,
  output ALU_SRC,
  output RegWrite,
  output SysCALL,
  output SignedExt,
  output RegDst,
  output BEQ,
  output BNE,
  output JR,
  output JUMP,
  output JAL,
  output ShamtSrc,
  output LHU,
  output BGEZ,
  output ERET,
  output COP0
);

  wire and_1_out, and_2_out, and_4_out, and_5_out, and_6_out, and_7_out, and_8_out, and_9_out, and_10_out,
       and_11_out, and_12_out, and_13_out, and_14_out, and_15_out, and_16_out, and_17_out, and_19_out,
       and_20_out, and_21_out, and_22_out, and_23_out, and_24_out, and_25_out, and_26_out, and_27_out,
       and_28_out, and_29_out, not_1_out, not_2_out, not_3_out, not_4_out, not_5_out, not_6_out, not_7_out,
       not_8_out, not_9_out, not_10_out, not_11_out, not_12_out, not_13_out, not_14_out, not_15_out,
       not_16_out, not_17_out, not_18_out, not_19_out, not_20_out, not_21_out, not_22_out, not_23_out,
       not_24_out, not_25_out, not_26_out, not_27_out, not_28_out, not_29_out, not_30_out, not_31_out,
       not_32_out, not_33_out, not_34_out, not_35_out, not_36_out, not_37_out, not_38_out, not_39_out,
       not_40_out, not_41_out, not_42_out, not_43_out, not_44_out, not_45_out, not_46_out, not_47_out,
       not_48_out, not_49_out, not_50_out, not_51_out, not_52_out, not_53_out, not_54_out, not_55_out,
       not_56_out, not_57_out, not_58_out, not_59_out, not_60_out, not_61_out, not_62_out, not_63_out,
       not_64_out, not_65_out, not_66_out, not_67_out, not_68_out, not_69_out, not_70_out, not_71_out,
       not_72_out, not_73_out, not_74_out, not_75_out, not_76_out, not_77_out, not_78_out, not_79_out,
       not_80_out, not_81_out, not_82_out, not_83_out, not_84_out, not_85_out, not_86_out, not_87_out,
       not_88_out, not_89_out, not_90_out, not_91_out, not_92_out, not_93_out, not_94_out, not_95_out,
       not_96_out, not_97_out, not_98_out, not_99_out, not_100_out, not_101_out, not_102_out, not_103_out,
       not_104_out, not_105_out, not_106_out, not_107_out, not_108_out, not_109_out, not_110_out,
       not_111_out, not_112_out, not_113_out, not_114_out, not_115_out, not_116_out, not_117_out,
       not_118_out, not_119_out, not_120_out, not_121_out, not_122_out, not_123_out, not_124_out,
       not_125_out, not_126_out, not_127_out, not_128_out, not_129_out, not_130_out, not_131_out,
       not_132_out, not_133_out, not_134_out, not_135_out, not_136_out, not_137_out, not_138_out,
       not_139_out, not_140_out, not_141_out, not_142_out, not_143_out, not_144_out, not_145_out,
       not_146_out, not_147_out, not_148_out, not_149_out, not_150_out, not_151_out, not_152_out,
       not_153_out, not_154_out, not_155_out, not_156_out, not_157_out, not_158_out, not_159_out,
       not_160_out, not_161_out, not_162_out, not_163_out, not_164_out, not_165_out, not_166_out,
       not_167_out, not_168_out, not_169_out, not_170_out, not_171_out, not_172_out, not_173_out,
       not_174_out, not_175_out, not_176_out, not_177_out, not_178_out, not_179_out, not_180_out,
       not_181_out, not_182_out, not_183_out, not_184_out, not_185_out, not_186_out, not_187_out,
       not_188_out, not_189_out, not_190_out, not_191_out, not_192_out, not_193_out, not_194_out,
       not_195_out, not_196_out, not_197_out, not_198_out, not_199_out, not_200_out, not_201_out,
       not_202_out, not_203_out, not_204_out, not_205_out, not_206_out, not_207_out, not_208_out,
       not_209_out, not_210_out, not_211_out, not_212_out, not_213_out, not_214_out, not_215_out,
       not_216_out, not_217_out, not_218_out, not_219_out, not_220_out, not_221_out, not_222_out,
       not_223_out, not_224_out, not_225_out, not_226_out, not_227_out, not_228_out;

  not not_1 (not_1_out, OP1);
  not not_2 (not_2_out, OP3);
  not not_3 (not_3_out, OP4);
  not not_4 (not_4_out, OP2);
  not not_5 (not_5_out, OP3);
  not not_6 (not_6_out, OP4);
  not not_7 (not_7_out, OP2);
  not not_8 (not_8_out, OP4);
  not not_9 (not_9_out, OP0);
  not not_10 (not_10_out, OP2);
  not not_11 (not_11_out, OP4);
  not not_12 (not_12_out, OP5);
  not not_13 (not_13_out, OP1);
  not not_14 (not_14_out, OP4);
  not not_15 (not_15_out, OP5);
  not not_16 (not_16_out, OP1);
  not not_17 (not_17_out, OP3);
  not not_18 (not_18_out, OP4);
  not not_19 (not_19_out, OP2);
  not not_20 (not_20_out, OP4);
  not not_21 (not_21_out, OP0);
  not not_22 (not_22_out, OP1);
  not not_23 (not_23_out, OP2);
  not not_24 (not_24_out, OP4);
  not not_25 (not_25_out, OP5);
  not not_26 (not_26_out, F0);
  not not_27 (not_27_out, F2);
  not not_28 (not_28_out, F3);
  not not_29 (not_29_out, F4);
  not not_30 (not_30_out, OP0);
  not not_31 (not_31_out, OP1);
  not not_32 (not_32_out, OP2);
  not not_33 (not_33_out, OP4);
  not not_34 (not_34_out, OP5);
  not not_35 (not_35_out, F1);
  not not_36 (not_36_out, F3);
  not not_37 (not_37_out, F4);
  not not_38 (not_38_out, OP0);
  not not_39 (not_39_out, OP1);
  not not_40 (not_40_out, OP2);
  not not_41 (not_41_out, OP4);
  not not_42 (not_42_out, OP5);
  not not_43 (not_43_out, F3);
  not not_44 (not_44_out, F4);
  not not_45 (not_45_out, OP0);
  not not_46 (not_46_out, OP1);
  not not_47 (not_47_out, OP2);
  not not_48 (not_48_out, OP4);
  not not_49 (not_49_out, OP5);
  not not_50 (not_50_out, F0);
  not not_51 (not_51_out, F3);
  not not_52 (not_52_out, F4);
  not not_53 (not_53_out, OP0);
  not not_54 (not_54_out, OP1);
  not not_55 (not_55_out, OP2);
  not not_56 (not_56_out, OP4);
  not not_57 (not_57_out, OP5);
  not not_58 (not_58_out, F2);
  not not_59 (not_59_out, F3);
  not not_60 (not_60_out, F4);
  not not_61 (not_61_out, F5);
  not not_62 (not_62_out, OP0);
  not not_63 (not_63_out, OP1);
  not not_64 (not_64_out, OP2);
  not not_65 (not_65_out, OP4);
  not not_66 (not_66_out, OP5);
  not not_67 (not_67_out, F2);
  not not_68 (not_68_out, F4);
  not not_69 (not_69_out, OP0);
  not not_70 (not_70_out, OP2);
  not not_71 (not_71_out, OP4);
  not not_72 (not_72_out, OP5);
  not not_73 (not_73_out, OP1);
  not not_74 (not_74_out, OP4);
  not not_75 (not_75_out, OP5);
  not not_76 (not_76_out, OP1);
  not not_77 (not_77_out, OP3);
  not not_78 (not_78_out, OP4);
  not not_79 (not_79_out, OP2);
  not not_80 (not_80_out, OP3);
  not not_81 (not_81_out, OP4);
  not not_82 (not_82_out, OP0);
  not not_83 (not_83_out, OP1);
  not not_84 (not_84_out, OP2);
  not not_85 (not_85_out, OP3);
  not not_86 (not_86_out, OP4);
  not not_87 (not_87_out, OP5);
  not not_88 (not_88_out, F0);
  not not_89 (not_89_out, F1);
  not not_90 (not_90_out, F4);
  not not_91 (not_91_out, F5);
  not not_92 (not_92_out, OP0);
  not not_93 (not_93_out, OP2);
  not not_94 (not_94_out, OP4);
  not not_95 (not_95_out, OP5);
  not not_96 (not_96_out, OP1);
  not not_97 (not_97_out, OP3);
  not not_98 (not_98_out, OP4);
  not not_99 (not_99_out, OP5);
  not not_100 (not_100_out, OP1);
  not not_101 (not_101_out, OP3);
  not not_102 (not_102_out, OP4);
  not not_103 (not_103_out, OP5);
  not not_104 (not_104_out, OP1);
  not not_105 (not_105_out, OP3);
  not not_106 (not_106_out, OP4);
  not not_107 (not_107_out, OP2);
  not not_108 (not_108_out, OP4);
  not not_109 (not_109_out, OP0);
  not not_110 (not_110_out, OP1);
  not not_111 (not_111_out, OP2);
  not not_112 (not_112_out, OP3);
  not not_113 (not_113_out, OP4);
  not not_114 (not_114_out, OP5);
  not not_115 (not_115_out, F0);
  not not_116 (not_116_out, F2);
  not not_117 (not_117_out, F3);
  not not_118 (not_118_out, F4);
  not not_119 (not_119_out, OP0);
  not not_120 (not_120_out, OP1);
  not not_121 (not_121_out, OP2);
  not not_122 (not_122_out, OP3);
  not not_123 (not_123_out, OP4);
  not not_124 (not_124_out, OP5);
  not not_125 (not_125_out, F1);
  not not_126 (not_126_out, F3);
  not not_127 (not_127_out, F4);
  not not_128 (not_128_out, OP0);
  not not_129 (not_129_out, OP1);
  not not_130 (not_130_out, OP2);
  not not_131 (not_131_out, OP3);
  not not_132 (not_132_out, OP4);
  not not_133 (not_133_out, OP5);
  not not_134 (not_134_out, F3);
  not not_135 (not_135_out, F4);
  not not_136 (not_136_out, OP0);
  not not_137 (not_137_out, OP1);
  not not_138 (not_138_out, OP2);
  not not_139 (not_139_out, OP3);
  not not_140 (not_140_out, OP4);
  not not_141 (not_141_out, OP5);
  not not_142 (not_142_out, F0);
  not not_143 (not_143_out, F3);
  not not_144 (not_144_out, F4);
  not not_145 (not_145_out, OP0);
  not not_146 (not_146_out, OP1);
  not not_147 (not_147_out, OP2);
  not not_148 (not_148_out, OP3);
  not not_149 (not_149_out, OP4);
  not not_150 (not_150_out, OP5);
  not not_151 (not_151_out, F2);
  not not_152 (not_152_out, F3);
  not not_153 (not_153_out, F4);
  not not_154 (not_154_out, F5);
  not not_155 (not_155_out, OP0);
  not not_156 (not_156_out, OP1);
  not not_157 (not_157_out, OP2);
  not not_158 (not_158_out, OP3);
  not not_159 (not_159_out, OP4);
  not not_160 (not_160_out, OP5);
  not not_161 (not_161_out, F2);
  not not_162 (not_162_out, F4);
  not not_163 (not_163_out, OP0);
  not not_164 (not_164_out, OP1);
  not not_165 (not_165_out, OP3);
  not not_166 (not_166_out, OP4);
  not not_167 (not_167_out, OP5);
  not not_168 (not_168_out, OP1);
  not not_169 (not_169_out, OP3);
  not not_170 (not_170_out, OP4);
  not not_171 (not_171_out, OP5);
  not not_172 (not_172_out, OP0);
  not not_173 (not_173_out, OP1);
  not not_174 (not_174_out, OP2);
  not not_175 (not_175_out, OP3);
  not not_176 (not_176_out, OP4);
  not not_177 (not_177_out, OP5);
  not not_178 (not_178_out, F0);
  not not_179 (not_179_out, F1);
  not not_180 (not_180_out, F2);
  not not_181 (not_181_out, F4);
  not not_182 (not_182_out, F5);
  not not_183 (not_183_out, OP2);
  not not_184 (not_184_out, OP3);
  not not_185 (not_185_out, OP4);
  not not_186 (not_186_out, OP5);
  not not_187 (not_187_out, OP2);
  not not_188 (not_188_out, OP3);
  not not_189 (not_189_out, OP4);
  not not_190 (not_190_out, OP5);
  not not_191 (not_191_out, OP0);
  not not_192 (not_192_out, OP1);
  not not_193 (not_193_out, OP2);
  not not_194 (not_194_out, OP3);
  not not_195 (not_195_out, OP4);
  not not_196 (not_196_out, OP5);
  not not_197 (not_197_out, F0);
  not not_198 (not_198_out, F3);
  not not_199 (not_199_out, F4);
  not not_200 (not_200_out, F5);
  not not_201 (not_201_out, OP1);
  not not_202 (not_202_out, OP3);
  not not_203 (not_203_out, OP4);
  not not_204 (not_204_out, OP1);
  not not_205 (not_205_out, OP2);
  not not_206 (not_206_out, OP3);
  not not_207 (not_207_out, OP4);
  not not_208 (not_208_out, OP5);
  not not_209 (not_209_out, OP0);
  not not_210 (not_210_out, OP1);
  not not_211 (not_211_out, OP2);
  not not_212 (not_212_out, OP3);
  not not_213 (not_213_out, OP5);
  not not_214 (not_214_out, F0);
  not not_215 (not_215_out, F1);
  not not_216 (not_216_out, F2);
  not not_217 (not_217_out, F5);
  not not_218 (not_218_out, OP0);
  not not_219 (not_219_out, OP1);
  not not_220 (not_220_out, OP2);
  not not_221 (not_221_out, OP3);
  not not_222 (not_222_out, OP5);
  not not_223 (not_223_out, F0);
  not not_224 (not_224_out, F1);
  not not_225 (not_225_out, F2);
  not not_226 (not_226_out, F3);
  not not_227 (not_227_out, F4);
  not not_228 (not_228_out, F5);
  and and_1 (and_1_out, OP0, not_1_out, OP2, not_2_out, not_3_out, OP5);
  and and_2 (and_2_out, OP0, OP1, not_4_out, not_5_out, not_6_out, OP5);
  and and_3 (MemWrite, OP0, OP1, not_7_out, OP3, not_8_out, OP5);
  and and_4 (and_4_out, not_9_out, not_10_out, OP3, not_11_out, not_12_out);
  and and_5 (and_5_out, not_13_out, OP3, not_14_out, not_15_out);
  and and_6 (and_6_out, OP0, not_16_out, OP2, not_17_out, not_18_out, OP5);
  and and_7 (and_7_out, OP0, OP1, not_19_out, not_20_out, OP5);
  and and_8 (and_8_out, not_21_out, not_22_out, not_23_out, not_24_out, not_25_out, not_26_out, not_27_out, not_28_out, not_29_out);
  and and_9 (and_9_out, not_30_out, not_31_out, not_32_out, not_33_out, not_34_out, not_35_out, not_36_out, not_37_out, F5);
  and and_10 (and_10_out, not_38_out, not_39_out, not_40_out, not_41_out, not_42_out, F2, not_43_out, not_44_out, F5);
  and and_11 (and_11_out, not_45_out, not_46_out, not_47_out, not_48_out, not_49_out, not_50_out, F1, not_51_out, not_52_out);
  and and_12 (and_12_out, not_53_out, not_54_out, not_55_out, not_56_out, not_57_out, F1, not_58_out, not_59_out, not_60_out, not_61_out);
  and and_13 (and_13_out, not_62_out, not_63_out, not_64_out, not_65_out, not_66_out, F1, not_67_out, F3, not_68_out, F5);
  and and_14 (and_14_out, not_69_out, not_70_out, OP3, not_71_out, not_72_out);
  and and_15 (and_15_out, not_73_out, OP3, not_74_out, not_75_out);
  and and_16 (and_16_out, OP0, not_76_out, OP2, not_77_out, not_78_out, OP5);
  and and_17 (and_17_out, OP0, OP1, not_79_out, not_80_out, not_81_out);
  and and_18 (SysCALL, not_82_out, not_83_out, not_84_out, not_85_out, not_86_out, not_87_out, not_88_out, not_89_out, F2, F3, not_90_out, not_91_out);
  and and_19 (and_19_out, not_92_out, not_93_out, OP3, not_94_out, not_95_out);
  and and_20 (and_20_out, not_96_out, OP2, not_97_out, not_98_out, not_99_out);
  and and_21 (and_21_out, OP0, not_100_out, not_101_out, not_102_out, not_103_out);
  and and_22 (and_22_out, OP0, not_104_out, OP2, not_105_out, not_106_out);
  and and_23 (and_23_out, OP0, OP1, not_107_out, not_108_out, OP5);
  and and_24 (and_24_out, not_109_out, not_110_out, not_111_out, not_112_out, not_113_out, not_114_out, not_115_out, not_116_out, not_117_out, not_118_out);
  and and_25 (and_25_out, not_119_out, not_120_out, not_121_out, not_122_out, not_123_out, not_124_out, not_125_out, not_126_out, not_127_out, F5);
  and and_26 (and_26_out, not_128_out, not_129_out, not_130_out, not_131_out, not_132_out, not_133_out, F2, not_134_out, not_135_out, F5);
  and and_27 (and_27_out, not_136_out, not_137_out, not_138_out, not_139_out, not_140_out, not_141_out, not_142_out, F1, not_143_out, not_144_out);
  and and_28 (and_28_out, not_145_out, not_146_out, not_147_out, not_148_out, not_149_out, not_150_out, F1, not_151_out, not_152_out, not_153_out, not_154_out);
  and and_29 (and_29_out, not_155_out, not_156_out, not_157_out, not_158_out, not_159_out, not_160_out, F1, not_161_out, F3, not_162_out, F5);
  and and_30 (BEQ, not_163_out, not_164_out, OP2, not_165_out, not_166_out, not_167_out);
  and and_31 (BNE, OP0, not_168_out, OP2, not_169_out, not_170_out, not_171_out);
  and and_32 (JR, not_172_out, not_173_out, not_174_out, not_175_out, not_176_out, not_177_out, not_178_out, not_179_out, not_180_out, F3, not_181_out, not_182_out);
  and and_33 (JUMP, OP1, not_183_out, not_184_out, not_185_out, not_186_out);
  and and_34 (JAL, OP0, OP1, not_187_out, not_188_out, not_189_out, not_190_out);
  and and_35 (ShamtSrc, not_191_out, not_192_out, not_193_out, not_194_out, not_195_out, not_196_out, not_197_out, F1, F2, not_198_out, not_199_out, not_200_out);
  and and_36 (LHU, OP0, not_201_out, OP2, not_202_out, not_203_out, OP5);
  and and_37 (BGEZ, OP0, not_204_out, not_205_out, not_206_out, not_207_out, not_208_out);
  and and_38 (ERET, not_209_out, not_210_out, not_211_out, not_212_out, OP4, not_213_out, not_214_out, not_215_out, not_216_out, F3, F4, not_217_out);
  and and_39 (COP0, not_218_out, not_219_out, not_220_out, not_221_out, OP4, not_222_out, not_223_out, not_224_out, not_225_out, not_226_out, not_227_out, not_228_out);
  or or_1 (MemToReg, and_1_out, and_2_out);
  or or_2 (ALU_SRC, and_4_out, and_5_out, and_6_out, and_7_out);
  or or_3 (RegWrite, and_8_out, and_9_out, and_10_out, and_11_out, and_12_out, and_13_out, and_14_out, and_15_out, and_16_out, and_17_out);
  or or_4 (SignedExt, and_19_out, and_20_out, and_21_out, and_22_out, and_23_out);
  or or_5 (RegDst, and_24_out, and_25_out, and_26_out, and_27_out, and_28_out, and_29_out);
endmodule

// ALU
module MIPS_ALU (
  input  [4:0] shamt,
  input  [31:0] X,
  input  [31:0] Y,
  input  [3:0] AluOP,
  output Equal,
  output [31:0] Result,
  output [31:0] Result_2
);

  wire [0:0] comparator_1_lt, comparator_2_lt;
  wire [31:0] adder_1_out, AND_out, divider_1_out, divider_1_rem, multiplier_1_cout, multiplier_1_out,
       NOR_out, OR_out, shifter_1_out, shifter_2_out, shifter_3_out, subtractor_1_out, XOR_out;

  assign AND_out = X & Y;  // AND_Gate AND, 32 bits wide
  assign OR_out = X | Y;  // OR_Gate OR, 32 bits wide
  Shifter #(.width(32), .shift("ll")) shifter_1 (.in(Y), .\dist (shamt), .out(shifter_1_out));
  Shifter #(.width(32), .shift("ar")) shifter_2 (.in(Y), .\dist (shamt), .out(shifter_2_out));
  Shifter #(.width(32), .shift("lr")) shifter_3 (.in(Y), .\dist (shamt), .out(shifter_3_out));
  Multiplier #(.width(32)) multiplier_1 (.a(X), .b(Y), .out(multiplier_1_out), .cout(multiplier_1_cout));  // open: cin
  Divider #(.width(32)) divider_1 (.a(X), .b(Y), .out(divider_1_out), .rem(divider_1_rem));  // open: upper
  Adder #(.width(32)) adder_1 (.a(X), .b(Y), .out(adder_1_out));  // open: cin, cout
  Subtractor #(.width(32)) subtractor_1 (.a(X), .b(Y), .out(subtractor_1_out));  // open: bin, bout
  assign XOR_out = X ^ Y;  // XOR_Gate XOR, 32 bits wide
  assign NOR_out = ~(X | Y);  // NOR_Gate NOR, 32 bits wide
  Comparator #(.width(32), .mode("twosComplement")) comparator_1 (
    .a(X), .b(Y), .eq(Equal), .lt(comparator_1_lt[0]));  // open: gt
  Comparator #(.width(32), .mode("unsigned")) comparator_2 (.a(X), .b(Y), .lt(comparator_2_lt[0]));  // open: gt, eq
  Multiplexer #(.select(4), .width(32), .disabled("Z"), .enable("false")) multiplexer_1 (
    .in0(shifter_1_out), .in1(shifter_2_out), .in2(shifter_3_out), .in3(multiplier_1_out),
    .in4(divider_1_out), .in5(adder_1_out), .in6(subtractor_1_out), .in7(AND_out), .in8(OR_out),
    .in9(XOR_out), .in10(NOR_out), .in11({{31{1'b0}}, comparator_1_lt[0]}),
    .in12({{31{1'b0}}, comparator_2_lt[0]}), .in13({32{1'b0}}), .in14({32{1'b0}}), .in15({32{1'b0}}),
    .out(Result), .sel(AluOP));
  Multiplexer #(.select(4), .width(32), .disabled("Z"), .enable("false")) multiplexer_2 (
    .in0({32{1'b0}}), .in1({32{1'b0}}), .in2({32{1'b0}}), .in3(multiplier_1_cout), .in4(divider_1_rem),
    .in5({32{1'b0}}), .in6({32{1'b0}}), .in7({32{1'b0}}), .in8({32{1'b0}}), .in9({32{1'b0}}),
    .in10({32{1'b0}}), .in11({32{1'b0}}), .in12({32{1'b0}}), .in13({32{1'b0}}), .in14({32{1'b0}}),
    .in15({32{1'b0}}), .out(Result_2), .sel(AluOP));

  // Other names for the same wires on the sheet: Result2[31:0] = Result_2; S[3:0] = AluOP

  // Notes on the sheet:
  //   不要改变此引脚区域内容，也不要改变ALU封装形式
  //   输入引脚
  //   输出引脚
endmodule

module MIPS_Regifile (
  input  [31:0] Din,
  input  Clk,
  input  WE,
  input  [4:0] R1_num,
  input  [4:0] W_num,
  input  [4:0] R2_num,
  output [31:0] R1,
  output [31:0] R2
);

  // RegisterFile registerfile_1: pin names not known; wires that end beside it: Din, Clk, WE, W_num, R1_num, R2_num, R1, R2
endmodule

module \理想流水线  (
  output RegWrite,
  output MemWrite,
  output [31:0] IF_PC,
  output [31:0] ID_PC,
  output [31:0] EX_PC,
  output [31:0] M_PC,
  output [31:0] WB_PC,
  output [31:0] RDin,
  output [31:0] MDin,
  output [31:0] LedData
);

  wire and_1_out, and_2_out, and_3_out, and_4_out, and_5_out, and_8_out, and_9_out, and_10_out, and_11_out,
       and_12_out, and_13_out, Branch, CLK, comparator_1_eq, d_ff_1_q, d_ff_2_q, d_ff_3_q,
       demultiplexer_1_out1, demultiplexer_1_out2, demultiplexer_1_out3, ERET, ex_mem_1_statusout,
       ex_mem_1_stopout, Go, IR1, IR2, IR3, load_use, mem_wb_1_stopout, mips_alu_1_equal, MTC0,
       multiplexer_10_out, multiplexer_11_out, multiplexer_12_out, multiplexer_14_out, multiplexer_29_out,
       not_1_out, not_2_out, not_3_out, not_4_out, not_5_out, not_6_out, or_1_out, or_5_out, or_6_out,
       or_7_out, or_8_out, or_9_out, or_10_out, or_11_out, or_12_out, or_13_out, priority_encoder_1_en_out,
       priority_encoder_1_gs, rd0, RST, SignedExt, W1, W2, W3, \中断CPU , \单周期硬布线控制器_1_eret ,
       \单周期硬布线控制器_1_regdst , \源寄存器使用情况_1_r1_used , \源寄存器使用情况_1_r2_used ;
  wire [0:0] ex_mem_1_memout, \中断使能_q ;
  wire [1:0] id_ex_1_memout, multiplexer_6_out, priority_encoder_1_out;
  wire [1:1] \单周期硬布线控制器_1_memwrite ;
  wire [2:0] and_6_out, IR1_q, \中断屏蔽字_q ;
  wire [2:1] if_id_1_statusout;
  wire [3:0] ex_mem_1_wbout, id_ex_1_forwardout, id_ex_1_wbout, mem_wb_1_wbout, multiplexer_19_out,
       \单周期硬布线控制器_1_lhu , \数据相关检测_1_相关性 ;
  wire [4:0] ex_mem_1_targetout, id_ex_1_shamtout, id_ex_1_targetout, mem_wb_1_targetout, multiplexer_7_out,
       multiplexer_8_out, multiplexer_13_out, multiplexer_15_out, multiplexer_21_out;
  wire [5:0] EX_OP;
  wire [14:0] id_ex_1_exout, \单周期硬布线控制器_1_jr ;
  wire [15:0] \LoadUse次数 , multiplexer_25_out, \总周期数 , \插入气泡数 , \无条件分支数 , \条件分支成功数 ;
  wire [25:0] id_ex_1_irout;
  wire [27:0] multiplexer_19_out_2;
  wire [31:0] adder_1_out, adder_2_out, adder_3_out, adder_4_out, bit_extender_1_out, bit_extender_2_out,
       EPC_q, ex_mem_1_aluout, ex_mem_1_irout, id_ex_1_immout, id_ex_1_r1out, id_ex_1_r2out, if_id_1_irout,
       mem_wb_1_aluout, mem_wb_1_memdataout, mips_alu_1_result, mips_regifile_1_r1, mips_regifile_1_r2,
       multiplexer_1_out, multiplexer_2_out, multiplexer_3_out, multiplexer_4_out, multiplexer_5_out,
       multiplexer_9_out, multiplexer_16_out, multiplexer_18_out, multiplexer_20_out, multiplexer_22_out,
       multiplexer_23_out, multiplexer_24_out, multiplexer_26_out, multiplexer_27_out, newPC, ram_1_data,
       rom_1_data;

  Button \u_总复位  (.out(RST));
  Button _1 (.out(IR1));
  Button _2 (.out(IR2));
  Button _3 (.out(IR3));
  Button \u_继续运行  (.out(Go));
  LED #(.active("true")) led_1 (.in(W1));
  LED #(.active("true")) led_2 (.in(W2));
  LED #(.active("true")) led_3 (.in(W3));
  or or_1 (or_1_out, \中断CPU , ERET);
  Multiplexer #(.select(1), .width(32), .disabled("Z"), .enable("false")) multiplexer_1 (
    .in0(multiplexer_2_out), .in1(newPC), .out(multiplexer_1_out), .sel(or_1_out));
  not not_1 (not_1_out, or_9_out);
  D_Flip_Flop #(.trigger("rising"), .Pre_Clr_Positions("LEGACY"), .NegatePresetClear("false"), .enable("true"), .NewFFLayout("false")) d_ff_1 (
    .clk(IR1), .D(1'b1), .Q(d_ff_1_q), .reset(IR1_q[0]));  // open: Qn, preset, en
  or or_2 (W1, IR1_q[0], d_ff_1_q);
  D_Flip_Flop #(.trigger("rising"), .Pre_Clr_Positions("LEGACY"), .NegatePresetClear("false"), .enable("true"), .NewFFLayout("false")) d_ff_2 (
    .clk(IR2), .D(1'b1), .Q(d_ff_2_q), .reset(IR1_q[1]));  // open: Qn, preset, en
  or or_3 (W2, IR1_q[1], d_ff_2_q);
  D_Flip_Flop #(.trigger("rising"), .Pre_Clr_Positions("LEGACY"), .NegatePresetClear("false"), .enable("true"), .NewFFLayout("false")) d_ff_3 (
    .clk(IR3), .D(1'b1), .Q(d_ff_3_q), .reset(IR1_q[2]));  // open: Qn, preset, en
  or or_4 (W3, IR1_q[2], d_ff_3_q);
  Hex_Digit_Display hex_digit_display_1 (.value(LedData[31:28]));  // open: dp
  Multiplexer #(.select(1), .width(32), .disabled("Z"), .enable("false")) multiplexer_2 (
    .in0(adder_1_out), .in1(multiplexer_23_out), .out(multiplexer_2_out), .sel(Branch));
  Register #(.width(32), .trigger("rising"), .Select("low")) PC (
    .D(multiplexer_1_out), .en(not_1_out), .Q(IF_PC), .clk(CLK));  // open: clr
  and and_1 (and_1_out, rd0, MTC0);
  and and_2 (and_2_out, ~rd0, MTC0);  // AND_Gate
  or or_5 (or_5_out, d_ff_1_q, IR1_q[0]);
  or or_6 (or_6_out, d_ff_2_q, IR1_q[1]);
  or or_7 (or_7_out, d_ff_3_q, IR1_q[2]);
  Hex_Digit_Display hex_digit_display_2 (.value(LedData[23:20]));  // open: dp
  Hex_Digit_Display hex_digit_display_3 (.value(LedData[27:24]));  // open: dp
  Adder #(.width(32)) adder_1 (.a(32'h4), .b(IF_PC), .out(adder_1_out), .cin(1'b0));  // open: cout
  Multiplexer #(.select(1), .width(32), .disabled("Z"), .enable("false")) multiplexer_3 (
    .in0(multiplexer_5_out), .in1({multiplexer_19_out_2, multiplexer_19_out}), .out(multiplexer_3_out),
    .sel(and_2_out));
  or or_8 (or_8_out, and_2_out, \中断CPU );
  Hex_Digit_Display hex_digit_display_4 (.value(LedData[15:12]));  // open: dp
  Hex_Digit_Display hex_digit_display_5 (.value(LedData[19:16]));  // open: dp
  Register #(.width(32), .trigger("rising"), .Select("low")) EPC (
    .D(multiplexer_3_out), .en(or_8_out), .Q(EPC_q), .clk(CLK));  // open: clr
  and and_3 (and_3_out, or_5_out, ~demultiplexer_1_out1);  // AND_Gate
  and and_4 (and_4_out, or_6_out, ~demultiplexer_1_out2);  // AND_Gate
  and and_5 (and_5_out, or_7_out, ~demultiplexer_1_out3);  // AND_Gate
  Hex_Digit_Display hex_digit_display_6 (.value(LedData[11:8]));  // open: dp
  Hex_Digit_Display hex_digit_display_7 (.value(LedData[7:4]));  // open: dp
  Clock #(.highDuration(1), .lowDuration(1)) clock_1 (.out(CLK));
  ROM #(.addrWidth(10), .dataWidth(32), .Select("high")) rom_1 (.addr(IF_PC[11:2]), .data(rom_1_data), .sel(1'b1));
  or or_9 (or_9_out, not_6_out, load_use);
  Multiplexer #(.select(3), .width(32), .disabled("Z"), .enable("false")) multiplexer_4 (
    .in0(IF_PC), .in1(IF_PC), .in2(ID_PC), .in3(ID_PC), .in4(EX_PC), .in5(EX_PC), .in6(EX_PC), .in7(EX_PC),
    .out(multiplexer_4_out), .sel({if_id_1_statusout, 1'b1}));
  D_Flip_Flop #(.trigger("rising"), .Pre_Clr_Positions("LEGACY"), .NegatePresetClear("false"), .enable("true"), .NewFFLayout("false")) u_IR1 (
    .clk(CLK), .D(and_3_out), .Q(IR1_q[0]));  // open: Qn, preset, en, reset
  D_Flip_Flop #(.trigger("rising"), .Pre_Clr_Positions("LEGACY"), .NegatePresetClear("false"), .enable("true"), .NewFFLayout("false")) u_IR2 (
    .clk(CLK), .D(and_4_out), .Q(IR1_q[1]));  // open: Qn, preset, en, reset
  D_Flip_Flop #(.trigger("rising"), .Pre_Clr_Positions("LEGACY"), .NegatePresetClear("false"), .enable("true"), .NewFFLayout("false")) u_IR3 (
    .clk(CLK), .D(and_5_out), .Q(IR1_q[2]));  // open: Qn, preset, en, reset
  Register #(.width(3), .trigger("rising"), .Select("low")) \u_中断屏蔽字  (
    .D(multiplexer_19_out[3:1]), .en(and_1_out), .Q(\中断屏蔽字_q ), .clk(CLK));  // open: clr
  Hex_Digit_Display hex_digit_display_8 (.value(LedData[3:0]));  // open: dp
  Multiplexer #(.select(1), .width(32), .disabled("Z"), .enable("false")) multiplexer_5 (
    .in0(multiplexer_4_out), .in1(EPC_q), .out(multiplexer_5_out), .sel(ERET));
  assign and_6_out = IR1_q & ~\中断屏蔽字_q ;  // AND_Gate and_6, 3 bits wide
  or or_10 (or_10_out, Branch, \中断CPU , ERET);
  IF_ID if_id_1 (
    .IR(rom_1_data), .PC(IF_PC), .Status(1'b1),
    .IRout({if_id_1_irout[31:12], \单周期硬布线控制器_1_jr [13], if_id_1_irout[10:0]}), .PCout(ID_PC),
    .StatusOut(if_id_1_statusout[1]), .Clear(or_10_out), .CLK(CLK), .\使能端_低电平有效 (or_9_out));
  not not_2 (not_2_out, priority_encoder_1_en_out);
  Priority_Encoder #(.select(2), .disabled("Z")) priority_encoder_1 (
    .in0(1'b0), .in1(and_6_out[0]), .in2(and_6_out[1]), .in3(and_6_out[2]), .out(priority_encoder_1_out),
    .gs(priority_encoder_1_gs), .en_out(priority_encoder_1_en_out), .en_in(1'b1));
  // Probe on \总周期数 
  // Probe on \无条件分支数 
  // Probe on \条件分支成功数 
  // Probe on \插入气泡数 
  // Probe on \LoadUse次数 
  // Probe on priority_encoder_1_out
  Multiplexer #(.select(1), .width(2), .disabled("Z"), .enable("false")) multiplexer_6 (
    .in0(2'b00), .in1(priority_encoder_1_out), .out(multiplexer_6_out), .sel(priority_encoder_1_gs));
  Demultiplexer #(.select(2), .width(1), .tristate("false"), .disabled("Z"), .enable("false")) demultiplexer_1 (
    .out1(demultiplexer_1_out1), .out2(demultiplexer_1_out2), .out3(demultiplexer_1_out3), .in(ERET),
    .sel(multiplexer_6_out));  // open: out0
  // Probe on IF_PC[11:0]
  assign bit_extender_1_out = {{16{1'b0}}, {if_id_1_irout[15:12], \单周期硬布线控制器_1_jr [13], if_id_1_irout[10:0]}};  // Bit_Extender bit_extender_1
  assign bit_extender_2_out = {{16{if_id_1_irout[15]}}, {if_id_1_irout[15:12], \单周期硬布线控制器_1_jr [13], if_id_1_irout[10:0]}};  // Bit_Extender bit_extender_2
  // Probe on EX_PC[11:0]
  // Probe on ID_PC[11:0]
  \源寄存器使用情况  \u_源寄存器使用情况_1  (
    .OP0(if_id_1_irout[26]), .OP1(if_id_1_irout[27]), .OP2(if_id_1_irout[28]), .OP3(if_id_1_irout[29]),
    .OP4(if_id_1_irout[30]), .OP5(if_id_1_irout[31]), .F0(if_id_1_irout[0]), .F1(if_id_1_irout[1]),
    .F2(if_id_1_irout[2]), .F3(if_id_1_irout[3]), .F4(if_id_1_irout[4]), .F5(if_id_1_irout[5]),
    .R1_Used(\源寄存器使用情况_1_r1_used ), .R2_Used(\源寄存器使用情况_1_r2_used ));
  \单周期硬布线控制器  \u_单周期硬布线控制器_1  (
    .Func(if_id_1_irout[5:0]), .OP(if_id_1_irout[31:26]), .ALU_OP(\单周期硬布线控制器_1_jr [8:5]),
    .MemToReg(\单周期硬布线控制器_1_lhu [3]), .MemWrite(\单周期硬布线控制器_1_memwrite [1]), .ALU_SRC(\单周期硬布线控制器_1_jr [9]),
    .SysCALL(\单周期硬布线控制器_1_jr [11]), .SignedExt(SignedExt), .RegDst(\单周期硬布线控制器_1_regdst ),
    .JR(\单周期硬布线控制器_1_jr [0]), .JMP(\单周期硬布线控制器_1_jr [1]), .Beq(\单周期硬布线控制器_1_jr [3]),
    .JAL(\单周期硬布线控制器_1_lhu [2]), .Bne(\单周期硬布线控制器_1_jr [4]), .ShamtSrc(\单周期硬布线控制器_1_jr [10]),
    .LHU(\单周期硬布线控制器_1_lhu [0]), .BGEZ(\单周期硬布线控制器_1_jr [2]), .ERET(\单周期硬布线控制器_1_eret ),
    .CPsrc(if_id_1_irout[25:21]), .MFC0(\单周期硬布线控制器_1_jr [14]), .MTC0(\单周期硬布线控制器_1_jr [12]),
    .RegWrite(\单周期硬布线控制器_1_lhu [1]));  // open: COP0
  Multiplexer #(.select(1), .width(5), .disabled("Z"), .enable("false")) multiplexer_7 (
    .in0(if_id_1_irout[25:21]), .in1(5'b00010), .out(multiplexer_7_out), .sel(\单周期硬布线控制器_1_jr [11]));
  Multiplexer #(.select(1), .width(5), .disabled(0), .enable("false")) multiplexer_8 (
    .in0(if_id_1_irout[20:16]), .in1(5'b00100), .out(multiplexer_8_out), .sel(\单周期硬布线控制器_1_jr [11]));
  Multiplexer #(.select(1), .width(32), .disabled("Z"), .enable("false")) multiplexer_9 (
    .in0(bit_extender_1_out), .in1(bit_extender_2_out), .out(multiplexer_9_out), .sel(SignedExt));
  Multiplexer #(.select(1), .width(1), .disabled("Z"), .enable("false")) multiplexer_10 (
    .in0(\中断使能_q [0]), .in1(1'b1), .out(multiplexer_10_out), .sel(\中断CPU ));
  Multiplexer #(.select(1), .width(1), .disabled("Z"), .enable("false")) multiplexer_11 (
    .in0(multiplexer_10_out), .in1(1'b0), .out(multiplexer_11_out), .sel(ERET));
  // Probe on M_PC[11:0]
  Multiplexer #(.select(1), .width(1), .disabled("Z"), .enable("false")) multiplexer_12 (
    .in0(\源寄存器使用情况_1_r2_used ), .in1(1'b0), .out(multiplexer_12_out), .sel(\单周期硬布线控制器_1_jr [14]));
  Multiplexer #(.select(1), .width(5), .disabled("Z"), .enable("false")) multiplexer_13 (
    .in0(if_id_1_irout[20:16]), .in1({if_id_1_irout[15:12], \单周期硬布线控制器_1_jr [13]}), .out(multiplexer_13_out),
    .sel(\单周期硬布线控制器_1_regdst ));
  Register #(.width(1), .trigger("rising"), .Select("low")) \u_中断使能  (
    .D(multiplexer_14_out), .Q(\中断使能_q [0]), .clk(CLK));  // open: en, clr
  Multiplexer #(.select(1), .width(1), .disabled("Z"), .enable("false")) multiplexer_14 (
    .in0(multiplexer_11_out), .in1(multiplexer_19_out[0]), .out(multiplexer_14_out), .sel(and_1_out));
  // Probe on WB_PC[11:0]
  \数据相关检测  \u_数据相关检测_1  (
    .R1_num(multiplexer_7_out), .EX_WriteReg_num(id_ex_1_targetout), .MEM_WriteReg_num(ex_mem_1_targetout),
    .R2_num(multiplexer_8_out), .R1_Used(\源寄存器使用情况_1_r1_used ), .R2_Used(multiplexer_12_out),
    .\相关性 (\数据相关检测_1_相关性 ), .EX_RegWrite(id_ex_1_wbout[1]), .MEM_RegWrite(ex_mem_1_wbout[1]));  // open: 数据相关
  Multiplexer #(.select(1), .width(5), .disabled("Z"), .enable("false")) multiplexer_15 (
    .in0(multiplexer_13_out), .in1({5{1'b1}}), .out(multiplexer_15_out), .sel(\单周期硬布线控制器_1_lhu [2]));
  Multiplexer #(.select(1), .width(32), .disabled("Z"), .enable("false")) multiplexer_16 (
    .in0(EPC_q), .in1({{28{1'b0}}, \中断屏蔽字_q , \中断使能_q [0]}), .out(multiplexer_16_out), .sel(id_ex_1_irout[11]));
  and and_7 (\中断CPU , not_2_out, ~\中断使能_q [0]);  // AND_Gate
  and and_8 (and_8_out, load_use, multiplexer_29_out);
  \load_use检测  \load_use检测_1  (.\相关性 (\数据相关检测_1_相关性 ), .OP(EX_OP), .load_use(load_use));
  Multiplexer #(.select(1), .width(32), .disabled("Z"), .enable("false")) multiplexer_17 (
    .in0(multiplexer_5_out), .in1({{28{1'b0}}, priority_encoder_1_out, 2'b00}), .out(newPC), .sel(\中断CPU ));
  MIPS_Regifile mips_regifile_1 (
    .Din(RDin), .Clk(CLK), .R1(mips_regifile_1_r1), .R2(mips_regifile_1_r2), .WE(RegWrite),
    .W_num(mem_wb_1_targetout), .R1_num(multiplexer_7_out), .R2_num(multiplexer_8_out));
  Counter #(.width(16), .max('hffff), .ongoal("wrap"), .trigger("rising"), .behavior("new")) counter_1 (
    .load(1'b0), .D({16{1'b0}}), .count(and_8_out), .Q(\LoadUse次数 ), .clk(CLK), .preset(1'b0), .down(1'b0));  // open: carry, clr
  or or_11 (or_11_out, ERET, load_use, Branch, \中断CPU );
  ID_EX id_ex_1 (
    .WB(\单周期硬布线控制器_1_lhu ), .MEM({\单周期硬布线控制器_1_memwrite [1], \单周期硬布线控制器_1_lhu [3]}), .EX(\单周期硬布线控制器_1_jr ),
    .R1(mips_regifile_1_r1), .R2(mips_regifile_1_r2), .Status(if_id_1_statusout[1]), .WBout(id_ex_1_wbout),
    .MEMout(id_ex_1_memout), .EXout({id_ex_1_exout[14], rd0, MTC0, id_ex_1_exout[11:0]}),
    .R1out(id_ex_1_r1out), .R2out(id_ex_1_r2out), .StatusOut(if_id_1_statusout[2]), .Clear(or_11_out),
    .CLK(CLK), .\使能端_低电平有效 (not_6_out), .Shamt(if_id_1_irout[10:6]), .ShamtOut(id_ex_1_shamtout),
    .Imm(multiplexer_9_out), .ImmOut(id_ex_1_immout), .PC(ID_PC), .PCout(EX_PC),
    .IR({if_id_1_irout[31:12], \单周期硬布线控制器_1_jr [13], if_id_1_irout[10:0]}), .IRout({EX_OP, id_ex_1_irout}),
    .Target(multiplexer_15_out), .TargetOut(id_ex_1_targetout), .Forward(\数据相关检测_1_相关性 ),
    .ForwardOut(id_ex_1_forwardout), .ERET(\单周期硬布线控制器_1_eret ), .ERETout(ERET));
  Multiplexer #(.select(2), .width(32), .disabled("Z"), .enable("false")) multiplexer_18 (
    .in0(id_ex_1_r1out), .in1(RDin), .in2(ex_mem_1_aluout), .in3(ex_mem_1_aluout), .out(multiplexer_18_out),
    .sel(id_ex_1_forwardout[3:2]));
  Multiplexer #(.select(2), .width(32), .disabled("Z"), .enable("false")) multiplexer_19 (
    .in0(id_ex_1_r2out), .in1(RDin), .in2(ex_mem_1_aluout), .in3(ex_mem_1_aluout),
    .out({multiplexer_19_out_2, multiplexer_19_out}), .sel(id_ex_1_forwardout[1:0]));
  Adder #(.width(32)) adder_2 (.a(32'h4), .b(EX_PC), .out(adder_2_out));  // open: cin, cout
  Multiplexer #(.select(1), .width(32), .disabled("Z"), .enable("false")) multiplexer_20 (
    .in0({multiplexer_19_out_2, multiplexer_19_out}), .in1(id_ex_1_immout), .out(multiplexer_20_out),
    .sel(id_ex_1_exout[9]));
  not not_3 (not_3_out, mips_alu_1_equal);
  MIPS_ALU mips_alu_1 (
    .X(multiplexer_18_out), .Y(multiplexer_20_out), .AluOP(id_ex_1_exout[8:5]), .Equal(mips_alu_1_equal),
    .Result(mips_alu_1_result), .shamt(multiplexer_21_out));  // open: Result_2
  Multiplexer #(.select(1), .width(5), .disabled("Z"), .enable("false")) multiplexer_21 (
    .in0(id_ex_1_shamtout), .in1(multiplexer_18_out[4:0]), .out(multiplexer_21_out), .sel(id_ex_1_exout[10]));
  Adder #(.width(32)) adder_3 (
    .a(adder_2_out), .b({id_ex_1_immout[29:0], 2'b00}), .out(adder_3_out));  // open: cin, cout
  Multiplexer #(.select(1), .width(32), .disabled("Z"), .enable("false")) multiplexer_22 (
    .in0(adder_3_out), .in1(multiplexer_18_out), .out(multiplexer_22_out), .sel(id_ex_1_exout[0]));
  not not_4 (not_4_out, multiplexer_18_out[31]);
  Multiplexer #(.select(1), .width(32), .disabled("Z"), .enable("false")) multiplexer_23 (
    .in0(multiplexer_22_out), .in1({EX_PC[31:28], id_ex_1_irout, 2'b00}), .out(multiplexer_23_out),
    .sel(id_ex_1_exout[1]));
  or or_12 (or_12_out, id_ex_1_exout[0], id_ex_1_exout[1]);
  and and_9 (and_9_out, id_ex_1_exout[2], not_4_out);
  or or_13 (or_13_out, and_9_out, and_10_out, and_11_out);
  and and_10 (and_10_out, id_ex_1_exout[3], mips_alu_1_equal);
  and and_11 (and_11_out, id_ex_1_exout[4], not_3_out);
  Comparator #(.width(32), .mode("twosComplement")) comparator_1 (
    .a(32'h22), .b(multiplexer_18_out), .eq(comparator_1_eq));  // open: gt, lt
  Multiplexer #(.select(1), .width(32), .disabled("Z"), .enable("false")) multiplexer_24 (
    .in0(mips_alu_1_result), .in1(multiplexer_16_out), .out(multiplexer_24_out), .sel(id_ex_1_exout[14]));
  or or_14 (Branch, or_12_out, or_13_out);
  and and_12 (and_12_out, id_ex_1_exout[11], ~comparator_1_eq);  // AND_Gate
  and and_13 (and_13_out, id_ex_1_exout[11], comparator_1_eq);
  Counter #(.width(16), .max('hffff), .ongoal("wrap"), .trigger("rising"), .behavior("new")) counter_2 (
    .load(1'b0), .D({16{1'b0}}), .count(or_12_out), .Q(\无条件分支数 ), .clk(CLK), .preset(1'b0), .down(1'b0));  // open: carry, clr
  Register #(.width(32), .trigger("rising"), .Select("low")) register_1 (
    .D({multiplexer_19_out_2, multiplexer_19_out}), .en(and_13_out), .Q(LedData), .clk(CLK));  // open: clr
  EX_MEM ex_mem_1 (
    .WB(id_ex_1_wbout), .MEM(id_ex_1_memout), .ALU(multiplexer_24_out),
    .R2({multiplexer_19_out_2, multiplexer_19_out}), .IR({EX_OP, id_ex_1_irout}), .PC(EX_PC),
    .Status(if_id_1_statusout[2]), .WBout(ex_mem_1_wbout), .MEMout({MemWrite, ex_mem_1_memout[0]}),
    .ALUout(ex_mem_1_aluout), .R2out(MDin), .IRout(ex_mem_1_irout), .PCout(M_PC),
    .StatusOut(ex_mem_1_statusout), .Clear(\中断CPU ), .CLK(CLK), .\使能端_低电平有效 (not_6_out), .Stop(and_12_out),
    .StopOut(ex_mem_1_stopout), .Target(id_ex_1_targetout), .TargetOut(ex_mem_1_targetout));
  Counter #(.width(16), .max('hffff), .ongoal("wrap"), .trigger("rising"), .behavior("new")) counter_3 (
    .load(1'b0), .D({16{1'b0}}), .count(or_13_out), .Q(\条件分支成功数 ), .clk(CLK), .preset(1'b0), .down(1'b0));  // open: carry, clr
  RAM #(.addrWidth(10), .dataWidth(32), .bus("separate"), .Select("high")) ram_1 (
    .addr(ex_mem_1_aluout[11:2]), .din(MDin), .data(ram_1_data), .str(MemWrite), .sel(1'b1), .clk(CLK),
    .ld(ex_mem_1_memout[0]));  // open: clr
  MEM_WB mem_wb_1 (
    .WB(ex_mem_1_wbout), .ALU(ex_mem_1_aluout), .MemData(ram_1_data), .IR(ex_mem_1_irout), .PC(M_PC),
    .Status(ex_mem_1_statusout), .WBout({mem_wb_1_wbout[3:2], RegWrite, mem_wb_1_wbout[0]}),
    .ALUout(mem_wb_1_aluout), .MemDataOut(mem_wb_1_memdataout), .PCout(WB_PC), .CLK(CLK),
    .\使能端_低电平有效 (not_6_out), .Stop(ex_mem_1_stopout), .StopOut(mem_wb_1_stopout),
    .Target(ex_mem_1_targetout), .TargetOut(mem_wb_1_targetout));  // open: IRout, StatusOut, Clear
  Multiplexer #(.select(1), .width(16), .disabled("Z"), .enable("false")) multiplexer_25 (
    .in0(mem_wb_1_memdataout[15:0]), .in1(mem_wb_1_memdataout[31:16]), .out(multiplexer_25_out),
    .sel(mem_wb_1_aluout[1]));
  Adder #(.width(32)) adder_4 (.a(32'h4), .b(WB_PC), .out(adder_4_out));  // open: cin, cout
  Multiplexer #(.select(1), .width(32), .disabled("Z"), .enable("false")) multiplexer_26 (
    .in0(mem_wb_1_memdataout), .in1({{16{1'b0}}, multiplexer_25_out}), .out(multiplexer_26_out),
    .sel(mem_wb_1_wbout[0]));
  Multiplexer #(.select(1), .width(32), .disabled("Z"), .enable("false")) multiplexer_27 (
    .in0(mem_wb_1_aluout), .in1(multiplexer_26_out), .out(multiplexer_27_out), .sel(mem_wb_1_wbout[3]));
  Multiplexer #(.select(1), .width(32), .disabled("Z"), .enable("false")) multiplexer_28 (
    .in0(multiplexer_27_out), .in1(adder_4_out), .out(RDin), .sel(mem_wb_1_wbout[2]));
  not not_5 (not_5_out, mem_wb_1_stopout);
  not not_6 (not_6_out, multiplexer_29_out);
  Multiplexer #(.select(1), .width(1), .disabled("Z"), .enable("false")) multiplexer_29 (
    .in0(not_5_out), .in1(mem_wb_1_stopout), .out(multiplexer_29_out), .sel(Go));
  Counter #(.width(16), .max('hffff), .ongoal("wrap"), .trigger("rising"), .behavior("new")) counter_4 (
    .load(1'b0), .D({16{1'b0}}), .count(multiplexer_29_out), .Q(\总周期数 ), .clk(CLK), .preset(1'b0), .down(1'b0));  // open: carry, clr

  // Other names for the same wires on the sheet: MEM_PC[31:0] = M_PC

  // Notes on the sheet:
  //   中断源
  //   中断等待指示
  //   数码管输出
  //   指令存储器
  //   指令字
  //   contents of rom_1 (hex, n*v repeats v):
  //   20100000 20110000 20120000 20130000 36100000 36310001 36520002 36730003 ae100000 ae110004 ae120008
  //   ae13000c 2002000a 20110000 20120000 20130000 c
  //   OP
  //   Func
  //   rs
  //   rt
  //   rd
  //   shamt
  //   JMP
  //   JR
  //   LHU
  //   OP
  //   Func
  //   Syscall
  //   BGEZ
  //   Beq
  //   Bne
  //   MemToReg
  //   MemWrite
  //   AluOP
  //   AluSrcB
  //   RegWrite
  //   JAL
  //   RegDst
  //   ShamtSrc
  //   流水调试日志用
  //   为方便自动评测，需要输出流水线各段保存的PC值，注意是PC不是PC+4，另外ID段寄存器写入信息，Mem段内存写入信息也要输出
endmodule

module \气泡流水线  (
);

  wire and_1_out, and_2_out, and_3_out, and_4_out, and_5_out, and_6_out, Branch, CLK, comparator_1_eq,
       ex_mem_1_statusout, ex_mem_1_stopout, Go, id_ex_1_statusout, if_id_1_statusout, IR1, IR2, IR3,
       mem_wb_1_stopout, mips_alu_1_equal, multiplexer_15_out, not_1_out, not_2_out, not_3_out, not_4_out,
       not_5_out, or_1_out, or_2_out, or_3_out, or_4_out, RST, SignedExt, W1, W2, W3, \单周期硬布线控制器_1_regdst ,
       \数据相关 , \源寄存器使用情况_1_r1_used , \源寄存器使用情况_1_r2_used ;
  wire [1:0] ex_mem_1_memout, id_ex_1_memout;
  wire [1:1] \单周期硬布线控制器_1_memwrite ;
  wire [3:0] ex_mem_1_wbout, id_ex_1_wbout, mem_wb_1_wbout, \单周期硬布线控制器_1_lhu ;
  wire [4:0] ex_mem_1_targetout, id_ex_1_shamtout, id_ex_1_targetout, mem_wb_1_targetout, multiplexer_2_out,
       multiplexer_3_out, multiplexer_5_out, multiplexer_6_out, multiplexer_8_out;
  wire [14:0] id_ex_1_exout, \单周期硬布线控制器_1_jr ;
  wire [15:0] \LoadUse次数 , multiplexer_11_out, \总周期数 , \插入气泡数 , \无条件分支数 , \条件分支成功数 ;
  wire [31:0] adder_1_out, adder_2_out, adder_3_out, adder_4_out, bit_extender_1_out, bit_extender_2_out,
       ex_mem_1_aluout, ex_mem_1_irout, ex_mem_1_r2out, EX_PC, id_ex_1_immout, id_ex_1_irout, id_ex_1_r1out,
       id_ex_1_r2out, ID_PC, if_id_1_irout, IF_PC, LedData, MEM_PC, mem_wb_1_aluout, mem_wb_1_memdataout,
       mips_alu_1_result, mips_regifile_1_r1, mips_regifile_1_r2, multiplexer_1_out, multiplexer_4_out,
       multiplexer_7_out, multiplexer_9_out, multiplexer_10_out, multiplexer_12_out, multiplexer_13_out,
       multiplexer_14_out, ram_1_data, rom_1_data, WB_PC;

  Button \u_总复位  (.out(RST));
  Button _1 (.out(IR1));
  Button _2 (.out(IR2));
  Button _3 (.out(IR3));
  Button \u_继续运行  (.out(Go));
  LED #(.active("true")) led_1 (.in(W1));
  LED #(.active("true")) led_2 (.in(W2));
  LED #(.active("true")) led_3 (.in(W3));
  not not_1 (not_1_out, or_1_out);
  Hex_Digit_Display hex_digit_display_1 (.value(LedData[31:28]));  // open: dp
  Multiplexer #(.select(1), .width(32), .disabled("Z"), .enable("false")) multiplexer_1 (
    .in0(adder_1_out), .in1(multiplexer_10_out), .out(multiplexer_1_out), .sel(Branch));
  Register #(.width(32), .trigger("rising"), .Select("low")) PC (
    .D(multiplexer_1_out), .en(not_1_out), .Q(IF_PC), .clk(CLK));  // open: clr
  Hex_Digit_Display hex_digit_display_2 (.value(LedData[23:20]));  // open: dp
  Hex_Digit_Display hex_digit_display_3 (.value(LedData[27:24]));  // open: dp
  Adder #(.width(32)) adder_1 (.a(32'h4), .b(IF_PC), .out(adder_1_out), .cin(1'b0));  // open: cout
  Hex_Digit_Display hex_digit_display_4 (.value(LedData[15:12]));  // open: dp
  Hex_Digit_Display hex_digit_display_5 (.value(LedData[19:16]));  // open: dp
  Hex_Digit_Display hex_digit_display_6 (.value(LedData[7:4]));  // open: dp
  Hex_Digit_Display hex_digit_display_7 (.value(LedData[11:8]));  // open: dp
  Clock #(.highDuration(1), .lowDuration(1)) clock_1 (.out(CLK));
  ROM #(.addrWidth(10), .dataWidth(32), .Select("high")) rom_1 (.addr(IF_PC[11:2]), .data(rom_1_data), .sel(1'b1));
  or or_1 (or_1_out, not_4_out, \数据相关 );
  Hex_Digit_Display hex_digit_display_8 (.value(LedData[3:0]));  // open: dp
  IF_ID if_id_1 (
    .IR(rom_1_data), .PC(IF_PC), .Status(1'b1), .IRout(if_id_1_irout), .PCout(ID_PC),
    .StatusOut(if_id_1_statusout), .Clear(Branch), .CLK(CLK), .\使能端_低电平有效 (or_1_out));
  // Probe on \总周期数 
  // Probe on \无条件分支数 
  // Probe on \条件分支成功数 
  // Probe on \插入气泡数 
  // Probe on \LoadUse次数 
  // Probe on IF_PC[11:0]
  assign bit_extender_1_out = {{16{1'b0}}, if_id_1_irout[15:0]};  // Bit_Extender bit_extender_1
  assign bit_extender_2_out = {{16{if_id_1_irout[15]}}, if_id_1_irout[15:0]};  // Bit_Extender bit_extender_2
  // Probe on ID_PC[11:0]
  // Probe on EX_PC[11:0]
  \源寄存器使用情况  \u_源寄存器使用情况_1  (
    .OP0(if_id_1_irout[26]), .OP1(if_id_1_irout[27]), .OP2(if_id_1_irout[28]), .OP3(if_id_1_irout[29]),
    .OP4(if_id_1_irout[30]), .OP5(if_id_1_irout[31]), .F0(if_id_1_irout[0]), .F1(if_id_1_irout[1]),
    .F2(if_id_1_irout[2]), .F3(if_id_1_irout[3]), .F4(if_id_1_irout[4]), .F5(if_id_1_irout[5]),
    .R1_Used(\源寄存器使用情况_1_r1_used ), .R2_Used(\源寄存器使用情况_1_r2_used ));
  \单周期硬布线控制器  \u_单周期硬布线控制器_1  (
    .Func(if_id_1_irout[5:0]), .OP(if_id_1_irout[31:26]), .ALU_OP(\单周期硬布线控制器_1_jr [8:5]),
    .MemToReg(\单周期硬布线控制器_1_lhu [3]), .MemWrite(\单周期硬布线控制器_1_memwrite [1]), .ALU_SRC(\单周期硬布线控制器_1_jr [9]),
    .SysCALL(\单周期硬布线控制器_1_jr [11]), .SignedExt(SignedExt), .RegDst(\单周期硬布线控制器_1_regdst ),
    .JR(\单周期硬布线控制器_1_jr [0]), .JMP(\单周期硬布线控制器_1_jr [1]), .Beq(\单周期硬布线控制器_1_jr [3]),
    .JAL(\单周期硬布线控制器_1_lhu [2]), .Bne(\单周期硬布线控制器_1_jr [4]), .ShamtSrc(\单周期硬布线控制器_1_jr [10]),
    .LHU(\单周期硬布线控制器_1_lhu [0]), .BGEZ(\单周期硬布线控制器_1_jr [2]), .RegWrite(\单周期硬布线控制器_1_lhu [1]));  // open: ERET, COP0, CPsrc, MFC0, MTC0
  Multiplexer #(.select(1), .width(5), .disabled("Z"), .enable("false")) multiplexer_2 (
    .in0(if_id_1_irout[25:21]), .in1(5'b00010), .out(multiplexer_2_out), .sel(\单周期硬布线控制器_1_jr [11]));
  Multiplexer #(.select(1), .width(5), .disabled(0), .enable("false")) multiplexer_3 (
    .in0(if_id_1_irout[20:16]), .in1(5'b00100), .out(multiplexer_3_out), .sel(\单周期硬布线控制器_1_jr [11]));
  Multiplexer #(.select(1), .width(32), .disabled("Z"), .enable("false")) multiplexer_4 (
    .in0(bit_extender_1_out), .in1(bit_extender_2_out), .out(multiplexer_4_out), .sel(SignedExt));
  // Probe on MEM_PC[11:0]
  Multiplexer #(.select(1), .width(5), .disabled("Z"), .enable("false")) multiplexer_5 (
    .in0(if_id_1_irout[20:16]), .in1(if_id_1_irout[15:11]), .out(multiplexer_5_out),
    .sel(\单周期硬布线控制器_1_regdst ));
  Multiplexer #(.select(1), .width(5), .disabled("Z"), .enable("false")) multiplexer_6 (
    .in0(multiplexer_5_out), .in1({5{1'b1}}), .out(multiplexer_6_out), .sel(\单周期硬布线控制器_1_lhu [2]));
  // Probe on WB_PC[11:0]
  \数据相关检测  \u_数据相关检测_1  (
    .R1_num(multiplexer_2_out), .EX_WriteReg_num(id_ex_1_targetout), .MEM_WriteReg_num(ex_mem_1_targetout),
    .R2_num(multiplexer_3_out), .R1_Used(\源寄存器使用情况_1_r1_used ), .R2_Used(\源寄存器使用情况_1_r2_used ),
    .\数据相关 (\数据相关 ), .EX_RegWrite(id_ex_1_wbout[1]), .MEM_RegWrite(ex_mem_1_wbout[1]));  // open: 相关性
  MIPS_Regifile mips_regifile_1 (
    .Din(multiplexer_14_out), .Clk(CLK), .R1(mips_regifile_1_r1), .R2(mips_regifile_1_r2),
    .WE(mem_wb_1_wbout[1]), .W_num(mem_wb_1_targetout), .R1_num(multiplexer_2_out), .R2_num(multiplexer_3_out));
  or or_2 (or_2_out, \数据相关 , Branch);
  ID_EX id_ex_1 (
    .WB(\单周期硬布线控制器_1_lhu ), .MEM({\单周期硬布线控制器_1_memwrite [1], \单周期硬布线控制器_1_lhu [3]}), .EX(\单周期硬布线控制器_1_jr ),
    .R1(mips_regifile_1_r1), .R2(mips_regifile_1_r2), .Status(if_id_1_statusout), .WBout(id_ex_1_wbout),
    .MEMout(id_ex_1_memout), .EXout(id_ex_1_exout), .R1out(id_ex_1_r1out), .R2out(id_ex_1_r2out),
    .StatusOut(id_ex_1_statusout), .Clear(or_2_out), .CLK(CLK), .\使能端_低电平有效 (not_4_out),
    .Shamt(if_id_1_irout[10:6]), .ShamtOut(id_ex_1_shamtout), .Imm(multiplexer_4_out),
    .ImmOut(id_ex_1_immout), .PC(ID_PC), .PCout(EX_PC), .IR(if_id_1_irout), .IRout(id_ex_1_irout),
    .Target(multiplexer_6_out), .TargetOut(id_ex_1_targetout));  // open: Forward, ForwardOut, ERET, ERETout
  and and_1 (and_1_out, \数据相关 , multiplexer_15_out);
  Counter #(.width(16), .max('hffff), .ongoal("wrap"), .trigger("rising"), .behavior("new")) counter_1 (
    .load(1'b0), .D({16{1'b0}}), .count(and_1_out), .Q(\插入气泡数 ), .clk(CLK), .preset(1'b0), .down(1'b0));  // open: carry, clr
  Adder #(.width(32)) adder_2 (.a(32'h4), .b(EX_PC), .out(adder_2_out));  // open: cin, cout
  Multiplexer #(.select(1), .width(32), .disabled("Z"), .enable("false")) multiplexer_7 (
    .in0(id_ex_1_r2out), .in1(id_ex_1_immout), .out(multiplexer_7_out), .sel(id_ex_1_exout[9]));
  not not_2 (not_2_out, mips_alu_1_equal);
  MIPS_ALU mips_alu_1 (
    .X(id_ex_1_r1out), .Y(multiplexer_7_out), .AluOP(id_ex_1_exout[8:5]), .Equal(mips_alu_1_equal),
    .Result(mips_alu_1_result), .shamt(multiplexer_8_out));  // open: Result_2
  Multiplexer #(.select(1), .width(5), .disabled("Z"), .enable("false")) multiplexer_8 (
    .in0(id_ex_1_shamtout), .in1(id_ex_1_r1out[4:0]), .out(multiplexer_8_out), .sel(id_ex_1_exout[10]));
  Adder #(.width(32)) adder_3 (
    .a(adder_2_out), .b({id_ex_1_immout[29:0], 2'b00}), .out(adder_3_out));  // open: cin, cout
  Multiplexer #(.select(1), .width(32), .disabled("Z"), .enable("false")) multiplexer_9 (
    .in0(adder_3_out), .in1(id_ex_1_r1out), .out(multiplexer_9_out), .sel(id_ex_1_exout[0]));
  not not_3 (not_3_out, id_ex_1_r1out[31]);
  Multiplexer #(.select(1), .width(32), .disabled("Z"), .enable("false")) multiplexer_10 (
    .in0(multiplexer_9_out), .in1({EX_PC[31:28], id_ex_1_irout[25:0], 2'b00}), .out(multiplexer_10_out),
    .sel(id_ex_1_exout[1]));
  and and_2 (and_2_out, id_ex_1_exout[2], not_3_out);
  and and_3 (and_3_out, id_ex_1_exout[3], mips_alu_1_equal);
  and and_4 (and_4_out, id_ex_1_exout[4], not_2_out);
  or or_3 (or_3_out, id_ex_1_exout[0], id_ex_1_exout[1]);
  or or_4 (or_4_out, and_2_out, and_3_out, and_4_out);
  Comparator #(.width(32), .mode("twosComplement")) comparator_1 (
    .a(32'h22), .b(id_ex_1_r1out), .eq(comparator_1_eq));  // open: gt, lt
  or or_5 (Branch, or_3_out, or_4_out);
  Counter #(.width(16), .max('hffff), .ongoal("wrap"), .trigger("rising"), .behavior("new")) counter_2 (
    .load(1'b0), .D({16{1'b0}}), .count(or_3_out), .Q(\无条件分支数 ), .clk(CLK), .preset(1'b0), .down(1'b0));  // open: carry, clr
  and and_5 (and_5_out, id_ex_1_exout[11], ~comparator_1_eq);  // AND_Gate
  and and_6 (and_6_out, id_ex_1_exout[11], comparator_1_eq);
  Register #(.width(32), .trigger("rising"), .Select("low")) register_1 (
    .D(id_ex_1_r2out), .en(and_6_out), .Q(LedData), .clk(CLK));  // open: clr
  Counter #(.width(16), .max('hffff), .ongoal("wrap"), .trigger("rising"), .behavior("new")) counter_3 (
    .load(1'b0), .D({16{1'b0}}), .count(or_4_out), .Q(\条件分支成功数 ), .clk(CLK), .preset(1'b0), .down(1'b0));  // open: carry, clr
  EX_MEM ex_mem_1 (
    .WB(id_ex_1_wbout), .MEM(id_ex_1_memout), .ALU(mips_alu_1_result), .R2(id_ex_1_r2out),
    .IR(id_ex_1_irout), .PC(EX_PC), .Status(id_ex_1_statusout), .WBout(ex_mem_1_wbout),
    .MEMout(ex_mem_1_memout), .ALUout(ex_mem_1_aluout), .R2out(ex_mem_1_r2out), .IRout(ex_mem_1_irout),
    .PCout(MEM_PC), .StatusOut(ex_mem_1_statusout), .CLK(CLK), .\使能端_低电平有效 (not_4_out), .Stop(and_5_out),
    .StopOut(ex_mem_1_stopout), .Target(id_ex_1_targetout), .TargetOut(ex_mem_1_targetout));  // open: Clear
  RAM #(.addrWidth(10), .dataWidth(32), .bus("separate"), .Select("high")) ram_1 (
    .addr(ex_mem_1_aluout[11:2]), .din(ex_mem_1_r2out), .data(ram_1_data), .str(ex_mem_1_memout[1]),
    .sel(1'b1), .clk(CLK), .ld(ex_mem_1_memout[0]));  // open: clr
  MEM_WB mem_wb_1 (
    .WB(ex_mem_1_wbout), .ALU(ex_mem_1_aluout), .MemData(ram_1_data), .IR(ex_mem_1_irout), .PC(MEM_PC),
    .Status(ex_mem_1_statusout), .WBout(mem_wb_1_wbout), .ALUout(mem_wb_1_aluout),
    .MemDataOut(mem_wb_1_memdataout), .PCout(WB_PC), .CLK(CLK), .\使能端_低电平有效 (not_4_out),
    .Stop(ex_mem_1_stopout), .StopOut(mem_wb_1_stopout), .Target(ex_mem_1_targetout),
    .TargetOut(mem_wb_1_targetout));  // open: IRout, StatusOut, Clear
  Multiplexer #(.select(1), .width(16), .disabled("Z"), .enable("false")) multiplexer_11 (
    .in0(mem_wb_1_memdataout[15:0]), .in1(mem_wb_1_memdataout[31:16]), .out(multiplexer_11_out),
    .sel(mem_wb_1_aluout[1]));
  Adder #(.width(32)) adder_4 (.a(32'h4), .b(WB_PC), .out(adder_4_out));  // open: cin, cout
  Multiplexer #(.select(1), .width(32), .disabled("Z"), .enable("false")) multiplexer_12 (
    .in0(mem_wb_1_memdataout), .in1({{16{1'b0}}, multiplexer_11_out}), .out(multiplexer_12_out),
    .sel(mem_wb_1_wbout[0]));
  Multiplexer #(.select(1), .width(32), .disabled("Z"), .enable("false")) multiplexer_13 (
    .in0(mem_wb_1_aluout), .in1(multiplexer_12_out), .out(multiplexer_13_out), .sel(mem_wb_1_wbout[3]));
  Multiplexer #(.select(1), .width(32), .disabled("Z"), .enable("false")) multiplexer_14 (
    .in0(multiplexer_13_out), .in1(adder_4_out), .out(multiplexer_14_out), .sel(mem_wb_1_wbout[2]));
  not not_4 (not_4_out, multiplexer_15_out);
  not not_5 (not_5_out, mem_wb_1_stopout);
  Multiplexer #(.select(1), .width(1), .disabled("Z"), .enable("false")) multiplexer_15 (
    .in0(not_5_out), .in1(mem_wb_1_stopout), .out(multiplexer_15_out), .sel(Go));
  Counter #(.width(16), .max('hffff), .ongoal("wrap"), .trigger("rising"), .behavior("new")) counter_4 (
    .load(1'b0), .D({16{1'b0}}), .count(multiplexer_15_out), .Q(\总周期数 ), .clk(CLK), .preset(1'b0), .down(1'b0));  // open: carry, clr

  // Notes on the sheet:
  //   中断源
  //   中断等待指示
  //   数码管输出
  //   指令存储器
  //   指令字
  //   contents of rom_1 (hex, n*v repeats v):
  //   20110001 8000c05 20110001 20120002 20130003 8000c09 20110001 20120002 20130003 8000c0d 20110001
  //   20120002 20130003 8000c11 20110001 20120002 20130003 c000cb8 20100001 20110001 118fc0 112020
  //   20020022 c 118882 12200001 8000c15 112020 20020022 c 20110001 118880 112020 20020022 c 12200001
  //   8000c1f 20110001 118fc0 112020 20020022 c 1188c3 112020 20020022 c 118903 112020 20020022 c 118903
  //   112020 20020022 c 118903 112020 20020022 c 118903 112020 20020022 c 118903 112020 20020022 c 118903
  //   112020 20020022 c 118903 112020 20020022 c 20100001 109fc0 139fc3 8021 2012000c 24160003 26100001
  //   3210000f 20080008 20090001 139900 2709825 132020 20020022 c 1094022 1500fff9 22100001 2018000f
  //   2188024 108700 20080008 20090001 139902 2709825 132021 20020022 c 1094022 1500fff9 108702 2c9b022
  //   12c00001 8000c50 4020 1084027 84400 3508ffff 82021 20020022 c 2010ffff 20110000 ae300000 22100001
  //   22310004 ae300000 22100001 22310004 ae300000 22100001 22310004 ae300000 22100001 22310004 ae300000
  //   22100001 22310004 ae300000 22100001 22310004 ae300000 22100001 22310004 ae300000 22100001 22310004
  //   ae300000 22100001 22310004 ae300000 22100001 22310004 ae300000 22100001 22310004 ae300000 22100001
  //   22310004 ae300000 22100001 22310004 ae300000 22100001 22310004 ae300000 22100001 22310004 ae300000
  //   22100001 22310004 22100001 8020 2011003c 8e130000 8e340000 274402a 11000002 ae330000 ae140000
  //   2231fffc 1611fff8 102020 20020022 c 22100004 2011003c 1611fff2 20020032 c 20100000 22100001 102020
  //   20020022 c 22100002 102020 20020022 c 22100003 102020 20020022 c 22100004 102020 20020022 c 22100005
  //   102020 20020022 c 22100006 102020 20020022 c 22100007 102020 20020022 c 22100008 102020 20020022
  //   20020022 c 3e00008
  //   OP
  //   Func
  //   rs
  //   rt
  //   rd
  //   shamt
  //   JMP
  //   JR
  //   LHU
  //   OP
  //   Func
  //   Syscall
  //   BGEZ
  //   Beq
  //   Bne
  //   MemToReg
  //   MemWrite
  //   AluOP
  //   AluSrcB
  //   RegWrite
  //   JAL
  //   RegDst
  //   ShamtSrc
  //   流水调试日志用
endmodule
module \重定向流水线  (
  output RegWrite,
  output MemWrite,
  output [31:0] IF_PC,
  output [31:0] ID_PC,
  output [31:0] EX_PC,
  output [31:0] M_PC,
  output [31:0] WB_PC,
  output [31:0] RDin,
  output [31:0] MDin,
  output [31:0] LedData
);

  wire and_1_out, and_2_out, and_3_out, and_4_out, and_5_out, and_8_out, and_9_out, and_10_out, and_11_out,
       and_12_out, and_13_out, Branch, CLK, comparator_1_eq, d_ff_1_q, d_ff_2_q, d_ff_3_q,
       demultiplexer_1_out1, demultiplexer_1_out2, demultiplexer_1_out3, ERET, ex_mem_1_statusout,
       ex_mem_1_stopout, Go, IR1, IR2, IR3, load_use, mem_wb_1_stopout, mips_alu_1_equal, MTC0,
       multiplexer_10_out, multiplexer_11_out, multiplexer_12_out, multiplexer_14_out, multiplexer_29_out,
       not_1_out, not_2_out, not_3_out, not_4_out, not_5_out, not_6_out, or_1_out, or_5_out, or_6_out,
       or_7_out, or_8_out, or_9_out, or_10_out, or_11_out, or_12_out, or_13_out, priority_encoder_1_en_out,
       priority_encoder_1_gs, rd0, RST, SignedExt, W1, W2, W3, \中断CPU , \单周期硬布线控制器_1_eret ,
       \单周期硬布线控制器_1_regdst , \源寄存器使用情况_1_r1_used , \源寄存器使用情况_1_r2_used ;
  wire [0:0] ex_mem_1_memout, \中断使能_q ;
  wire [1:0] id_ex_1_memout, multiplexer_6_out, priority_encoder_1_out;
  wire [1:1] \单周期硬布线控制器_1_memwrite ;
  wire [2:0] and_6_out, IR1_q, \中断屏蔽字_q ;
  wire [2:1] if_id_1_statusout;
  wire [3:0] ex_mem_1_wbout, id_ex_1_forwardout, id_ex_1_wbout, mem_wb_1_wbout, multiplexer_19_out,
       \单周期硬布线控制器_1_lhu , \数据相关检测_1_相关性 ;
  wire [4:0] ex_mem_1_targetout, id_ex_1_shamtout, id_ex_1_targetout, mem_wb_1_targetout, multiplexer_7_out,
       multiplexer_8_out, multiplexer_13_out, multiplexer_15_out, multiplexer_21_out;
  wire [5:0] EX_OP;
  wire [14:0] id_ex_1_exout, \单周期硬布线控制器_1_jr ;
  wire [15:0] \LoadUse次数 , multiplexer_25_out, \总周期数 , \插入气泡数 , \无条件分支数 , \条件分支成功数 ;
  wire [25:0] id_ex_1_irout;
  wire [27:0] multiplexer_19_out_2;
  wire [31:0] adder_1_out, adder_2_out, adder_3_out, adder_4_out, bit_extender_1_out, bit_extender_2_out,
       EPC_q, ex_mem_1_aluout, ex_mem_1_irout, id_ex_1_immout, id_ex_1_r1out, id_ex_1_r2out, if_id_1_irout,
       mem_wb_1_aluout, mem_wb_1_memdataout, mips_alu_1_result, mips_regifile_1_r1, mips_regifile_1_r2,
       multiplexer_1_out, multiplexer_2_out, multiplexer_3_out, multiplexer_4_out, multiplexer_5_out,
       multiplexer_9_out, multiplexer_16_out, multiplexer_18_out, multiplexer_20_out, multiplexer_22_out,
       multiplexer_23_out, multiplexer_24_out, multiplexer_26_out, multiplexer_27_out, newPC, ram_1_data,
       rom_1_data;

  Button \u_总复位  (.out(RST));
  Button _1 (.out(IR1));
  Button _2 (.out(IR2));
  Button _3 (.out(IR3));
  Button \u_继续运行  (.out(Go));
  LED #(.active("true")) led_1 (.in(W1));
  LED #(.active("true")) led_2 (.in(W2));
  LED #(.active("true")) led_3 (.in(W3));
  or or_1 (or_1_out, \中断CPU , ERET);
  Multiplexer #(.select(1), .width(32), .disabled("Z"), .enable("false")) multiplexer_1 (
    .in0(multiplexer_2_out), .in1(newPC), .out(multiplexer_1_out), .sel(or_1_out));
  not not_1 (not_1_out, or_9_out);
  D_Flip_Flop #(.trigger("rising"), .Pre_Clr_Positions("LEGACY"), .NegatePresetClear("false"), .enable("true"), .NewFFLayout("false")) d_ff_1 (
    .clk(IR1), .D(1'b1), .Q(d_ff_1_q), .reset(IR1_q[0]));  // open: Qn, preset, en
  or or_2 (W1, IR1_q[0], d_ff_1_q);
  D_Flip_Flop #(.trigger("rising"), .Pre_Clr_Positions("LEGACY"), .NegatePresetClear("false"), .enable("true"), .NewFFLayout("false")) d_ff_2 (
    .clk(IR2), .D(1'b1), .Q(d_ff_2_q), .reset(IR1_q[1]));  // open: Qn, preset, en
  or or_3 (W2, IR1_q[1], d_ff_2_q);
  D_Flip_Flop #(.trigger("rising"), .Pre_Clr_Positions("LEGACY"), .NegatePresetClear("false"), .enable("true"), .NewFFLayout("false")) d_ff_3 (
    .clk(IR3), .D(1'b1), .Q(d_ff_3_q), .reset(IR1_q[2]));  // open: Qn, preset, en
  or or_4 (W3, IR1_q[2], d_ff_3_q);
  Hex_Digit_Display hex_digit_display_1 (.value(LedData[31:28]));  // open: dp
  Multiplexer #(.select(1), .width(32), .disabled("Z"), .enable("false")) multiplexer_2 (
    .in0(adder_1_out), .in1(multiplexer_23_out), .out(multiplexer_2_out), .sel(Branch));
  Register #(.width(32), .trigger("rising"), .Select("low")) PC (
    .D(multiplexer_1_out), .en(not_1_out), .Q(IF_PC), .clk(CLK));  // open: clr
  and and_1 (and_1_out, rd0, MTC0);
  and and_2 (and_2_out, ~rd0, MTC0);  // AND_Gate
  or or_5 (or_5_out, d_ff_1_q, IR1_q[0]);
  or or_6 (or_6_out, d_ff_2_q, IR1_q[1]);
  or or_7 (or_7_out, d_ff_3_q, IR1_q[2]);
  Hex_Digit_Display hex_digit_display_2 (.value(LedData[27:24]));  // open: dp
  Hex_Digit_Display hex_digit_display_3 (.value(LedData[23:20]));  // open: dp
  Adder #(.width(32)) adder_1 (.a(32'h4), .b(IF_PC), .out(adder_1_out), .cin(1'b0));  // open: cout
  Multiplexer #(.select(1), .width(32), .disabled("Z"), .enable("false")) multiplexer_3 (
    .in0(multiplexer_5_out), .in1({multiplexer_19_out_2, multiplexer_19_out}), .out(multiplexer_3_out),
    .sel(and_2_out));
  or or_8 (or_8_out, and_2_out, \中断CPU );
  Hex_Digit_Display hex_digit_display_4 (.value(LedData[15:12]));  // open: dp
  Hex_Digit_Display hex_digit_display_5 (.value(LedData[19:16]));  // open: dp
  Register #(.width(32), .trigger("rising"), .Select("low")) EPC (
    .D(multiplexer_3_out), .en(or_8_out), .Q(EPC_q), .clk(CLK));  // open: clr
  and and_3 (and_3_out, or_5_out, ~demultiplexer_1_out1);  // AND_Gate
  and and_4 (and_4_out, or_6_out, ~demultiplexer_1_out2);  // AND_Gate
  and and_5 (and_5_out, or_7_out, ~demultiplexer_1_out3);  // AND_Gate
  Hex_Digit_Display hex_digit_display_6 (.value(LedData[7:4]));  // open: dp
  Hex_Digit_Display hex_digit_display_7 (.value(LedData[11:8]));  // open: dp
  Clock #(.highDuration(1), .lowDuration(1)) clock_1 (.out(CLK));
  ROM #(.addrWidth(10), .dataWidth(32), .Select("high")) rom_1 (.addr(IF_PC[11:2]), .data(rom_1_data), .sel(1'b1));
  or or_9 (or_9_out, not_6_out, load_use);
  Multiplexer #(.select(3), .width(32), .disabled("Z"), .enable("false")) multiplexer_4 (
    .in0(IF_PC), .in1(IF_PC), .in2(ID_PC), .in3(ID_PC), .in4(EX_PC), .in5(EX_PC), .in6(EX_PC), .in7(EX_PC),
    .out(multiplexer_4_out), .sel({if_id_1_statusout, 1'b1}));
  D_Flip_Flop #(.trigger("rising"), .Pre_Clr_Positions("LEGACY"), .NegatePresetClear("false"), .enable("true"), .NewFFLayout("false")) u_IR1 (
    .clk(CLK), .D(and_3_out), .Q(IR1_q[0]));  // open: Qn, preset, en, reset
  D_Flip_Flop #(.trigger("rising"), .Pre_Clr_Positions("LEGACY"), .NegatePresetClear("false"), .enable("true"), .NewFFLayout("false")) u_IR2 (
    .clk(CLK), .D(and_4_out), .Q(IR1_q[1]));  // open: Qn, preset, en, reset
  D_Flip_Flop #(.trigger("rising"), .Pre_Clr_Positions("LEGACY"), .NegatePresetClear("false"), .enable("true"), .NewFFLayout("false")) u_IR3 (
    .clk(CLK), .D(and_5_out), .Q(IR1_q[2]));  // open: Qn, preset, en, reset
  Register #(.width(3), .trigger("rising"), .Select("low")) \u_中断屏蔽字  (
    .D(multiplexer_19_out[3:1]), .en(and_1_out), .Q(\中断屏蔽字_q ), .clk(CLK));  // open: clr
  Hex_Digit_Display hex_digit_display_8 (.value(LedData[3:0]));  // open: dp
  Multiplexer #(.select(1), .width(32), .disabled("Z"), .enable("false")) multiplexer_5 (
    .in0(multiplexer_4_out), .in1(EPC_q), .out(multiplexer_5_out), .sel(ERET));
  assign and_6_out = IR1_q & ~\中断屏蔽字_q ;  // AND_Gate and_6, 3 bits wide
  or or_10 (or_10_out, Branch, \中断CPU , ERET);
  IF_ID if_id_1 (
    .IR(rom_1_data), .PC(IF_PC), .Status(1'b1),
    .IRout({if_id_1_irout[31:12], \单周期硬布线控制器_1_jr [13], if_id_1_irout[10:0]}), .PCout(ID_PC),
    .StatusOut(if_id_1_statusout[1]), .Clear(or_10_out), .CLK(CLK), .\使能端_低电平有效 (or_9_out));
  not not_2 (not_2_out, priority_encoder_1_en_out);
  Priority_Encoder #(.select(2), .disabled("Z")) priority_encoder_1 (
    .in0(1'b0), .in1(and_6_out[0]), .in2(and_6_out[1]), .in3(and_6_out[2]), .out(priority_encoder_1_out),
    .gs(priority_encoder_1_gs), .en_out(priority_encoder_1_en_out), .en_in(1'b1));
  // Probe on \总周期数 
  // Probe on \无条件分支数 
  // Probe on \条件分支成功数 
  // Probe on \插入气泡数 
  // Probe on \LoadUse次数 
  // Probe on priority_encoder_1_out
  Multiplexer #(.select(1), .width(2), .disabled("Z"), .enable("false")) multiplexer_6 (
    .in0(2'b00), .in1(priority_encoder_1_out), .out(multiplexer_6_out), .sel(priority_encoder_1_gs));
  Demultiplexer #(.select(2), .width(1), .tristate("false"), .disabled("Z"), .enable("false")) demultiplexer_1 (
    .out1(demultiplexer_1_out1), .out2(demultiplexer_1_out2), .out3(demultiplexer_1_out3), .in(ERET),
    .sel(multiplexer_6_out));  // open: out0
  // Probe on IF_PC[11:0]
  assign bit_extender_1_out = {{16{1'b0}}, {if_id_1_irout[15:12], \单周期硬布线控制器_1_jr [13], if_id_1_irout[10:0]}};  // Bit_Extender bit_extender_1
  assign bit_extender_2_out = {{16{if_id_1_irout[15]}}, {if_id_1_irout[15:12], \单周期硬布线控制器_1_jr [13], if_id_1_irout[10:0]}};  // Bit_Extender bit_extender_2
  // Probe on EX_PC[11:0]
  // Probe on ID_PC[11:0]
  \源寄存器使用情况  \u_源寄存器使用情况_1  (
    .OP0(if_id_1_irout[26]), .OP1(if_id_1_irout[27]), .OP2(if_id_1_irout[28]), .OP3(if_id_1_irout[29]),
    .OP4(if_id_1_irout[30]), .OP5(if_id_1_irout[31]), .F0(if_id_1_irout[0]), .F1(if_id_1_irout[1]),
    .F2(if_id_1_irout[2]), .F3(if_id_1_irout[3]), .F4(if_id_1_irout[4]), .F5(if_id_1_irout[5]),
    .R1_Used(\源寄存器使用情况_1_r1_used ), .R2_Used(\源寄存器使用情况_1_r2_used ));
  \单周期硬布线控制器  \u_单周期硬布线控制器_1  (
    .Func(if_id_1_irout[5:0]), .OP(if_id_1_irout[31:26]), .ALU_OP(\单周期硬布线控制器_1_jr [8:5]),
    .MemToReg(\单周期硬布线控制器_1_lhu [3]), .MemWrite(\单周期硬布线控制器_1_memwrite [1]), .ALU_SRC(\单周期硬布线控制器_1_jr [9]),
    .SysCALL(\单周期硬布线控制器_1_jr [11]), .SignedExt(SignedExt), .RegDst(\单周期硬布线控制器_1_regdst ),
    .JR(\单周期硬布线控制器_1_jr [0]), .JMP(\单周期硬布线控制器_1_jr [1]), .Beq(\单周期硬布线控制器_1_jr [3]),
    .JAL(\单周期硬布线控制器_1_lhu [2]), .Bne(\单周期硬布线控制器_1_jr [4]), .ShamtSrc(\单周期硬布线控制器_1_jr [10]),
    .LHU(\单周期硬布线控制器_1_lhu [0]), .BGEZ(\单周期硬布线控制器_1_jr [2]), .ERET(\单周期硬布线控制器_1_eret ),
    .CPsrc(if_id_1_irout[25:21]), .MFC0(\单周期硬布线控制器_1_jr [14]), .MTC0(\单周期硬布线控制器_1_jr [12]),
    .RegWrite(\单周期硬布线控制器_1_lhu [1]));  // open: COP0
  Multiplexer #(.select(1), .width(5), .disabled("Z"), .enable("false")) multiplexer_7 (
    .in0(if_id_1_irout[25:21]), .in1(5'b00010), .out(multiplexer_7_out), .sel(\单周期硬布线控制器_1_jr [11]));
  Multiplexer #(.select(1), .width(5), .disabled(0), .enable("false")) multiplexer_8 (
    .in0(if_id_1_irout[20:16]), .in1(5'b00100), .out(multiplexer_8_out), .sel(\单周期硬布线控制器_1_jr [11]));
  Multiplexer #(.select(1), .width(32), .disabled("Z"), .enable("false")) multiplexer_9 (
    .in0(bit_extender_1_out), .in1(bit_extender_2_out), .out(multiplexer_9_out), .sel(SignedExt));
  Multiplexer #(.select(1), .width(1), .disabled("Z"), .enable("false")) multiplexer_10 (
    .in0(\中断使能_q [0]), .in1(1'b1), .out(multiplexer_10_out), .sel(\中断CPU ));
  Multiplexer #(.select(1), .width(1), .disabled("Z"), .enable("false")) multiplexer_11 (
    .in0(multiplexer_10_out), .in1(1'b0), .out(multiplexer_11_out), .sel(ERET));
  // Probe on M_PC[11:0]
  Multiplexer #(.select(1), .width(1), .disabled("Z"), .enable("false")) multiplexer_12 (
    .in0(\源寄存器使用情况_1_r2_used ), .in1(1'b0), .out(multiplexer_12_out), .sel(\单周期硬布线控制器_1_jr [14]));
  Multiplexer #(.select(1), .width(5), .disabled("Z"), .enable("false")) multiplexer_13 (
    .in0(if_id_1_irout[20:16]), .in1({if_id_1_irout[15:12], \单周期硬布线控制器_1_jr [13]}), .out(multiplexer_13_out),
    .sel(\单周期硬布线控制器_1_regdst ));
  Multiplexer #(.select(1), .width(1), .disabled("Z"), .enable("false")) multiplexer_14 (
    .in0(multiplexer_11_out), .in1(multiplexer_19_out[0]), .out(multiplexer_14_out), .sel(and_1_out));
  Register #(.width(1), .trigger("rising"), .Select("low")) \u_中断使能  (
    .D(multiplexer_14_out), .Q(\中断使能_q [0]), .clk(CLK));  // open: en, clr
  // Probe on WB_PC[11:0]
  \数据相关检测  \u_数据相关检测_1  (
    .R1_num(multiplexer_7_out), .EX_WriteReg_num(id_ex_1_targetout), .MEM_WriteReg_num(ex_mem_1_targetout),
    .R2_num(multiplexer_8_out), .R1_Used(\源寄存器使用情况_1_r1_used ), .R2_Used(multiplexer_12_out),
    .\相关性 (\数据相关检测_1_相关性 ), .EX_RegWrite(id_ex_1_wbout[1]), .MEM_RegWrite(ex_mem_1_wbout[1]));  // open: 数据相关
  Multiplexer #(.select(1), .width(5), .disabled("Z"), .enable("false")) multiplexer_15 (
    .in0(multiplexer_13_out), .in1({5{1'b1}}), .out(multiplexer_15_out), .sel(\单周期硬布线控制器_1_lhu [2]));
  Multiplexer #(.select(1), .width(32), .disabled("Z"), .enable("false")) multiplexer_16 (
    .in0(EPC_q), .in1({{28{1'b0}}, \中断屏蔽字_q , \中断使能_q [0]}), .out(multiplexer_16_out), .sel(id_ex_1_irout[11]));
  and and_7 (\中断CPU , not_2_out, ~\中断使能_q [0]);  // AND_Gate
  and and_8 (and_8_out, load_use, multiplexer_29_out);
  \load_use检测  \load_use检测_1  (.\相关性 (\数据相关检测_1_相关性 ), .OP(EX_OP), .load_use(load_use));
  Multiplexer #(.select(1), .width(32), .disabled("Z"), .enable("false")) multiplexer_17 (
    .in0(multiplexer_5_out), .in1({{28{1'b0}}, priority_encoder_1_out, 2'b00}), .out(newPC), .sel(\中断CPU ));
  MIPS_Regifile mips_regifile_1 (
    .Din(RDin), .Clk(CLK), .R1(mips_regifile_1_r1), .R2(mips_regifile_1_r2), .WE(RegWrite),
    .W_num(mem_wb_1_targetout), .R1_num(multiplexer_7_out), .R2_num(multiplexer_8_out));
  Counter #(.width(16), .max('hffff), .ongoal("wrap"), .trigger("rising"), .behavior("new")) counter_1 (
    .load(1'b0), .D({16{1'b0}}), .count(and_8_out), .Q(\LoadUse次数 ), .clk(CLK), .preset(1'b0), .down(1'b0));  // open: carry, clr
  or or_11 (or_11_out, ERET, load_use, Branch, \中断CPU );
  ID_EX id_ex_1 (
    .WB(\单周期硬布线控制器_1_lhu ), .MEM({\单周期硬布线控制器_1_memwrite [1], \单周期硬布线控制器_1_lhu [3]}), .EX(\单周期硬布线控制器_1_jr ),
    .R1(mips_regifile_1_r1), .R2(mips_regifile_1_r2), .Status(if_id_1_statusout[1]), .WBout(id_ex_1_wbout),
    .MEMout(id_ex_1_memout), .EXout({id_ex_1_exout[14], rd0, MTC0, id_ex_1_exout[11:0]}),
    .R1out(id_ex_1_r1out), .R2out(id_ex_1_r2out), .StatusOut(if_id_1_statusout[2]), .Clear(or_11_out),
    .CLK(CLK), .\使能端_低电平有效 (not_6_out), .Shamt(if_id_1_irout[10:6]), .ShamtOut(id_ex_1_shamtout),
    .Imm(multiplexer_9_out), .ImmOut(id_ex_1_immout), .PC(ID_PC), .PCout(EX_PC),
    .IR({if_id_1_irout[31:12], \单周期硬布线控制器_1_jr [13], if_id_1_irout[10:0]}), .IRout({EX_OP, id_ex_1_irout}),
    .Target(multiplexer_15_out), .TargetOut(id_ex_1_targetout), .Forward(\数据相关检测_1_相关性 ),
    .ForwardOut(id_ex_1_forwardout), .ERET(\单周期硬布线控制器_1_eret ), .ERETout(ERET));
  Multiplexer #(.select(2), .width(32), .disabled("Z"), .enable("false")) multiplexer_18 (
    .in0(id_ex_1_r1out), .in1(RDin), .in2(ex_mem_1_aluout), .in3(ex_mem_1_aluout), .out(multiplexer_18_out),
    .sel(id_ex_1_forwardout[3:2]));
  Multiplexer #(.select(2), .width(32), .disabled("Z"), .enable("false")) multiplexer_19 (
    .in0(id_ex_1_r2out), .in1(RDin), .in2(ex_mem_1_aluout), .in3(ex_mem_1_aluout),
    .out({multiplexer_19_out_2, multiplexer_19_out}), .sel(id_ex_1_forwardout[1:0]));
  Adder #(.width(32)) adder_2 (.a(32'h4), .b(EX_PC), .out(adder_2_out));  // open: cin, cout
  Multiplexer #(.select(1), .width(32), .disabled("Z"), .enable("false")) multiplexer_20 (
    .in0({multiplexer_19_out_2, multiplexer_19_out}), .in1(id_ex_1_immout), .out(multiplexer_20_out),
    .sel(id_ex_1_exout[9]));
  not not_3 (not_3_out, mips_alu_1_equal);
  MIPS_ALU mips_alu_1 (
    .X(multiplexer_18_out), .Y(multiplexer_20_out), .AluOP(id_ex_1_exout[8:5]), .Equal(mips_alu_1_equal),
    .Result(mips_alu_1_result), .shamt(multiplexer_21_out));  // open: Result_2
  Multiplexer #(.select(1), .width(5), .disabled("Z"), .enable("false")) multiplexer_21 (
    .in0(id_ex_1_shamtout), .in1(multiplexer_18_out[4:0]), .out(multiplexer_21_out), .sel(id_ex_1_exout[10]));
  Adder #(.width(32)) adder_3 (
    .a(adder_2_out), .b({id_ex_1_immout[29:0], 2'b00}), .out(adder_3_out));  // open: cin, cout
  Multiplexer #(.select(1), .width(32), .disabled("Z"), .enable("false")) multiplexer_22 (
    .in0(adder_3_out), .in1(multiplexer_18_out), .out(multiplexer_22_out), .sel(id_ex_1_exout[0]));
  not not_4 (not_4_out, multiplexer_18_out[31]);
  Multiplexer #(.select(1), .width(32), .disabled("Z"), .enable("false")) multiplexer_23 (
    .in0(multiplexer_22_out), .in1({EX_PC[31:28], id_ex_1_irout, 2'b00}), .out(multiplexer_23_out),
    .sel(id_ex_1_exout[1]));
  or or_12 (or_12_out, id_ex_1_exout[0], id_ex_1_exout[1]);
  and and_9 (and_9_out, id_ex_1_exout[2], not_4_out);
  or or_13 (or_13_out, and_9_out, and_10_out, and_11_out);
  and and_10 (and_10_out, id_ex_1_exout[3], mips_alu_1_equal);
  and and_11 (and_11_out, id_ex_1_exout[4], not_3_out);
  Comparator #(.width(32), .mode("twosComplement")) comparator_1 (
    .a(32'h22), .b(multiplexer_18_out), .eq(comparator_1_eq));  // open: gt, lt
  Multiplexer #(.select(1), .width(32), .disabled("Z"), .enable("false")) multiplexer_24 (
    .in0(mips_alu_1_result), .in1(multiplexer_16_out), .out(multiplexer_24_out), .sel(id_ex_1_exout[14]));
  or or_14 (Branch, or_12_out, or_13_out);
  and and_12 (and_12_out, id_ex_1_exout[11], ~comparator_1_eq);  // AND_Gate
  and and_13 (and_13_out, id_ex_1_exout[11], comparator_1_eq);
  Counter #(.width(16), .max('hffff), .ongoal("wrap"), .trigger("rising"), .behavior("new")) counter_2 (
    .D({16{1'b0}}), .count(or_12_out), .Q(\无条件分支数 ), .clk(CLK));  // open: load, carry, clr, preset, down
  Register #(.width(32), .trigger("rising"), .Select("low")) register_1 (
    .D({multiplexer_19_out_2, multiplexer_19_out}), .en(and_13_out), .Q(LedData), .clk(CLK));  // open: clr
  EX_MEM ex_mem_1 (
    .WB(id_ex_1_wbout), .MEM(id_ex_1_memout), .ALU(multiplexer_24_out),
    .R2({multiplexer_19_out_2, multiplexer_19_out}), .IR({EX_OP, id_ex_1_irout}), .PC(EX_PC),
    .Status(if_id_1_statusout[2]), .WBout(ex_mem_1_wbout), .MEMout({MemWrite, ex_mem_1_memout[0]}),
    .ALUout(ex_mem_1_aluout), .R2out(MDin), .IRout(ex_mem_1_irout), .PCout(M_PC),
    .StatusOut(ex_mem_1_statusout), .Clear(\中断CPU ), .CLK(CLK), .\使能端_低电平有效 (not_6_out), .Stop(and_12_out),
    .StopOut(ex_mem_1_stopout), .Target(id_ex_1_targetout), .TargetOut(ex_mem_1_targetout));
  Counter #(.width(16), .max('hffff), .ongoal("wrap"), .trigger("rising"), .behavior("new")) counter_3 (
    .D({16{1'b0}}), .count(or_13_out), .Q(\条件分支成功数 ), .clk(CLK));  // open: load, carry, clr, preset, down
  RAM #(.addrWidth(10), .dataWidth(32), .bus("separate"), .Select("high")) ram_1 (
    .addr(ex_mem_1_aluout[11:2]), .din(MDin), .data(ram_1_data), .str(MemWrite), .sel(1'b1), .clk(CLK),
    .ld(ex_mem_1_memout[0]));  // open: clr
  MEM_WB mem_wb_1 (
    .WB(ex_mem_1_wbout), .ALU(ex_mem_1_aluout), .MemData(ram_1_data), .IR(ex_mem_1_irout), .PC(M_PC),
    .Status(ex_mem_1_statusout), .WBout({mem_wb_1_wbout[3:2], RegWrite, mem_wb_1_wbout[0]}),
    .ALUout(mem_wb_1_aluout), .MemDataOut(mem_wb_1_memdataout), .PCout(WB_PC), .CLK(CLK),
    .\使能端_低电平有效 (not_6_out), .Stop(ex_mem_1_stopout), .StopOut(mem_wb_1_stopout),
    .Target(ex_mem_1_targetout), .TargetOut(mem_wb_1_targetout));  // open: IRout, StatusOut, Clear
  Multiplexer #(.select(1), .width(16), .disabled("Z"), .enable("false")) multiplexer_25 (
    .in0(mem_wb_1_memdataout[15:0]), .in1(mem_wb_1_memdataout[31:16]), .out(multiplexer_25_out),
    .sel(mem_wb_1_aluout[1]));
  Adder #(.width(32)) adder_4 (.a(32'h4), .b(WB_PC), .out(adder_4_out));  // open: cin, cout
  Multiplexer #(.select(1), .width(32), .disabled("Z"), .enable("false")) multiplexer_26 (
    .in0(mem_wb_1_memdataout), .in1({{16{1'b0}}, multiplexer_25_out}), .out(multiplexer_26_out),
    .sel(mem_wb_1_wbout[0]));
  Multiplexer #(.select(1), .width(32), .disabled("Z"), .enable("false")) multiplexer_27 (
    .in0(mem_wb_1_aluout), .in1(multiplexer_26_out), .out(multiplexer_27_out), .sel(mem_wb_1_wbout[3]));
  Multiplexer #(.select(1), .width(32), .disabled("Z"), .enable("false")) multiplexer_28 (
    .in0(multiplexer_27_out), .in1(adder_4_out), .out(RDin), .sel(mem_wb_1_wbout[2]));
  not not_5 (not_5_out, mem_wb_1_stopout);
  not not_6 (not_6_out, multiplexer_29_out);
  Multiplexer #(.select(1), .width(1), .disabled("Z"), .enable("false")) multiplexer_29 (
    .in0(not_5_out), .in1(mem_wb_1_stopout), .out(multiplexer_29_out), .sel(Go));
  Counter #(.width(16), .max('hffff), .ongoal("wrap"), .trigger("rising"), .behavior("new")) counter_4 (
    .load(1'b0), .D({16{1'b0}}), .count(multiplexer_29_out), .Q(\总周期数 ), .clk(CLK), .preset(1'b0), .down(1'b0));  // open: carry, clr

  // Other names for the same wires on the sheet: MEM_PC[31:0] = M_PC

  // Notes on the sheet:
  //   中断源
  //   中断等待指示
  //   数码管输出
  //   指令存储器
  //   指令字
  //   contents of rom_1 (hex, n*v repeats v):
  //   20110001 8000c05 20110001 20120002 20130003 8000c09 20110001 20120002 20130003 8000c0d 20110001
  //   20120002 20130003 8000c11 20110001 20120002 20130003 c000cb8 20100001 20110001 118fc0 112020
  //   20020022 c 118882 12200001 8000c15 112020 20020022 c 20110001 118880 112020 20020022 c 12200001
  //   8000c1f 20110001 118fc0 112020 20020022 c 1188c3 112020 20020022 c 118903 112020 20020022 c 118903
  //   112020 20020022 c 118903 112020 20020022 c 118903 112020 20020022 c 118903 112020 20020022 c 118903
  //   112020 20020022 c 118903 112020 20020022 c 20100001 109fc0 139fc3 8021 2012000c 24160003 26100001
  //   3210000f 20080008 20090001 139900 2709825 132020 20020022 c 1094022 1500fff9 22100001 2018000f
  //   2188024 108700 20080008 20090001 139902 2709825 132021 20020022 c 1094022 1500fff9 108702 2c9b022
  //   12c00001 8000c50 4020 1084027 84400 3508ffff 82021 20020022 c 2010ffff 20110000 ae300000 22100001
  //   22310004 ae300000 22100001 22310004 ae300000 22100001 22310004 ae300000 22100001 22310004 ae300000
  //   22100001 22310004 ae300000 22100001 22310004 ae300000 22100001 22310004 ae300000 22100001 22310004
  //   ae300000 22100001 22310004 ae300000 22100001 22310004 ae300000 22100001 22310004 ae300000 22100001
  //   22310004 ae300000 22100001 22310004 ae300000 22100001 22310004 ae300000 22100001 22310004 ae300000
  //   22100001 22310004 22100001 8020 2011003c 8e130000 8e340000 274402a 11000002 ae330000 ae140000
  //   2231fffc 1611fff8 102020 20020022 c 22100004 2011003c 1611fff2 20020032 c 20100000 22100001 102020
  //   20020022 c 22100002 102020 20020022 c 22100003 102020 20020022 c 22100004 102020 20020022 c 22100005
  //   102020 20020022 c 22100006 102020 20020022 c 22100007 102020 20020022 c 22100008 102020 20020022
  //   20020022 c 3e00008
  //   OP
  //   Func
  //   rs
  //   rt
  //   rd
  //   shamt
  //   JMP
  //   JR
  //   LHU
  //   OP
  //   Func
  //   Syscall
  //   BGEZ
  //   Beq
  //   Bne
  //   MemToReg
  //   MemWrite
  //   AluOP
  //   AluSrcB
  //   RegWrite
  //   JAL
  //   RegDst
  //   ShamtSrc
  //   流水调试日志用
  //   为方便自动评测，需要输出流水线各段保存的PC值，注意是PC不是PC+4，另外ID段寄存器写入信息，Mem段内存写入信息也要输出
endmodule

module \中断按键参考电路  (
  input  \同步清零信号 ,
  output \与中断屏蔽位与 
);

  wire \_1号中断_out , and_1_out, clock_1_out, d_ff_1_q, or_1_out, or_2_out;

  Clock #(.highDuration(1), .lowDuration(1)) clock_1 (.out(clock_1_out));
  Button \_1号中断  (.out(\_1号中断_out ));
  LED #(.active("true")) \_1号中断等待指示灯  (.in(or_1_out));
  or or_1 (or_1_out, \与中断屏蔽位与 , d_ff_1_q);
  D_Flip_Flop #(.trigger("rising"), .Pre_Clr_Positions("LEGACY"), .NegatePresetClear("false"), .enable("true"), .NewFFLayout("false")) d_ff_1 (
    .clk(\_1号中断_out ), .D(1'b1), .Q(d_ff_1_q), .reset(\与中断屏蔽位与 ));  // open: Qn, preset, en
  or or_2 (or_2_out, d_ff_1_q, \与中断屏蔽位与 );
  and and_1 (and_1_out, or_2_out, ~\同步清零信号 );  // AND_Gate
  D_Flip_Flop #(.trigger("rising"), .Pre_Clr_Positions("LEGACY"), .NegatePresetClear("false"), .enable("true"), .NewFFLayout("false")) IR1 (
    .clk(clock_1_out), .D(and_1_out), .Q(\与中断屏蔽位与 ));  // open: Qn, preset, en, reset

  // Notes on the sheet:
  //   中断信号采样参考电路
  //   Reset 
endmodule

module IF_ID (
  input  [31:0] IR,
  input  [31:0] PC,
  input  Status,
  input  Clear,
  input  CLK,
  input  \使能端_低电平有效 ,
  output [31:0] IRout,
  output [31:0] PCout,
  output StatusOut
);

  wire multiplexer_3_out, pull_resistor_2_node;
  wire [31:0] multiplexer_1_out, multiplexer_2_out;

  Multiplexer #(.select(1), .width(32), .disabled("Z"), .enable("false")) multiplexer_1 (
    .in0(IR), .in1({32{1'b0}}), .out(multiplexer_1_out), .sel(Clear));
  Multiplexer #(.select(1), .width(32), .disabled("Z"), .enable("false")) multiplexer_2 (
    .in0(PC), .in1({32{1'b0}}), .out(multiplexer_2_out), .sel(Clear));
  Multiplexer #(.select(1), .width(1), .disabled("Z"), .enable("false")) multiplexer_3 (
    .in0(Status), .in1(1'b0), .out(multiplexer_3_out), .sel(Clear));
  Pull_Resistor #(.pull(0)) pull_resistor_1 (.node(Clear));
  Register #(.width(32), .trigger("rising"), .Select("low")) register_1 (
    .D(multiplexer_1_out), .en(pull_resistor_2_node), .Q(IRout), .clk(CLK));  // open: clr
  Register #(.width(32), .trigger("rising"), .Select("low")) register_2 (
    .D(multiplexer_2_out), .en(pull_resistor_2_node), .Q(PCout), .clk(CLK));  // open: clr
  Register #(.width(1), .trigger("rising"), .Select("low")) register_3 (
    .D(multiplexer_3_out), .en(pull_resistor_2_node), .Q(StatusOut), .clk(CLK));  // open: clr
  Pull_Resistor #(.pull(0)) pull_resistor_2 (.node(pull_resistor_2_node));
  not not_1 (pull_resistor_2_node, \使能端_低电平有效 );
endmodule

module ID_EX (
  input  [3:0] WB,
  input  [3:0] Forward,
  input  [4:0] Target,
  input  [1:0] MEM,
  input  ERET,
  input  [14:0] EX,
  input  [31:0] R1,
  input  [31:0] R2,
  input  [4:0] Shamt,
  input  [31:0] Imm,
  input  [31:0] IR,
  input  [31:0] PC,
  input  Status,
  input  Clear,
  input  CLK,
  input  \使能端_低电平有效 ,
  output [3:0] WBout,
  output [3:0] ForwardOut,
  output [4:0] TargetOut,
  output [1:0] MEMout,
  output ERETout,
  output [14:0] EXout,
  output [31:0] R1out,
  output [31:0] R2out,
  output [4:0] ShamtOut,
  output [31:0] ImmOut,
  output [31:0] IRout,
  output [31:0] PCout,
  output StatusOut
);

  wire and_1_out, multiplexer_5_out, multiplexer_13_out, pull_resistor_2_node;
  wire [1:0] multiplexer_4_out;
  wire [3:0] multiplexer_1_out, multiplexer_2_out;
  wire [4:0] multiplexer_3_out, multiplexer_9_out;
  wire [14:0] multiplexer_6_out;
  wire [31:0] multiplexer_7_out, multiplexer_8_out, multiplexer_10_out, multiplexer_11_out,
       multiplexer_12_out;

  Multiplexer #(.select(1), .width(4), .disabled("Z"), .enable("false")) multiplexer_1 (
    .in0(WB), .in1(4'b0000), .out(multiplexer_1_out), .sel(Clear));
  Multiplexer #(.select(1), .width(4), .disabled("Z"), .enable("false")) multiplexer_2 (
    .in0(Forward), .in1(4'b0000), .out(multiplexer_2_out), .sel(Clear));
  Multiplexer #(.select(1), .width(5), .disabled("Z"), .enable("false")) multiplexer_3 (
    .in0(Target), .in1({5{1'b0}}), .out(multiplexer_3_out), .sel(Clear));
  Multiplexer #(.select(1), .width(2), .disabled("Z"), .enable("false")) multiplexer_4 (
    .in0(MEM), .in1(2'b00), .out(multiplexer_4_out), .sel(Clear));
  Multiplexer #(.select(1), .width(1), .disabled("Z"), .enable("false")) multiplexer_5 (
    .in0(ERET), .in1(1'b0), .out(multiplexer_5_out), .sel(Clear));
  Multiplexer #(.select(1), .width(15), .disabled("Z"), .enable("false")) multiplexer_6 (
    .in0(EX), .in1({15{1'b0}}), .out(multiplexer_6_out), .sel(Clear));
  Multiplexer #(.select(1), .width(32), .disabled("Z"), .enable("false")) multiplexer_7 (
    .in0(R1), .in1({32{1'b0}}), .out(multiplexer_7_out), .sel(Clear));
  Multiplexer #(.select(1), .width(32), .disabled("Z"), .enable("false")) multiplexer_8 (
    .in0(R2), .in1({32{1'b0}}), .out(multiplexer_8_out), .sel(Clear));
  Multiplexer #(.select(1), .width(5), .disabled("Z"), .enable("false")) multiplexer_9 (
    .in0(Shamt), .in1({5{1'b0}}), .out(multiplexer_9_out), .sel(Clear));
  Multiplexer #(.select(1), .width(32), .disabled("Z"), .enable("false")) multiplexer_10 (
    .in0(Imm), .in1({32{1'b0}}), .out(multiplexer_10_out), .sel(Clear));
  Multiplexer #(.select(1), .width(32), .disabled("Z"), .enable("false")) multiplexer_11 (
    .in0(IR), .in1({32{1'b0}}), .out(multiplexer_11_out), .sel(Clear));
  Multiplexer #(.select(1), .width(32), .disabled("Z"), .enable("false")) multiplexer_12 (
    .in0(PC), .in1({32{1'b0}}), .out(multiplexer_12_out), .sel(Clear));
  Multiplexer #(.select(1), .width(1), .disabled("Z"), .enable("false")) multiplexer_13 (
    .in0(Status), .in1(1'b0), .out(multiplexer_13_out), .sel(Clear));
  Pull_Resistor #(.pull(0)) pull_resistor_1 (.node(Clear));
  and and_1 (and_1_out, Status, pull_resistor_2_node);
  Register #(.width(4), .trigger("rising"), .Select("low")) register_1 (
    .D(multiplexer_1_out), .en(and_1_out), .Q(WBout), .clk(CLK));  // open: clr
  Register #(.width(4), .trigger("rising"), .Select("low")) register_2 (
    .D(multiplexer_2_out), .en(and_1_out), .Q(ForwardOut), .clk(CLK));  // open: clr
  Register #(.width(5), .trigger("rising"), .Select("low")) register_3 (
    .D(multiplexer_3_out), .en(and_1_out), .Q(TargetOut), .clk(CLK));  // open: clr
  Register #(.width(2), .trigger("rising"), .Select("low")) register_4 (
    .D(multiplexer_4_out), .en(and_1_out), .Q(MEMout), .clk(CLK));  // open: clr
  Register #(.width(1), .trigger("rising"), .Select("low")) register_5 (
    .D(multiplexer_5_out), .en(and_1_out), .Q(ERETout), .clk(CLK));  // open: clr
  Register #(.width(15), .trigger("rising"), .Select("low")) register_6 (
    .D(multiplexer_6_out), .en(and_1_out), .Q(EXout), .clk(CLK));  // open: clr
  Register #(.width(32), .trigger("rising"), .Select("low")) register_7 (
    .D(multiplexer_7_out), .en(and_1_out), .Q(R1out), .clk(CLK));  // open: clr
  Register #(.width(32), .trigger("rising"), .Select("low")) register_8 (
    .D(multiplexer_8_out), .en(and_1_out), .Q(R2out), .clk(CLK));  // open: clr
  Register #(.width(5), .trigger("rising"), .Select("low")) register_9 (
    .D(multiplexer_9_out), .en(and_1_out), .Q(ShamtOut), .clk(CLK));  // open: clr
  Register #(.width(32), .trigger("rising"), .Select("low")) register_10 (
    .D(multiplexer_10_out), .en(and_1_out), .Q(ImmOut), .clk(CLK));  // open: clr
  Register #(.width(32), .trigger("rising"), .Select("low")) register_11 (
    .D(multiplexer_11_out), .en(and_1_out), .Q(IRout), .clk(CLK));  // open: clr
  Register #(.width(32), .trigger("rising"), .Select("low")) register_12 (
    .D(multiplexer_12_out), .en(and_1_out), .Q(PCout), .clk(CLK));  // open: clr
  Register #(.width(1), .trigger("rising"), .Select("low")) register_13 (
    .D(multiplexer_13_out), .en(and_1_out), .Q(StatusOut), .clk(CLK));  // open: clr
  Pull_Resistor #(.pull(0)) pull_resistor_2 (.node(pull_resistor_2_node));
  not not_1 (pull_resistor_2_node, \使能端_低电平有效 );
endmodule

module EX_MEM (
  input  [3:0] WB,
  input  [4:0] Target,
  input  Stop,
  input  [1:0] MEM,
  input  [31:0] ALU,
  input  [31:0] R2,
  input  [31:0] IR,
  input  [31:0] PC,
  input  Status,
  input  Clear,
  input  CLK,
  input  \使能端_低电平有效 ,
  output [3:0] WBout,
  output [4:0] TargetOut,
  output StopOut,
  output [1:0] MEMout,
  output [31:0] ALUout,
  output [31:0] R2out,
  output [31:0] IRout,
  output [31:0] PCout,
  output StatusOut
);

  wire multiplexer_3_out, multiplexer_9_out, not_1_out;
  wire [1:0] multiplexer_4_out;
  wire [3:0] multiplexer_1_out;
  wire [4:0] multiplexer_2_out;
  wire [31:0] multiplexer_5_out, multiplexer_6_out, multiplexer_7_out, multiplexer_8_out;

  Multiplexer #(.select(1), .width(4), .disabled("Z"), .enable("false")) multiplexer_1 (
    .in0(WB), .in1(4'b0000), .out(multiplexer_1_out), .sel(Clear));
  Multiplexer #(.select(1), .width(5), .disabled("Z"), .enable("false")) multiplexer_2 (
    .in0(Target), .in1({5{1'b0}}), .out(multiplexer_2_out), .sel(Clear));
  Multiplexer #(.select(1), .width(1), .disabled("Z"), .enable("false")) multiplexer_3 (
    .in0(Stop), .in1(1'b0), .out(multiplexer_3_out), .sel(Clear));
  Multiplexer #(.select(1), .width(2), .disabled("Z"), .enable("false")) multiplexer_4 (
    .in0(MEM), .in1(2'b00), .out(multiplexer_4_out), .sel(Clear));
  Multiplexer #(.select(1), .width(32), .disabled("Z"), .enable("false")) multiplexer_5 (
    .in0(ALU), .in1({32{1'b0}}), .out(multiplexer_5_out), .sel(Clear));
  Multiplexer #(.select(1), .width(32), .disabled("Z"), .enable("false")) multiplexer_6 (
    .in0(R2), .in1({32{1'b0}}), .out(multiplexer_6_out), .sel(Clear));
  Multiplexer #(.select(1), .width(32), .disabled("Z"), .enable("false")) multiplexer_7 (
    .in0(IR), .in1({32{1'b0}}), .out(multiplexer_7_out), .sel(Clear));
  Multiplexer #(.select(1), .width(32), .disabled("Z"), .enable("false")) multiplexer_8 (
    .in0(PC), .in1({32{1'b0}}), .out(multiplexer_8_out), .sel(Clear));
  Multiplexer #(.select(1), .width(1), .disabled("Z"), .enable("false")) multiplexer_9 (
    .in0(Status), .in1(1'b0), .out(multiplexer_9_out), .sel(Clear));
  Pull_Resistor #(.pull(0)) pull_resistor_1 (.node(Clear));
  not not_1 (not_1_out, \使能端_低电平有效 );
  Register #(.width(4), .trigger("rising"), .Select("low")) register_1 (
    .D(multiplexer_1_out), .en(not_1_out), .Q(WBout), .clk(CLK));  // open: clr
  Register #(.width(5), .trigger("rising"), .Select("low")) register_2 (
    .D(multiplexer_2_out), .en(not_1_out), .Q(TargetOut), .clk(CLK));  // open: clr
  Register #(.width(1), .trigger("rising"), .Select("low")) register_3 (
    .D(multiplexer_3_out), .en(not_1_out), .Q(StopOut), .clk(CLK));  // open: clr
  Register #(.width(2), .trigger("rising"), .Select("low")) register_4 (
    .D(multiplexer_4_out), .en(not_1_out), .Q(MEMout), .clk(CLK));  // open: clr
  Register #(.width(32), .trigger("rising"), .Select("low")) register_5 (
    .D(multiplexer_5_out), .en(not_1_out), .Q(ALUout), .clk(CLK));  // open: clr
  Register #(.width(32), .trigger("rising"), .Select("low")) register_6 (
    .D(multiplexer_6_out), .en(not_1_out), .Q(R2out), .clk(CLK));  // open: clr
  Register #(.width(32), .trigger("rising"), .Select("low")) register_7 (
    .D(multiplexer_7_out), .en(not_1_out), .Q(IRout), .clk(CLK));  // open: clr
  Register #(.width(32), .trigger("rising"), .Select("low")) register_8 (
    .D(multiplexer_8_out), .en(not_1_out), .Q(PCout), .clk(CLK));  // open: clr
  Register #(.width(1), .trigger("rising"), .Select("low")) register_9 (
    .D(multiplexer_9_out), .en(not_1_out), .Q(StatusOut), .clk(CLK));  // open: clr
  Pull_Resistor #(.pull(0)) pull_resistor_2 (.node(not_1_out));
endmodule

module MEM_WB (
  input  [3:0] WB,
  input  [4:0] Target,
  input  Stop,
  input  [31:0] ALU,
  input  [31:0] MemData,
  input  [31:0] IR,
  input  [31:0] PC,
  input  Status,
  input  Clear,
  input  CLK,
  input  \使能端_低电平有效 ,
  output [3:0] WBout,
  output [4:0] TargetOut,
  output StopOut,
  output [31:0] ALUout,
  output [31:0] MemDataOut,
  output [31:0] IRout,
  output [31:0] PCout,
  output StatusOut
);

  wire multiplexer_3_out, multiplexer_8_out, not_1_out;
  wire [3:0] multiplexer_1_out;
  wire [4:0] multiplexer_2_out;
  wire [31:0] multiplexer_4_out, multiplexer_5_out, multiplexer_6_out, multiplexer_7_out;

  Multiplexer #(.select(1), .width(4), .disabled("Z"), .enable("false")) multiplexer_1 (
    .in0(WB), .in1(4'b0000), .out(multiplexer_1_out), .sel(Clear));
  Multiplexer #(.select(1), .width(5), .disabled("Z"), .enable("false")) multiplexer_2 (
    .in0(Target), .in1({5{1'b0}}), .out(multiplexer_2_out), .sel(Clear));
  Multiplexer #(.select(1), .width(1), .disabled("Z"), .enable("false")) multiplexer_3 (
    .in0(Stop), .in1(1'b0), .out(multiplexer_3_out), .sel(Clear));
  Multiplexer #(.select(1), .width(32), .disabled("Z"), .enable("false")) multiplexer_4 (
    .in0(ALU), .in1({32{1'b0}}), .out(multiplexer_4_out), .sel(Clear));
  Multiplexer #(.select(1), .width(32), .disabled("Z"), .enable("false")) multiplexer_5 (
    .in0(MemData), .in1({32{1'b0}}), .out(multiplexer_5_out), .sel(Clear));
  Multiplexer #(.select(1), .width(32), .disabled("Z"), .enable("false")) multiplexer_6 (
    .in0(IR), .in1({32{1'b0}}), .out(multiplexer_6_out), .sel(Clear));
  Multiplexer #(.select(1), .width(32), .disabled("Z"), .enable("false")) multiplexer_7 (
    .in0(PC), .in1({32{1'b0}}), .out(multiplexer_7_out), .sel(Clear));
  Multiplexer #(.select(1), .width(1), .disabled("Z"), .enable("false")) multiplexer_8 (
    .in0(Status), .in1(1'b0), .out(multiplexer_8_out), .sel(Clear));
  Pull_Resistor #(.pull(0)) pull_resistor_1 (.node(Clear));
  not not_1 (not_1_out, \使能端_低电平有效 );
  Register #(.width(4), .trigger("rising"), .Select("low")) register_1 (
    .D(multiplexer_1_out), .en(not_1_out), .Q(WBout), .clk(CLK));  // open: clr
  Register #(.width(5), .trigger("rising"), .Select("low")) register_2 (
    .D(multiplexer_2_out), .en(not_1_out), .Q(TargetOut), .clk(CLK));  // open: clr
  Register #(.width(1), .trigger("rising"), .Select("low")) register_3 (
    .D(multiplexer_3_out), .en(not_1_out), .Q(StopOut), .clk(CLK));  // open: clr
  Register #(.width(32), .trigger("rising"), .Select("low")) register_4 (
    .D(multiplexer_4_out), .en(not_1_out), .Q(ALUout), .clk(CLK));  // open: clr
  Register #(.width(32), .trigger("rising"), .Select("low")) register_5 (
    .D(multiplexer_5_out), .en(not_1_out), .Q(MemDataOut), .clk(CLK));  // open: clr
  Register #(.width(32), .trigger("rising"), .Select("low")) register_6 (
    .D(multiplexer_6_out), .en(not_1_out), .Q(IRout), .clk(CLK));  // open: clr
  Register #(.width(32), .trigger("rising"), .Select("low")) register_7 (
    .D(multiplexer_7_out), .en(not_1_out), .Q(PCout), .clk(CLK));  // open: clr
  Register #(.width(1), .trigger("rising"), .Select("low")) register_8 (
    .D(multiplexer_8_out), .en(not_1_out), .Q(StatusOut), .clk(CLK));  // open: clr
  Pull_Resistor #(.pull(0)) pull_resistor_2 (.node(not_1_out));
endmodule

module \源寄存器使用情况  (
  input  OP0,
  input  OP1,
  input  OP2,
  input  OP3,
  input  OP4,
  input  OP5,
  input  F0,
  input  F1,
  input  F2,
  input  F3,
  input  F4,
  input  F5,
  output R1_Used,
  output R2_Used
);

  wire and_1_out, and_2_out, and_3_out, and_4_out, and_5_out, and_6_out, and_7_out, and_8_out, and_9_out,
       and_10_out, and_11_out, and_12_out, and_13_out, and_14_out, and_15_out, and_16_out, and_17_out,
       and_18_out, and_19_out, and_20_out, and_21_out, and_22_out, and_23_out, and_24_out, and_25_out,
       and_26_out, and_27_out, and_28_out, and_29_out, and_30_out, not_1_out, not_2_out, not_3_out,
       not_4_out, not_5_out, not_6_out, not_7_out, not_8_out, not_9_out, not_10_out, not_11_out, not_12_out,
       not_13_out, not_14_out, not_15_out, not_16_out, not_17_out, not_18_out, not_19_out, not_20_out,
       not_21_out, not_22_out, not_23_out, not_24_out, not_25_out, not_26_out, not_27_out, not_28_out,
       not_29_out, not_30_out, not_31_out, not_32_out, not_33_out, not_34_out, not_35_out, not_36_out,
       not_37_out, not_38_out, not_39_out, not_40_out, not_41_out, not_42_out, not_43_out, not_44_out,
       not_45_out, not_46_out, not_47_out, not_48_out, not_49_out, not_50_out, not_51_out, not_52_out,
       not_53_out, not_54_out, not_55_out, not_56_out, not_57_out, not_58_out, not_59_out, not_60_out,
       not_61_out, not_62_out, not_63_out, not_64_out, not_65_out, not_66_out, not_67_out, not_68_out,
       not_69_out, not_70_out, not_71_out, not_72_out, not_73_out, not_74_out, not_75_out, not_76_out,
       not_77_out, not_78_out, not_79_out, not_80_out, not_81_out, not_82_out, not_83_out, not_84_out,
       not_85_out, not_86_out, not_87_out, not_88_out, not_89_out, not_90_out, not_91_out, not_92_out,
       not_93_out, not_94_out, not_95_out, not_96_out, not_97_out, not_98_out, not_99_out, not_100_out,
       not_101_out, not_102_out, not_103_out, not_104_out, not_105_out, not_106_out, not_107_out,
       not_108_out, not_109_out, not_110_out, not_111_out, not_112_out, not_113_out, not_114_out,
       not_115_out, not_116_out, not_117_out, not_118_out, not_119_out, not_120_out, not_121_out,
       not_122_out, not_123_out, not_124_out, not_125_out, not_126_out, not_127_out, not_128_out,
       not_129_out, not_130_out, not_131_out, not_132_out, not_133_out, not_134_out, not_135_out,
       not_136_out, not_137_out, not_138_out, not_139_out, not_140_out, not_141_out, not_142_out,
       not_143_out, not_144_out, not_145_out, not_146_out, not_147_out, not_148_out, not_149_out,
       not_150_out, not_151_out, not_152_out, not_153_out, not_154_out, not_155_out, not_156_out,
       not_157_out, not_158_out, not_159_out, not_160_out, not_161_out, not_162_out, not_163_out,
       not_164_out, not_165_out, not_166_out, not_167_out, not_168_out, not_169_out, not_170_out,
       not_171_out, not_172_out, not_173_out, not_174_out, not_175_out, not_176_out, not_177_out,
       not_178_out, not_179_out, not_180_out, not_181_out, not_182_out, not_183_out, not_184_out,
       not_185_out, not_186_out, not_187_out, not_188_out, not_189_out, not_190_out, not_191_out,
       not_192_out, not_193_out, not_194_out, not_195_out, not_196_out, not_197_out, not_198_out,
       not_199_out, not_200_out, not_201_out, not_202_out, not_203_out, not_204_out, not_205_out,
       not_206_out, not_207_out, not_208_out, not_209_out, not_210_out, not_211_out, not_212_out,
       not_213_out, not_214_out;

  not not_1 (not_1_out, OP1);
  not not_2 (not_2_out, OP4);
  not not_3 (not_3_out, OP5);
  not not_4 (not_4_out, F0);
  not not_5 (not_5_out, F3);
  not not_6 (not_6_out, F4);
  not not_7 (not_7_out, OP1);
  not not_8 (not_8_out, OP4);
  not not_9 (not_9_out, OP5);
  not not_10 (not_10_out, F1);
  not not_11 (not_11_out, F3);
  not not_12 (not_12_out, F4);
  not not_13 (not_13_out, OP1);
  not not_14 (not_14_out, OP4);
  not not_15 (not_15_out, OP5);
  not not_16 (not_16_out, F0);
  not not_17 (not_17_out, F1);
  not not_18 (not_18_out, F4);
  not not_19 (not_19_out, F5);
  not not_20 (not_20_out, OP1);
  not not_21 (not_21_out, OP4);
  not not_22 (not_22_out, OP5);
  not not_23 (not_23_out, F3);
  not not_24 (not_24_out, F4);
  not not_25 (not_25_out, OP1);
  not not_26 (not_26_out, OP4);
  not not_27 (not_27_out, OP5);
  not not_28 (not_28_out, F2);
  not not_29 (not_29_out, F4);
  not not_30 (not_30_out, OP1);
  not not_31 (not_31_out, OP4);
  not not_32 (not_32_out, OP5);
  not not_33 (not_33_out, F0);
  not not_34 (not_34_out, F3);
  not not_35 (not_35_out, F4);
  not not_36 (not_36_out, OP0);
  not not_37 (not_37_out, OP2);
  not not_38 (not_38_out, OP4);
  not not_39 (not_39_out, OP5);
  not not_40 (not_40_out, OP1);
  not not_41 (not_41_out, OP4);
  not not_42 (not_42_out, OP5);
  not not_43 (not_43_out, OP1);
  not not_44 (not_44_out, OP4);
  not not_45 (not_45_out, OP5);
  not not_46 (not_46_out, OP1);
  not not_47 (not_47_out, OP3);
  not not_48 (not_48_out, OP4);
  not not_49 (not_49_out, OP2);
  not not_50 (not_50_out, OP4);
  not not_51 (not_51_out, OP5);
  not not_52 (not_52_out, OP4);
  not not_53 (not_53_out, OP3);
  not not_54 (not_54_out, OP2);
  not not_55 (not_55_out, OP1);
  not not_56 (not_56_out, OP0);
  not not_57 (not_57_out, F5);
  not not_58 (not_58_out, F4);
  not not_59 (not_59_out, F3);
  not not_60 (not_60_out, F2);
  not not_61 (not_61_out, F1);
  not not_62 (not_62_out, F0);
  not not_63 (not_63_out, OP5);
  not not_64 (not_64_out, OP4);
  not not_65 (not_65_out, OP3);
  not not_66 (not_66_out, OP2);
  not not_67 (not_67_out, OP1);
  not not_68 (not_68_out, OP0);
  not not_69 (not_69_out, F5);
  not not_70 (not_70_out, F4);
  not not_71 (not_71_out, F3);
  not not_72 (not_72_out, F2);
  not not_73 (not_73_out, OP5);
  not not_74 (not_74_out, OP4);
  not not_75 (not_75_out, OP3);
  not not_76 (not_76_out, OP2);
  not not_77 (not_77_out, OP1);
  not not_78 (not_78_out, OP0);
  not not_79 (not_79_out, F5);
  not not_80 (not_80_out, F4);
  not not_81 (not_81_out, F3);
  not not_82 (not_82_out, F2);
  not not_83 (not_83_out, F0);
  not not_84 (not_84_out, OP5);
  not not_85 (not_85_out, OP4);
  not not_86 (not_86_out, OP3);
  not not_87 (not_87_out, OP2);
  not not_88 (not_88_out, OP1);
  not not_89 (not_89_out, OP0);
  not not_90 (not_90_out, F4);
  not not_91 (not_91_out, F3);
  not not_92 (not_92_out, F2);
  not not_93 (not_93_out, F1);
  not not_94 (not_94_out, F0);
  not not_95 (not_95_out, OP5);
  not not_96 (not_96_out, OP4);
  not not_97 (not_97_out, OP3);
  not not_98 (not_98_out, OP2);
  not not_99 (not_99_out, OP1);
  not not_100 (not_100_out, OP0);
  not not_101 (not_101_out, F4);
  not not_102 (not_102_out, F3);
  not not_103 (not_103_out, F2);
  not not_104 (not_104_out, F1);
  not not_105 (not_105_out, OP5);
  not not_106 (not_106_out, OP4);
  not not_107 (not_107_out, OP3);
  not not_108 (not_108_out, OP2);
  not not_109 (not_109_out, OP1);
  not not_110 (not_110_out, OP0);
  not not_111 (not_111_out, F4);
  not not_112 (not_112_out, F3);
  not not_113 (not_113_out, F2);
  not not_114 (not_114_out, F0);
  not not_115 (not_115_out, OP5);
  not not_116 (not_116_out, OP4);
  not not_117 (not_117_out, OP3);
  not not_118 (not_118_out, OP2);
  not not_119 (not_119_out, OP1);
  not not_120 (not_120_out, OP0);
  not not_121 (not_121_out, F4);
  not not_122 (not_122_out, F3);
  not not_123 (not_123_out, F1);
  not not_124 (not_124_out, F0);
  not not_125 (not_125_out, OP5);
  not not_126 (not_126_out, OP4);
  not not_127 (not_127_out, OP3);
  not not_128 (not_128_out, OP2);
  not not_129 (not_129_out, OP1);
  not not_130 (not_130_out, OP0);
  not not_131 (not_131_out, F4);
  not not_132 (not_132_out, F3);
  not not_133 (not_133_out, F1);
  not not_134 (not_134_out, OP5);
  not not_135 (not_135_out, OP4);
  not not_136 (not_136_out, OP3);
  not not_137 (not_137_out, OP2);
  not not_138 (not_138_out, OP1);
  not not_139 (not_139_out, OP0);
  not not_140 (not_140_out, F4);
  not not_141 (not_141_out, F3);
  not not_142 (not_142_out, OP5);
  not not_143 (not_143_out, OP4);
  not not_144 (not_144_out, OP3);
  not not_145 (not_145_out, OP2);
  not not_146 (not_146_out, OP1);
  not not_147 (not_147_out, OP0);
  not not_148 (not_148_out, F4);
  not not_149 (not_149_out, F2);
  not not_150 (not_150_out, F0);
  not not_151 (not_151_out, OP5);
  not not_152 (not_152_out, OP4);
  not not_153 (not_153_out, OP3);
  not not_154 (not_154_out, OP2);
  not not_155 (not_155_out, OP1);
  not not_156 (not_156_out, OP0);
  not not_157 (not_157_out, F4);
  not not_158 (not_158_out, F2);
  not not_159 (not_159_out, OP5);
  not not_160 (not_160_out, OP4);
  not not_161 (not_161_out, OP3);
  not not_162 (not_162_out, OP2);
  not not_163 (not_163_out, OP1);
  not not_164 (not_164_out, OP0);
  not not_165 (not_165_out, F5);
  not not_166 (not_166_out, F4);
  not not_167 (not_167_out, F1);
  not not_168 (not_168_out, F0);
  not not_169 (not_169_out, OP5);
  not not_170 (not_170_out, OP4);
  not not_171 (not_171_out, OP3);
  not not_172 (not_172_out, OP1);
  not not_173 (not_173_out, OP0);
  not not_174 (not_174_out, OP5);
  not not_175 (not_175_out, OP4);
  not not_176 (not_176_out, OP3);
  not not_177 (not_177_out, OP1);
  not not_178 (not_178_out, OP4);
  not not_179 (not_179_out, OP2);
  not not_180 (not_180_out, OP5);
  not not_181 (not_181_out, OP4);
  not not_182 (not_182_out, OP3);
  not not_183 (not_183_out, OP2);
  not not_184 (not_184_out, OP1);
  not not_185 (not_185_out, OP0);
  not not_186 (not_186_out, F5);
  not not_187 (not_187_out, F4);
  not not_188 (not_188_out, F3);
  not not_189 (not_189_out, F0);
  not not_190 (not_190_out, OP5);
  not not_191 (not_191_out, OP4);
  not not_192 (not_192_out, OP3);
  not not_193 (not_193_out, OP2);
  not not_194 (not_194_out, OP1);
  not not_195 (not_195_out, OP0);
  not not_196 (not_196_out, F4);
  not not_197 (not_197_out, F3);
  not not_198 (not_198_out, F0);
  not not_199 (not_199_out, OP5);
  not not_200 (not_200_out, OP4);
  not not_201 (not_201_out, OP3);
  not not_202 (not_202_out, OP2);
  not not_203 (not_203_out, OP1);
  not not_204 (not_204_out, OP5);
  not not_205 (not_205_out, OP3);
  not not_206 (not_206_out, OP2);
  not not_207 (not_207_out, OP1);
  not not_208 (not_208_out, OP0);
  not not_209 (not_209_out, F5);
  not not_210 (not_210_out, F4);
  not not_211 (not_211_out, F3);
  not not_212 (not_212_out, F2);
  not not_213 (not_213_out, F1);
  not not_214 (not_214_out, F0);
  and and_1 (and_1_out, not_1_out, not_2_out, not_3_out, not_4_out, not_5_out, not_6_out, F5);
  and and_2 (and_2_out, not_7_out, not_8_out, not_9_out, not_10_out, not_11_out, not_12_out, F5);
  and and_3 (and_3_out, not_13_out, not_14_out, not_15_out, not_16_out, not_17_out, F3, not_18_out, not_19_out);
  and and_4 (and_4_out, not_20_out, not_21_out, not_22_out, F2, not_23_out, not_24_out, F5);
  and and_5 (and_5_out, not_25_out, not_26_out, not_27_out, F1, not_28_out, F3, not_29_out, F5);
  and and_6 (and_6_out, not_30_out, not_31_out, not_32_out, not_33_out, F1, F2, not_34_out, not_35_out);
  and and_7 (and_7_out, not_36_out, not_37_out, OP3, not_38_out, not_39_out);
  and and_8 (and_8_out, not_40_out, OP2, not_41_out, not_42_out);
  and and_9 (and_9_out, OP0, not_43_out, not_44_out, not_45_out);
  and and_10 (and_10_out, OP0, not_46_out, OP2, not_47_out, not_48_out);
  and and_11 (and_11_out, OP0, OP1, not_49_out, not_50_out, OP5);
  and and_12 (and_12_out, not_51_out, not_52_out, not_53_out, not_54_out, not_55_out, not_56_out, not_57_out, not_58_out, not_59_out, not_60_out, not_61_out, not_62_out);
  and and_13 (and_13_out, not_63_out, not_64_out, not_65_out, not_66_out, not_67_out, not_68_out, not_69_out, not_70_out, not_71_out, not_72_out, F1, F0);
  and and_14 (and_14_out, not_73_out, not_74_out, not_75_out, not_76_out, not_77_out, not_78_out, not_79_out, not_80_out, not_81_out, not_82_out, F1, not_83_out);
  and and_15 (and_15_out, not_84_out, not_85_out, not_86_out, not_87_out, not_88_out, not_89_out, F5, not_90_out, not_91_out, not_92_out, not_93_out, not_94_out);
  and and_16 (and_16_out, not_95_out, not_96_out, not_97_out, not_98_out, not_99_out, not_100_out, F5, not_101_out, not_102_out, not_103_out, not_104_out, F0);
  and and_17 (and_17_out, not_105_out, not_106_out, not_107_out, not_108_out, not_109_out, not_110_out, F5, not_111_out, not_112_out, not_113_out, F1, not_114_out);
  and and_18 (and_18_out, not_115_out, not_116_out, not_117_out, not_118_out, not_119_out, not_120_out, F5, not_121_out, not_122_out, F2, not_123_out, not_124_out);
  and and_19 (and_19_out, not_125_out, not_126_out, not_127_out, not_128_out, not_129_out, not_130_out, F5, not_131_out, not_132_out, F2, not_133_out, F0);
  and and_20 (and_20_out, not_134_out, not_135_out, not_136_out, not_137_out, not_138_out, not_139_out, F5, not_140_out, not_141_out, F2, F1, F0);
  and and_21 (and_21_out, not_142_out, not_143_out, not_144_out, not_145_out, not_146_out, not_147_out, F5, not_148_out, F3, not_149_out, F1, not_150_out);
  and and_22 (and_22_out, not_151_out, not_152_out, not_153_out, not_154_out, not_155_out, not_156_out, F5, not_157_out, F3, not_158_out, F1, F0);
  and and_23 (and_23_out, not_159_out, not_160_out, not_161_out, not_162_out, not_163_out, not_164_out, not_165_out, not_166_out, F3, F2, not_167_out, not_168_out);
  and and_24 (and_24_out, not_169_out, not_170_out, not_171_out, OP2, not_172_out, not_173_out);
  and and_25 (and_25_out, not_174_out, not_175_out, not_176_out, OP2, not_177_out, OP0);
  and and_26 (and_26_out, OP5, not_178_out, OP3, not_179_out, OP1, OP0);
  and and_27 (and_27_out, not_180_out, not_181_out, not_182_out, not_183_out, not_184_out, not_185_out, not_186_out, not_187_out, not_188_out, F2, F1, not_189_out);
  and and_28 (and_28_out, not_190_out, not_191_out, not_192_out, not_193_out, not_194_out, not_195_out, F5, not_196_out, not_197_out, F2, F1, not_198_out);
  and and_29 (and_29_out, not_199_out, not_200_out, not_201_out, not_202_out, not_203_out, OP0);
  and and_30 (and_30_out, not_204_out, OP4, not_205_out, not_206_out, not_207_out, not_208_out, not_209_out, not_210_out, not_211_out, not_212_out, not_213_out, not_214_out);
  or or_1 (R1_Used, and_1_out, and_2_out, and_3_out, and_4_out, and_5_out, and_6_out, and_7_out, and_8_out, and_9_out, and_10_out, and_11_out);
  or or_2 (R2_Used, and_12_out, and_13_out, and_14_out, and_15_out, and_16_out, and_17_out, and_18_out, and_19_out, and_20_out, and_21_out, and_22_out, and_23_out, and_24_out, and_25_out, and_26_out, and_27_out, and_28_out, and_29_out, and_30_out);
endmodule

module \数据相关检测  (
  input  MEM_RegWrite,
  input  EX_RegWrite,
  input  R1_Used,
  input  [4:0] R1_num,
  input  [4:0] EX_WriteReg_num,
  input  [4:0] MEM_WriteReg_num,
  input  R2_Used,
  input  [4:0] R2_num,
  output [3:0] \相关性 ,
  output \数据相关 
);

  wire and_1_out, and_2_out, comparator_1_eq, comparator_2_eq, comparator_3_eq, comparator_4_eq,
       comparator_5_eq, comparator_6_eq;

  Comparator #(.width(5), .mode("twosComplement")) comparator_1 (
    .a(R1_num), .b({5{1'b0}}), .eq(comparator_1_eq));  // open: gt, lt
  Comparator #(.width(5), .mode("twosComplement")) comparator_2 (
    .a(R1_num), .b(EX_WriteReg_num), .eq(comparator_2_eq));  // open: gt, lt
  Comparator #(.width(5), .mode("twosComplement")) comparator_3 (
    .a(R1_num), .b(MEM_WriteReg_num), .eq(comparator_3_eq));  // open: gt, lt
  Comparator #(.width(5), .mode("twosComplement")) comparator_4 (
    .a(R2_num), .b({5{1'b0}}), .eq(comparator_4_eq));  // open: gt, lt
  Comparator #(.width(5), .mode("twosComplement")) comparator_5 (
    .a(R2_num), .b(EX_WriteReg_num), .eq(comparator_5_eq));  // open: gt, lt
  Comparator #(.width(5), .mode("twosComplement")) comparator_6 (
    .a(R2_num), .b(MEM_WriteReg_num), .eq(comparator_6_eq));  // open: gt, lt
  and and_1 (and_1_out, R1_Used, ~comparator_1_eq);  // AND_Gate
  and and_2 (and_2_out, R2_Used, ~comparator_4_eq);  // AND_Gate
  and and_3 (\相关性 [3], and_1_out, EX_RegWrite, comparator_2_eq);
  and and_4 (\相关性 [2], and_1_out, MEM_RegWrite, comparator_3_eq);
  and and_5 (\相关性 [1], and_2_out, EX_RegWrite, comparator_5_eq);
  and and_6 (\相关性 [0], and_2_out, MEM_RegWrite, comparator_6_eq);
  or or_1 (\数据相关 , \相关性 [3], \相关性 [2], \相关性 [1], \相关性 [0]);
endmodule

module \load_use检测  (
  input  [3:0] \相关性 ,
  input  [5:0] OP,
  output load_use
);

  wire comparator_1_eq, comparator_2_eq, or_1_out, or_2_out;

  Comparator #(.width(6), .mode("twosComplement")) comparator_1 (
    .a(OP), .b(6'b100011), .eq(comparator_1_eq));  // open: gt, lt
  Comparator #(.width(6), .mode("twosComplement")) comparator_2 (
    .a(OP), .b(6'b100101), .eq(comparator_2_eq));  // open: gt, lt
  or or_1 (or_1_out, \相关性 [1], \相关性 [3]);
  or or_2 (or_2_out, comparator_1_eq, comparator_2_eq);
  and and_1 (load_use, or_1_out, or_2_out);
endmodule

module \硬件堆栈  (
  input  [31:0] data,
  input  enable,
  input  eret,
  input  clk,
  output [31:0] dataOut
);

  wire and_1_out, and_2_out, and_3_out, decoder_1_out0, decoder_1_out1, decoder_1_out2, or_1_out;
  wire [1:0] counter_1_q;
  wire [31:0] register_1_q, register_2_q, register_3_q;

  or or_1 (or_1_out, enable, eret);
  Counter #(.width(2), .max('h3), .ongoal("wrap"), .trigger("rising"), .behavior("new")) counter_1 (
    .count(or_1_out), .Q(counter_1_q), .clk(clk), .down(eret));  // open: load, D, carry, clr, preset
  and and_1 (and_1_out, enable, decoder_1_out0);
  Decoder #(.select(2), .tristate("false"), .disabled("Z"), .enable("false")) decoder_1 (
    .out0(decoder_1_out0), .out1(decoder_1_out1), .out2(decoder_1_out2), .sel(counter_1_q));  // open: out3
  Register #(.width(32), .trigger("rising"), .Select("low")) register_1 (
    .D(data), .en(and_1_out), .Q(register_1_q), .clk(clk));  // open: clr
  and and_2 (and_2_out, enable, decoder_1_out1);
  Register #(.width(32), .trigger("rising"), .Select("low")) register_2 (
    .D(data), .en(and_2_out), .Q(register_2_q), .clk(clk));  // open: clr
  Register #(.width(32), .trigger("rising"), .Select("low")) register_3 (
    .D(data), .en(and_3_out), .Q(register_3_q), .clk(clk));  // open: clr
  and and_3 (and_3_out, enable, decoder_1_out2);
  Multiplexer #(.select(2), .width(32), .disabled("Z"), .enable("false")) multiplexer_1 (
    .in1(register_1_q), .in2(register_2_q), .in3(register_3_q), .out(dataOut), .sel(counter_1_q));  // open: in0
endmodule

module \_2位硬件堆栈  (
  input  [1:0] data,
  input  enable,
  input  pop,
  input  clk,
  output [1:0] dataOut
);

  wire and_1_out, and_2_out, and_3_out, decoder_1_out0, decoder_1_out1, decoder_1_out2, or_1_out;
  wire [1:0] counter_1_q, register_1_q, register_2_q, register_3_q;

  or or_1 (or_1_out, enable, pop);
  Counter #(.width(2), .max('h3), .ongoal("wrap"), .trigger("rising"), .behavior("new")) counter_1 (
    .count(or_1_out), .Q(counter_1_q), .clk(clk), .down(pop));  // open: load, D, carry, clr, preset
  and and_1 (and_1_out, enable, decoder_1_out0);
  Decoder #(.select(2), .tristate("false"), .disabled("Z"), .enable("false")) decoder_1 (
    .out0(decoder_1_out0), .out1(decoder_1_out1), .out2(decoder_1_out2), .sel(counter_1_q));  // open: out3
  Register #(.width(2), .trigger("rising"), .Select("low")) register_1 (
    .D(data), .en(and_1_out), .Q(register_1_q), .clk(clk));  // open: clr
  and and_2 (and_2_out, enable, decoder_1_out1);
  Register #(.width(2), .trigger("rising"), .Select("low")) register_2 (
    .D(data), .en(and_2_out), .Q(register_2_q), .clk(clk));  // open: clr
  Register #(.width(2), .trigger("rising"), .Select("low")) register_3 (
    .D(data), .en(and_3_out), .Q(register_3_q), .clk(clk));  // open: clr
  and and_3 (and_3_out, enable, decoder_1_out2);
  Multiplexer #(.select(2), .width(2), .disabled("Z"), .enable("false")) multiplexer_1 (
    .in0(2'b00), .in1(register_1_q), .in2(register_2_q), .in3(register_3_q), .out(dataOut), .sel(counter_1_q));
endmodule
