// Logisim project 加法器.circ as structural Verilog: 5 circuits, main circuit test
module \一位二进制半加器  (
  input  A,
  input  B,
  output S,
  output C
);

  xor xor_1 (S, A, B);
  and and_1 (C, A, B);
endmodule

module test (
  input  in_1,
  input  in_2,
  input  in_3,
  input  in_4,
  input  in_5,
  input  in_6,
  input  in_7,
  input  in_8,
  input  in_9,
  output out_10,
  output out_11,
  output out_12,
  output out_13,
  output out_14
);

  \先行进位的四位二进制并行加法器  \u_先行进位的四位二进制并行加法器_1  (
    .C0(in_1), .A0(in_5), .B0(in_9), .A1(in_4), .B1(in_8), .A2(in_3), .B2(in_7), .A3(in_2), .B3(in_6),
    .S0(out_13), .S1(out_12), .S2(out_11), .S3(out_10), .C4(out_14));
endmodule

module \一位二进制全加器  (
  input  A,
  input  B,
  input  C,
  output S,
  output C_2
);

  wire and_1_out, and_2_out, xor_1_out;

  xor xor_1 (xor_1_out, A, B);
  xor xor_2 (S, xor_1_out, C);
  and and_1 (and_1_out, xor_1_out, C);
  and and_2 (and_2_out, A, B);
  or or_1 (C_2, and_1_out, and_2_out);
endmodule

module \串行进位的四位二进制并行加法器  (
  input  A0,
  input  B0,
  input  C0,
  input  A1,
  input  B1,
  input  A2,
  input  B2,
  input  A3,
  input  B3,
  output S0,
  output S1,
  output S2,
  output S3,
  output C4
);

  wire \一位二进制全加器_1_c_2 , \一位二进制全加器_2_c_2 , \一位二进制全加器_3_c_2 ;

  \一位二进制全加器  \u_一位二进制全加器_1  (.A(A0), .B(B0), .C(C0), .S(S0), .C_2(\一位二进制全加器_1_c_2 ));
  \一位二进制全加器  \u_一位二进制全加器_2  (.A(A1), .B(B1), .C(\一位二进制全加器_1_c_2 ), .S(S1), .C_2(\一位二进制全加器_2_c_2 ));
  \一位二进制全加器  \u_一位二进制全加器_3  (.A(A2), .B(B2), .C(\一位二进制全加器_2_c_2 ), .S(S2), .C_2(\一位二进制全加器_3_c_2 ));
  \一位二进制全加器  \u_一位二进制全加器_4  (.A(A3), .B(B3), .C(\一位二进制全加器_3_c_2 ), .S(S3), .C_2(C4));
endmodule

module \先行进位的四位二进制并行加法器  (
  input  C0,
  input  A0,
  input  B0,
  input  A1,
  input  B1,
  input  A2,
  input  B2,
  input  A3,
  input  B3,
  output S0,
  output S1,
  output S2,
  output S3,
  output C4
);

  wire and_1_out, and_2_out, and_3_out, and_4_out, and_5_out, and_6_out, and_7_out, and_8_out, and_9_out,
       and_10_out, or_1_out, or_2_out, or_3_out, \一位二进制半加器_1_c , \一位二进制半加器_1_s , \一位二进制半加器_2_c ,
       \一位二进制半加器_2_s , \一位二进制半加器_3_c , \一位二进制半加器_3_s , \一位二进制半加器_4_c , \一位二进制半加器_4_s ;

  \一位二进制半加器  \u_一位二进制半加器_1  (.A(A0), .B(B0), .S(\一位二进制半加器_1_s ), .C(\一位二进制半加器_1_c ));
  \一位二进制半加器  \u_一位二进制半加器_2  (.A(A1), .B(B1), .S(\一位二进制半加器_2_s ), .C(\一位二进制半加器_2_c ));
  \一位二进制半加器  \u_一位二进制半加器_3  (.A(A2), .B(B2), .S(\一位二进制半加器_3_s ), .C(\一位二进制半加器_3_c ));
  \一位二进制半加器  \u_一位二进制半加器_4  (.A(A3), .B(B3), .S(\一位二进制半加器_4_s ), .C(\一位二进制半加器_4_c ));
  and and_1 (and_1_out, \一位二进制半加器_1_s , C0);
  and and_2 (and_2_out, C0, \一位二进制半加器_1_s , \一位二进制半加器_2_s );
  and and_3 (and_3_out, \一位二进制半加器_2_s , \一位二进制半加器_1_c );
  and and_4 (and_4_out, C0, \一位二进制半加器_1_s , \一位二进制半加器_2_s , \一位二进制半加器_3_s );
  and and_5 (and_5_out, \一位二进制半加器_2_s , \一位二进制半加器_3_s , \一位二进制半加器_1_c );
  and and_6 (and_6_out, \一位二进制半加器_3_s , \一位二进制半加器_2_c );
  and and_7 (and_7_out, C0, \一位二进制半加器_1_s , \一位二进制半加器_2_s , \一位二进制半加器_3_s , \一位二进制半加器_4_s );
  and and_8 (and_8_out, \一位二进制半加器_1_c , \一位二进制半加器_2_s , \一位二进制半加器_3_s , \一位二进制半加器_4_s );
  and and_9 (and_9_out, \一位二进制半加器_3_s , \一位二进制半加器_4_s , \一位二进制半加器_2_c );
  and and_10 (and_10_out, \一位二进制半加器_4_s , \一位二进制半加器_3_c );
  or or_1 (or_1_out, and_1_out, \一位二进制半加器_1_c );
  or or_2 (or_2_out, and_2_out, and_3_out, \一位二进制半加器_2_c );
  or or_3 (or_3_out, and_4_out, and_5_out, and_6_out, \一位二进制半加器_3_c );
  or or_4 (C4, and_7_out, and_8_out, and_9_out, and_10_out, \一位二进制半加器_4_c );
  xor xor_1 (S0, C0, \一位二进制半加器_1_s );
  xor xor_2 (S1, or_1_out, \一位二进制半加器_2_s );
  xor xor_3 (S2, or_2_out, \一位二进制半加器_3_s );
  xor xor_4 (S3, or_3_out, \一位二进制半加器_4_s );
endmodule
