// Logisim project 乘法器.circ as structural Verilog: 6 circuits, main circuit 32*32Mul
module _32_32Mul (
  input  [31:0] in_1,
  input  [31:0] in_2,
  output [31:0] out_3
);

  wire adder_1_cout, adder_2_cout, adder_3_cout, adder_4_cout, adder_5_cout, adder_6_cout;
  wire [31:0] adder_1_out, adder_2_out, adder_3_out, adder_4_out, adder_5_out, adder_6_out, n32_4mul_1_out_3,
       n32_4mul_2_out_3, n32_4mul_3_out_3, n32_4mul_4_out_3, n32_4mul_5_out_3, n32_4mul_6_out_3,
       n32_4mul_7_out_3, n32_4mul_8_out_3, shifter_1_out, shifter_2_out, shifter_3_out, shifter_4_out,
       shifter_5_out, shifter_6_out, shifter_7_out;

  _32_4Mul u_32_4mul_1 (.in_1(in_2[3:0]), .out_3(n32_4mul_1_out_3), .in_2(in_1));
  _32_4Mul u_32_4mul_2 (.in_1(in_2[11:8]), .out_3(n32_4mul_2_out_3), .in_2(in_1));
  _32_4Mul u_32_4mul_3 (.in_1(in_2[19:16]), .out_3(n32_4mul_3_out_3), .in_2(in_1));
  _32_4Mul u_32_4mul_4 (.in_1(in_2[27:24]), .out_3(n32_4mul_4_out_3), .in_2(in_1));
  _32_4Mul u_32_4mul_5 (.in_1(in_2[7:4]), .out_3(n32_4mul_5_out_3), .in_2(in_1));
  _32_4Mul u_32_4mul_6 (.in_1(in_2[15:12]), .out_3(n32_4mul_6_out_3), .in_2(in_1));
  _32_4Mul u_32_4mul_7 (.in_1(in_2[23:20]), .out_3(n32_4mul_7_out_3), .in_2(in_1));
  _32_4Mul u_32_4mul_8 (.in_1(in_2[31:28]), .out_3(n32_4mul_8_out_3), .in_2(in_1));
  Shifter #(.width(32)) shifter_1 (.in(n32_4mul_5_out_3), .\dist (5'b00100), .out(shifter_1_out));
  Shifter #(.width(32)) shifter_2 (.in(n32_4mul_6_out_3), .\dist (5'b01100), .out(shifter_2_out));
  Shifter #(.width(32)) shifter_3 (.in(n32_4mul_7_out_3), .\dist (5'b10100), .out(shifter_3_out));
  Shifter #(.width(32)) shifter_4 (.in(n32_4mul_8_out_3), .\dist (5'b11100), .out(shifter_4_out));
  Shifter #(.width(32)) shifter_5 (.in(n32_4mul_2_out_3), .\dist (5'b01000), .out(shifter_5_out));
  Shifter #(.width(32)) shifter_6 (.in(n32_4mul_3_out_3), .\dist (5'b10000), .out(shifter_6_out));
  Shifter #(.width(32)) shifter_7 (.in(n32_4mul_4_out_3), .\dist (5'b11000), .out(shifter_7_out));
  Adder #(.width(32)) adder_1 (
    .a(n32_4mul_1_out_3), .b(shifter_1_out), .out(adder_1_out), .cout(adder_1_cout));  // open: cin
  Adder #(.width(32)) adder_2 (
    .a(shifter_5_out), .b(shifter_2_out), .out(adder_2_out), .cin(adder_1_cout), .cout(adder_2_cout));
  Adder #(.width(32)) adder_3 (
    .a(shifter_6_out), .b(shifter_3_out), .out(adder_3_out), .cin(adder_2_cout), .cout(adder_3_cout));
  Adder #(.width(32)) adder_4 (
    .a(shifter_7_out), .b(shifter_4_out), .out(adder_4_out), .cin(adder_3_cout), .cout(adder_4_cout));
  Adder #(.width(32)) adder_5 (
    .a(adder_1_out), .b(adder_2_out), .out(adder_5_out), .cin(adder_4_cout), .cout(adder_5_cout));
  Adder #(.width(32)) adder_6 (
    .a(adder_3_out), .b(adder_4_out), .out(adder_6_out), .cin(adder_5_cout), .cout(adder_6_cout));
  Adder #(.width(32)) adder_7 (.a(adder_5_out), .b(adder_6_out), .out(out_3), .cin(adder_6_cout));  // open: cout
endmodule

module _4_4Mul (
  input  [3:0] in_1,
  input  [3:0] in_2,
  output [7:0] out_3
);

  wire [7:0] adder_1_out, adder_2_out, adder_3_out, adder_4_out, multiplexer_1_out, multiplexer_2_out,
       multiplexer_3_out, shifter_1_out, shifter_2_out, shifter_3_out;

  Adder adder_1 (.a({8{1'b0}}), .b({4'b0000, in_2}), .out(adder_1_out), .cin(1'b0));  // open: cout
  Multiplexer #(.width(8), .disabled(0), .enable("false")) multiplexer_1 (
    .in0({8{1'b0}}), .in1(adder_1_out), .out(multiplexer_1_out), .sel(in_1[0]));
  Shifter shifter_1 (.in({4'b0000, in_2}), .\dist (3'b001), .out(shifter_1_out));
  Adder adder_2 (.a(multiplexer_1_out), .b(shifter_1_out), .out(adder_2_out), .cin(1'b0));  // open: cout
  Multiplexer #(.width(8), .disabled(0), .enable("false")) multiplexer_2 (
    .in0(multiplexer_1_out), .in1(adder_2_out), .out(multiplexer_2_out), .sel(in_1[1]));
  Shifter shifter_2 (.in(shifter_1_out), .\dist (3'b001), .out(shifter_2_out));
  Adder adder_3 (.a(multiplexer_2_out), .b(shifter_2_out), .out(adder_3_out), .cin(1'b0));  // open: cout
  Multiplexer #(.width(8), .disabled(0), .enable("false")) multiplexer_3 (
    .in0(multiplexer_2_out), .in1(adder_3_out), .out(multiplexer_3_out), .sel(in_1[2]));
  Shifter shifter_3 (.in(shifter_2_out), .\dist (3'b001), .out(shifter_3_out));
  Adder adder_4 (.a(multiplexer_3_out), .b(shifter_3_out), .out(adder_4_out), .cin(1'b0));  // open: cout
  Multiplexer #(.width(8), .disabled(0), .enable("false")) multiplexer_4 (
    .in0(multiplexer_3_out), .in1(adder_4_out), .out(out_3), .sel(in_1[3]));
endmodule

module _32_4Mul (
  input  [3:0] in_1,
  input  [31:0] in_2,
  output [31:0] out_3
);

  wire [31:0] adder_1_out, adder_2_out, adder_3_out, adder_4_out, multiplexer_1_out, multiplexer_2_out,
       multiplexer_3_out, shifter_1_out, shifter_2_out, shifter_3_out;

  Adder #(.width(32)) adder_1 (.a({32{1'b0}}), .b(in_2), .out(adder_1_out), .cin(1'b0));  // open: cout
  Multiplexer #(.width(32), .disabled(0), .enable("false")) multiplexer_1 (
    .in0({32{1'b0}}), .in1(adder_1_out), .out(multiplexer_1_out), .sel(in_1[0]));
  Shifter #(.width(32)) shifter_1 (.in(in_2), .\dist (5'b00001), .out(shifter_1_out));
  Adder #(.width(32)) adder_2 (.a(multiplexer_1_out), .b(shifter_1_out), .out(adder_2_out), .cin(1'b0));  // open: cout
  Multiplexer #(.width(32), .disabled(0), .enable("false")) multiplexer_2 (
    .in0(multiplexer_1_out), .in1(adder_2_out), .out(multiplexer_2_out), .sel(in_1[1]));
  Shifter #(.width(32)) shifter_2 (.in(shifter_1_out), .\dist (5'b00001), .out(shifter_2_out));
  Adder #(.width(32)) adder_3 (.a(multiplexer_2_out), .b(shifter_2_out), .out(adder_3_out), .cin(1'b0));  // open: cout
  Multiplexer #(.width(32), .disabled(0), .enable("false")) multiplexer_3 (
    .in0(multiplexer_2_out), .in1(adder_3_out), .out(multiplexer_3_out), .sel(in_1[2]));
  Shifter #(.width(32)) shifter_3 (.in(shifter_2_out), .\dist (5'b00001), .out(shifter_3_out));
  Adder #(.width(32)) adder_4 (.a(multiplexer_3_out), .b(shifter_3_out), .out(adder_4_out), .cin(1'b0));  // open: cout
  Multiplexer #(.width(32), .disabled(0), .enable("false")) multiplexer_4 (
    .in0(multiplexer_3_out), .in1(adder_4_out), .out(out_3), .sel(in_1[3]));
endmodule

module test32_32 (
  input  [31:0] in_1,
  input  [31:0] in_2,
  output [31:0] out_3
);

  _32_32Mul u_32_32mul_1 (.in_2(in_2), .out_3(out_3), .in_1(in_1));
endmodule

module test4_4 (
  input  [3:0] in_1,
  input  [3:0] in_2,
  output [7:0] out_3
);

  _4_4Mul u_4_4mul_1 (.in_1(in_1), .in_2(in_2), .out_3(out_3));
endmodule

module test32_4 (
  input  [3:0] in_1,
  input  [31:0] in_2,
  output [31:0] out_3
);

  _32_4Mul u_32_4mul_1 (.in_1(in_1), .out_3(out_3), .in_2(in_2));
endmodule
