// Logisim project 除法器.circ as structural Verilog: 8 circuits, main circuit 4位div
module \_4位div  (
  input  [3:0] n2,
  input  [3:0] d,
  output [3:0] quot,
  output [3:0] rem
);

  wire comparator_1_lt, comparator_2_lt, comparator_3_lt, comparator_4_lt;
  wire [3:0] subtractor_1_out, subtractor_3_out, subtractor_4_out;
  wire [3:1] shifter_2_out_2;
  wire [7:0] multiplexer_1_out, multiplexer_2_out, multiplexer_3_out, shifter_1_out, shifter_2_out,
       shifter_3_out, shifter_4_out;
  wire [7:4] subtractor_2_out;

  Shifter shifter_1 (.in({4'b0000, n2}), .\dist (3'b001), .out(shifter_1_out));
  Comparator #(.width(4), .mode("unsigned")) comparator_1 (
    .a(shifter_1_out[7:4]), .b(d), .lt(comparator_1_lt));  // open: gt, eq
  Subtractor #(.width(4)) subtractor_1 (.a(shifter_1_out[7:4]), .b(d), .out(subtractor_1_out));  // open: bin, bout
  Multiplexer #(.width(8), .disabled(0), .enable("false")) multiplexer_1 (
    .in0({subtractor_1_out, shifter_1_out[3:1], 1'b1}), .in1(shifter_1_out), .out(multiplexer_1_out),
    .sel(comparator_1_lt));
  Shifter shifter_2 (
    .in(multiplexer_1_out), .\dist (3'b001), .out({shifter_2_out[7:4], shifter_2_out_2, shifter_2_out[0]}));
  Comparator #(.width(4), .mode("unsigned")) comparator_2 (
    .a(shifter_2_out[7:4]), .b(d), .lt(comparator_2_lt));  // open: gt, eq
  Subtractor #(.width(4)) subtractor_2 (.a(shifter_2_out[7:4]), .b(d), .out(subtractor_2_out));  // open: bin, bout
  Multiplexer #(.width(8), .disabled(0), .enable("false")) multiplexer_2 (
    .in0({subtractor_2_out, shifter_2_out_2, 1'b1}),
    .in1({shifter_2_out[7:4], shifter_2_out_2, shifter_2_out[0]}), .out(multiplexer_2_out),
    .sel(comparator_2_lt));
  Shifter shifter_3 (.in(multiplexer_2_out), .\dist (3'b001), .out(shifter_3_out));
  Comparator #(.width(4), .mode("unsigned")) comparator_3 (
    .a(shifter_3_out[7:4]), .b(d), .lt(comparator_3_lt));  // open: gt, eq
  Subtractor #(.width(4)) subtractor_3 (.a(shifter_3_out[7:4]), .b(d), .out(subtractor_3_out));  // open: bin, bout
  Multiplexer #(.width(8), .disabled(0), .enable("false")) multiplexer_3 (
    .in0({subtractor_3_out, shifter_3_out[3:1], 1'b1}), .in1(shifter_3_out), .out(multiplexer_3_out),
    .sel(comparator_3_lt));
  Shifter shifter_4 (.in(multiplexer_3_out), .\dist (3'b001), .out(shifter_4_out));
  Comparator #(.width(4), .mode("unsigned")) comparator_4 (
    .a(shifter_4_out[7:4]), .b(d), .lt(comparator_4_lt));  // open: gt, eq
  Subtractor #(.width(4)) subtractor_4 (.a(shifter_4_out[7:4]), .b(d), .out(subtractor_4_out));  // open: bin, bout
  Multiplexer #(.width(8), .disabled(0), .enable("false")) multiplexer_4 (
    .in0({subtractor_4_out, shifter_4_out[3:1], 1'b1}), .in1(shifter_4_out), .out({rem, quot}),
    .sel(comparator_4_lt));
endmodule

module testDiv4 (
  input  [3:0] in_1,
  input  [3:0] in_2,
  output [3:0] out_3,
  output [3:0] out_4
);

  \_4位div  \u_4位div_1  (.n2(in_1), .d(in_2), .quot(out_3), .rem(out_4));
endmodule

module \_32位div  (
  input  [31:0] in_1,
  input  [31:0] in_2,
  output [31:0] rem,
  output [31:0] quot
);

  wire [31:0] unit32_1_out_4, unit32_1_out_5, unit32_2_out_4, unit32_2_out_5, unit32_3_out_4, unit32_3_out_5,
       unit32_4_out_4, unit32_4_out_5, unit32_5_out_4, unit32_5_out_5, unit32_6_out_4, unit32_6_out_5,
       unit32_7_out_4, unit32_7_out_5, unit32_8_out_4, unit32_8_out_5, unit32_9_out_4, unit32_9_out_5,
       unit32_10_out_4, unit32_10_out_5, unit32_11_out_4, unit32_11_out_5, unit32_12_out_4, unit32_12_out_5,
       unit32_13_out_4, unit32_13_out_5, unit32_14_out_4, unit32_14_out_5, unit32_15_out_4, unit32_15_out_5,
       unit32_16_out_4, unit32_16_out_5, unit32_17_out_4, unit32_17_out_5, unit32_18_out_4, unit32_18_out_5,
       unit32_19_out_4, unit32_19_out_5, unit32_20_out_4, unit32_20_out_5, unit32_21_out_4, unit32_21_out_5,
       unit32_22_out_4, unit32_22_out_5, unit32_23_out_4, unit32_23_out_5, unit32_24_out_4, unit32_24_out_5,
       unit32_25_out_4, unit32_25_out_5, unit32_26_out_4, unit32_26_out_5, unit32_27_out_4, unit32_27_out_5,
       unit32_28_out_4, unit32_28_out_5, unit32_29_out_4, unit32_29_out_5, unit32_30_out_4, unit32_30_out_5,
       unit32_31_out_4, unit32_31_out_5;

  unit32 unit32_1 (.in_1({32{1'b0}}), .in_2(in_1), .in_3(in_2), .out_4(unit32_1_out_4), .out_5(unit32_1_out_5));
  unit32 unit32_2 (
    .in_1(unit32_29_out_5), .in_2(unit32_29_out_4), .in_3(in_2), .out_4(unit32_2_out_4),
    .out_5(unit32_2_out_5));
  unit32 unit32_3 (
    .in_1(unit32_30_out_5), .in_2(unit32_30_out_4), .in_3(in_2), .out_4(unit32_3_out_4),
    .out_5(unit32_3_out_5));
  unit32 unit32_4 (
    .in_1(unit32_31_out_5), .in_2(unit32_31_out_4), .in_3(in_2), .out_4(unit32_4_out_4),
    .out_5(unit32_4_out_5));
  unit32 unit32_5 (
    .in_1(unit32_1_out_5), .in_2(unit32_1_out_4), .in_3(in_2), .out_4(unit32_5_out_4), .out_5(unit32_5_out_5));
  unit32 unit32_6 (
    .in_1(unit32_2_out_5), .in_2(unit32_2_out_4), .in_3(in_2), .out_4(unit32_6_out_4), .out_5(unit32_6_out_5));
  unit32 unit32_7 (
    .in_1(unit32_3_out_5), .in_2(unit32_3_out_4), .in_3(in_2), .out_4(unit32_7_out_4), .out_5(unit32_7_out_5));
  unit32 unit32_8 (
    .in_1(unit32_4_out_5), .in_2(unit32_4_out_4), .in_3(in_2), .out_4(unit32_8_out_4), .out_5(unit32_8_out_5));
  unit32 unit32_9 (
    .in_1(unit32_5_out_5), .in_2(unit32_5_out_4), .in_3(in_2), .out_4(unit32_9_out_4), .out_5(unit32_9_out_5));
  unit32 unit32_10 (
    .in_1(unit32_6_out_5), .in_2(unit32_6_out_4), .in_3(in_2), .out_4(unit32_10_out_4),
    .out_5(unit32_10_out_5));
  unit32 unit32_11 (
    .in_1(unit32_7_out_5), .in_2(unit32_7_out_4), .in_3(in_2), .out_4(unit32_11_out_4),
    .out_5(unit32_11_out_5));
  unit32 unit32_12 (
    .in_1(unit32_8_out_5), .in_2(unit32_8_out_4), .in_3(in_2), .out_4(unit32_12_out_4),
    .out_5(unit32_12_out_5));
  unit32 unit32_13 (
    .in_1(unit32_9_out_5), .in_2(unit32_9_out_4), .in_3(in_2), .out_4(unit32_13_out_4),
    .out_5(unit32_13_out_5));
  unit32 unit32_14 (
    .in_1(unit32_10_out_5), .in_2(unit32_10_out_4), .in_3(in_2), .out_4(unit32_14_out_4),
    .out_5(unit32_14_out_5));
  unit32 unit32_15 (
    .in_1(unit32_11_out_5), .in_2(unit32_11_out_4), .in_3(in_2), .out_4(unit32_15_out_4),
    .out_5(unit32_15_out_5));
  unit32 unit32_16 (
    .in_1(unit32_12_out_5), .in_2(unit32_12_out_4), .in_3(in_2), .out_4(unit32_16_out_4),
    .out_5(unit32_16_out_5));
  unit32 unit32_17 (
    .in_1(unit32_13_out_5), .in_2(unit32_13_out_4), .in_3(in_2), .out_4(unit32_17_out_4),
    .out_5(unit32_17_out_5));
  unit32 unit32_18 (
    .in_1(unit32_14_out_5), .in_2(unit32_14_out_4), .in_3(in_2), .out_4(unit32_18_out_4),
    .out_5(unit32_18_out_5));
  unit32 unit32_19 (
    .in_1(unit32_15_out_5), .in_2(unit32_15_out_4), .in_3(in_2), .out_4(unit32_19_out_4),
    .out_5(unit32_19_out_5));
  unit32 unit32_20 (
    .in_1(unit32_16_out_5), .in_2(unit32_16_out_4), .in_3(in_2), .out_4(unit32_20_out_4),
    .out_5(unit32_20_out_5));
  unit32 unit32_21 (
    .in_1(unit32_17_out_5), .in_2(unit32_17_out_4), .in_3(in_2), .out_4(unit32_21_out_4),
    .out_5(unit32_21_out_5));
  unit32 unit32_22 (
    .in_1(unit32_18_out_5), .in_2(unit32_18_out_4), .in_3(in_2), .out_4(unit32_22_out_4),
    .out_5(unit32_22_out_5));
  unit32 unit32_23 (
    .in_1(unit32_19_out_5), .in_2(unit32_19_out_4), .in_3(in_2), .out_4(unit32_23_out_4),
    .out_5(unit32_23_out_5));
  unit32 unit32_24 (
    .in_1(unit32_20_out_5), .in_2(unit32_20_out_4), .in_3(in_2), .out_4(unit32_24_out_4),
    .out_5(unit32_24_out_5));
  unit32 unit32_25 (
    .in_1(unit32_21_out_5), .in_2(unit32_21_out_4), .in_3(in_2), .out_4(unit32_25_out_4),
    .out_5(unit32_25_out_5));
  unit32 unit32_26 (
    .in_1(unit32_22_out_5), .in_2(unit32_22_out_4), .in_3(in_2), .out_4(unit32_26_out_4),
    .out_5(unit32_26_out_5));
  unit32 unit32_27 (
    .in_1(unit32_23_out_5), .in_2(unit32_23_out_4), .in_3(in_2), .out_4(unit32_27_out_4),
    .out_5(unit32_27_out_5));
  unit32 unit32_28 (
    .in_1(unit32_24_out_5), .in_2(unit32_24_out_4), .in_3(in_2), .out_4(unit32_28_out_4),
    .out_5(unit32_28_out_5));
  unit32 unit32_29 (
    .in_1(unit32_25_out_5), .in_2(unit32_25_out_4), .in_3(in_2), .out_4(unit32_29_out_4),
    .out_5(unit32_29_out_5));
  unit32 unit32_30 (
    .in_1(unit32_26_out_5), .in_2(unit32_26_out_4), .in_3(in_2), .out_4(unit32_30_out_4),
    .out_5(unit32_30_out_5));
  unit32 unit32_31 (
    .in_1(unit32_27_out_5), .in_2(unit32_27_out_4), .in_3(in_2), .out_4(unit32_31_out_4),
    .out_5(unit32_31_out_5));
  unit32 unit32_32 (.in_1(unit32_28_out_5), .in_2(unit32_28_out_4), .in_3(in_2), .out_4(quot), .out_5(rem));
endmodule

module test32_4 (
  input  [31:0] in_1,
  input  [3:0] in_2,
  output [31:0] out_3,
  output [3:0] out_4
);

  _32_4 u_32_4_1 (.in_1(in_1), .in_2(in_2), .rem(out_4), .quot(out_3));
endmodule

module unit32_4 (
  input  [3:0] in_1,
  input  [31:0] in_2,
  input  [3:0] in_3,
  output [31:0] out_4,
  output [3:0] out_5
);

  wire comparator_1_lt;
  wire [3:0] subtractor_1_out;
  wire [31:0] shifter_1_out;

  Shifter #(.width(32)) shifter_1 (.in(in_2), .\dist (5'b00001), .out(shifter_1_out));
  Comparator #(.width(4), .mode("unsigned")) comparator_1 (
    .a({in_1[2:0], in_2[31]}), .b(in_3), .lt(comparator_1_lt));  // open: gt, eq
  Subtractor #(.width(4)) subtractor_1 (
    .a({in_1[2:0], in_2[31]}), .b(in_3), .out(subtractor_1_out));  // open: bin, bout
  Multiplexer #(.width(4), .disabled(0), .enable("false")) multiplexer_1 (
    .in0(subtractor_1_out), .in1({in_1[2:0], in_2[31]}), .out(out_5), .sel(comparator_1_lt));
  Multiplexer #(.width(32), .disabled(0), .enable("false")) multiplexer_2 (
    .in0({shifter_1_out[31:1], 1'b1}), .in1(shifter_1_out), .out(out_4), .sel(comparator_1_lt));
endmodule

module _32_4 (
  input  [31:0] in_1,
  input  [3:0] in_2,
  output [3:0] rem,
  output [31:0] quot
);

  wire [3:0] unit32_4_1_out_5, unit32_4_2_out_5, unit32_4_3_out_5, unit32_4_4_out_5, unit32_4_5_out_5,
       unit32_4_6_out_5, unit32_4_7_out_5, unit32_4_8_out_5, unit32_4_9_out_5, unit32_4_10_out_5,
       unit32_4_11_out_5, unit32_4_12_out_5, unit32_4_13_out_5, unit32_4_14_out_5, unit32_4_15_out_5,
       unit32_4_16_out_5, unit32_4_17_out_5, unit32_4_18_out_5, unit32_4_19_out_5, unit32_4_20_out_5,
       unit32_4_21_out_5, unit32_4_22_out_5, unit32_4_23_out_5, unit32_4_24_out_5, unit32_4_25_out_5,
       unit32_4_26_out_5, unit32_4_27_out_5, unit32_4_28_out_5, unit32_4_29_out_5, unit32_4_30_out_5,
       unit32_4_31_out_5;
  wire [31:0] unit32_4_1_out_4, unit32_4_2_out_4, unit32_4_3_out_4, unit32_4_4_out_4, unit32_4_5_out_4,
       unit32_4_6_out_4, unit32_4_7_out_4, unit32_4_8_out_4, unit32_4_9_out_4, unit32_4_10_out_4,
       unit32_4_11_out_4, unit32_4_12_out_4, unit32_4_13_out_4, unit32_4_14_out_4, unit32_4_15_out_4,
       unit32_4_16_out_4, unit32_4_17_out_4, unit32_4_18_out_4, unit32_4_19_out_4, unit32_4_20_out_4,
       unit32_4_21_out_4, unit32_4_22_out_4, unit32_4_23_out_4, unit32_4_24_out_4, unit32_4_25_out_4,
       unit32_4_26_out_4, unit32_4_27_out_4, unit32_4_28_out_4, unit32_4_29_out_4, unit32_4_30_out_4,
       unit32_4_31_out_4;

  unit32_4 unit32_4_1 (.in_2(in_1), .in_3(in_2), .out_4(unit32_4_1_out_4), .in_1(4'b0000), .out_5(unit32_4_1_out_5));
  unit32_4 unit32_4_2 (
    .in_2(unit32_4_29_out_4), .in_3(in_2), .out_4(unit32_4_2_out_4), .in_1(unit32_4_29_out_5),
    .out_5(unit32_4_2_out_5));
  unit32_4 unit32_4_3 (
    .in_2(unit32_4_30_out_4), .in_3(in_2), .out_4(unit32_4_3_out_4), .in_1(unit32_4_30_out_5),
    .out_5(unit32_4_3_out_5));
  unit32_4 unit32_4_4 (
    .in_2(unit32_4_31_out_4), .in_3(in_2), .out_4(unit32_4_4_out_4), .in_1(unit32_4_31_out_5),
    .out_5(unit32_4_4_out_5));
  unit32_4 unit32_4_5 (
    .in_2(unit32_4_1_out_4), .in_3(in_2), .out_4(unit32_4_5_out_4), .in_1(unit32_4_1_out_5),
    .out_5(unit32_4_5_out_5));
  unit32_4 unit32_4_6 (
    .in_2(unit32_4_2_out_4), .in_3(in_2), .out_4(unit32_4_6_out_4), .in_1(unit32_4_2_out_5),
    .out_5(unit32_4_6_out_5));
  unit32_4 unit32_4_7 (
    .in_2(unit32_4_3_out_4), .in_3(in_2), .out_4(unit32_4_7_out_4), .in_1(unit32_4_3_out_5),
    .out_5(unit32_4_7_out_5));
  unit32_4 unit32_4_8 (
    .in_2(unit32_4_4_out_4), .in_3(in_2), .out_4(unit32_4_8_out_4), .in_1(unit32_4_4_out_5),
    .out_5(unit32_4_8_out_5));
  unit32_4 unit32_4_9 (
    .in_2(unit32_4_5_out_4), .in_3(in_2), .out_4(unit32_4_9_out_4), .in_1(unit32_4_5_out_5),
    .out_5(unit32_4_9_out_5));
  unit32_4 unit32_4_10 (
    .in_2(unit32_4_6_out_4), .in_3(in_2), .out_4(unit32_4_10_out_4), .in_1(unit32_4_6_out_5),
    .out_5(unit32_4_10_out_5));
  unit32_4 unit32_4_11 (
    .in_2(unit32_4_7_out_4), .in_3(in_2), .out_4(unit32_4_11_out_4), .in_1(unit32_4_7_out_5),
    .out_5(unit32_4_11_out_5));
  unit32_4 unit32_4_12 (
    .in_2(unit32_4_8_out_4), .in_3(in_2), .out_4(unit32_4_12_out_4), .in_1(unit32_4_8_out_5),
    .out_5(unit32_4_12_out_5));
  unit32_4 unit32_4_13 (
    .in_2(unit32_4_9_out_4), .in_3(in_2), .out_4(unit32_4_13_out_4), .in_1(unit32_4_9_out_5),
    .out_5(unit32_4_13_out_5));
  unit32_4 unit32_4_14 (
    .in_2(unit32_4_10_out_4), .in_3(in_2), .out_4(unit32_4_14_out_4), .in_1(unit32_4_10_out_5),
    .out_5(unit32_4_14_out_5));
  unit32_4 unit32_4_15 (
    .in_2(unit32_4_11_out_4), .in_3(in_2), .out_4(unit32_4_15_out_4), .in_1(unit32_4_11_out_5),
    .out_5(unit32_4_15_out_5));
  unit32_4 unit32_4_16 (
    .in_2(unit32_4_12_out_4), .in_3(in_2), .out_4(unit32_4_16_out_4), .in_1(unit32_4_12_out_5),
    .out_5(unit32_4_16_out_5));
  unit32_4 unit32_4_17 (
    .in_2(unit32_4_13_out_4), .in_3(in_2), .out_4(unit32_4_17_out_4), .in_1(unit32_4_13_out_5),
    .out_5(unit32_4_17_out_5));
  unit32_4 unit32_4_18 (
    .in_2(unit32_4_14_out_4), .in_3(in_2), .out_4(unit32_4_18_out_4), .in_1(unit32_4_14_out_5),
    .out_5(unit32_4_18_out_5));
  unit32_4 unit32_4_19 (
    .in_2(unit32_4_15_out_4), .in_3(in_2), .out_4(unit32_4_19_out_4), .in_1(unit32_4_15_out_5),
    .out_5(unit32_4_19_out_5));
  unit32_4 unit32_4_20 (
    .in_2(unit32_4_16_out_4), .in_3(in_2), .out_4(unit32_4_20_out_4), .in_1(unit32_4_16_out_5),
    .out_5(unit32_4_20_out_5));
  unit32_4 unit32_4_21 (
    .in_2(unit32_4_17_out_4), .in_3(in_2), .out_4(unit32_4_21_out_4), .in_1(unit32_4_17_out_5),
    .out_5(unit32_4_21_out_5));
  unit32_4 unit32_4_22 (
    .in_2(unit32_4_18_out_4), .in_3(in_2), .out_4(unit32_4_22_out_4), .in_1(unit32_4_18_out_5),
    .out_5(unit32_4_22_out_5));
  unit32_4 unit32_4_23 (
    .in_2(unit32_4_19_out_4), .in_3(in_2), .out_4(unit32_4_23_out_4), .in_1(unit32_4_19_out_5),
    .out_5(unit32_4_23_out_5));
  unit32_4 unit32_4_24 (
    .in_2(unit32_4_20_out_4), .in_3(in_2), .out_4(unit32_4_24_out_4), .in_1(unit32_4_20_out_5),
    .out_5(unit32_4_24_out_5));
  unit32_4 unit32_4_25 (
    .in_2(unit32_4_21_out_4), .in_3(in_2), .out_4(unit32_4_25_out_4), .in_1(unit32_4_21_out_5),
    .out_5(unit32_4_25_out_5));
  unit32_4 unit32_4_26 (
    .in_2(unit32_4_22_out_4), .in_3(in_2), .out_4(unit32_4_26_out_4), .in_1(unit32_4_22_out_5),
    .out_5(unit32_4_26_out_5));
  unit32_4 unit32_4_27 (
    .in_2(unit32_4_23_out_4), .in_3(in_2), .out_4(unit32_4_27_out_4), .in_1(unit32_4_23_out_5),
    .out_5(unit32_4_27_out_5));
  unit32_4 unit32_4_28 (
    .in_2(unit32_4_24_out_4), .in_3(in_2), .out_4(unit32_4_28_out_4), .in_1(unit32_4_24_out_5),
    .out_5(unit32_4_28_out_5));
  unit32_4 unit32_4_29 (
    .in_2(unit32_4_25_out_4), .in_3(in_2), .out_4(unit32_4_29_out_4), .in_1(unit32_4_25_out_5),
    .out_5(unit32_4_29_out_5));
  unit32_4 unit32_4_30 (
    .in_2(unit32_4_26_out_4), .in_3(in_2), .out_4(unit32_4_30_out_4), .in_1(unit32_4_26_out_5),
    .out_5(unit32_4_30_out_5));
  unit32_4 unit32_4_31 (
    .in_2(unit32_4_27_out_4), .in_3(in_2), .out_4(unit32_4_31_out_4), .in_1(unit32_4_27_out_5),
    .out_5(unit32_4_31_out_5));
  unit32_4 unit32_4_32 (.in_2(unit32_4_28_out_4), .in_3(in_2), .out_4(quot), .in_1(unit32_4_28_out_5), .out_5(rem));
endmodule

module unit32 (
  input  [31:0] in_1,
  input  [31:0] in_2,
  input  [31:0] in_3,
  output [31:0] out_4,
  output [31:0] out_5
);

  wire comparator_1_lt;
  wire [31:0] shifter_1_out, subtractor_1_out;

  Shifter #(.width(32)) shifter_1 (.in(in_2), .\dist (5'b00001), .out(shifter_1_out));
  Comparator #(.width(32), .mode("unsigned")) comparator_1 (
    .a({in_1[30:0], in_2[31]}), .b(in_3), .lt(comparator_1_lt));  // open: gt, eq
  Subtractor #(.width(32)) subtractor_1 (
    .a({in_1[30:0], in_2[31]}), .b(in_3), .out(subtractor_1_out));  // open: bin, bout
  Multiplexer #(.width(32), .disabled(0), .enable("false")) multiplexer_1 (
    .in0(subtractor_1_out), .in1({in_1[30:0], in_2[31]}), .out(out_5), .sel(comparator_1_lt));
  Multiplexer #(.width(32), .disabled(0), .enable("false")) multiplexer_2 (
    .in0({shifter_1_out[31:1], 1'b1}), .in1(shifter_1_out), .out(out_4), .sel(comparator_1_lt));
endmodule

module test32 (
  input  [31:0] in_1,
  input  [31:0] in_2,
  output [31:0] out_3,
  output [31:0] out_4
);

  \_32位div  \u_32位div_1  (.in_1(in_1), .in_2(in_2), .rem(out_4), .quot(out_3));
endmodule
