// Logisim project 门禁.circ as structural Verilog: 9 circuits, main circuit 四位二进制可逆计数器
module \四位二进制可逆计数器  (
  input  CPu,
  input  CPd,
  input  CLR,
  output QA,
  output QB,
  output QC,
  output QD
);

  wire and_1_out, and_2_out, and_3_out, and_4_out, and_5_out, and_6_out, buffer_1_out, buffer_2_out, D1_qn,
       D2_qn, D3_qn, or_1_out, xor_1_out, xor_2_out, xor_3_out, xor_4_out;

  buf buffer_1 (buffer_1_out, CPu);
  buf buffer_2 (buffer_2_out, CPd);
  or or_1 (or_1_out, CPu, CPd);
  xor xor_1 (xor_1_out, buffer_1_out, buffer_2_out, QA);
  and and_1 (and_1_out, QA, buffer_1_out);
  and and_2 (and_2_out, QB, QA, buffer_1_out);
  and and_3 (and_3_out, QC, QB, QA, buffer_1_out);
  and and_4 (and_4_out, buffer_2_out, D1_qn, D2_qn, D3_qn);
  and and_5 (and_5_out, buffer_2_out, D1_qn, D2_qn);
  and and_6 (and_6_out, buffer_2_out, D1_qn);
  xor xor_2 (xor_2_out, and_1_out, and_6_out, QB);
  xor xor_3 (xor_3_out, and_2_out, and_5_out, QC);
  xor xor_4 (xor_4_out, and_3_out, and_4_out, QD);
  D_Flip_Flop #(.trigger("falling")) D1 (
    .clk(or_1_out), .D(xor_1_out), .Q(QA), .Qn(D1_qn), .reset(CLR));  // open: preset, en
  D_Flip_Flop #(.trigger("falling")) D2 (
    .clk(or_1_out), .D(xor_2_out), .Q(QB), .Qn(D2_qn), .reset(CLR));  // open: preset, en
  D_Flip_Flop #(.trigger("falling")) D3 (
    .clk(or_1_out), .D(xor_3_out), .Q(QC), .Qn(D3_qn), .reset(CLR));  // open: preset, en
  D_Flip_Flop #(.trigger("falling")) D4 (.clk(or_1_out), .D(xor_4_out), .Q(QD), .reset(CLR));  // open: Qn, preset, en
endmodule

module test (
  input  in_1,
  input  in_2,
  input  in_3,
  output out_4,
  output out_5,
  output out_6,
  output out_7
);

  \四位二进制可逆计数器  \u_四位二进制可逆计数器_1  (.CPu(in_1), .CPd(in_3), .CLR(in_2), .QA(out_7), .QB(out_6), .QC(out_5), .QD(out_4));
endmodule

module \二进制转8421BCD  (
  input  QD,
  input  QC,
  input  QB,
  input  QA,
  output S24,
  output S23,
  output S22,
  output S21,
  output S14,
  output S13,
  output S12,
  output S11
);

  wire or_1_out;

  and and_1 (S21, QD, or_1_out);
  or or_1 (or_1_out, QC, QB);
  \先行进位的四位二进制并行加法器  \u_先行进位的四位二进制并行加法器_1  (
    .C0(1'b0), .A0(1'b0), .B0(QA), .A1(S21), .B1(QB), .A2(S21), .B2(QC), .A3(1'b0), .B3(QD), .S0(S11),
    .S1(S12), .S2(S13), .S3(S14));  // open: C4

  assign S22 = 1'b0;
  assign S23 = 1'b0;
  assign S24 = 1'b0;
endmodule

module \七段译码器  (
  input  A3,
  input  A2,
  input  A1,
  input  A0,
  output a,
  output b,
  output c,
  output d,
  output e,
  output f,
  output g
);

  wire and_3_out, and_5_out, and_6_out, and_7_out, nand_1_out, nand_2_out, nand_3_out, nand_5_out,
       nand_6_out, nand_7_out, nand_8_out, nor_1_out, nor_2_out, not_1_out, not_2_out, not_3_out, not_4_out,
       or_1_out, or_2_out, or_3_out, or_4_out, or_6_out, or_8_out, xnor_1_out;

  nand nand_1 (nand_1_out, A3, A1);
  and and_1 (a, nand_1_out, nand_2_out, nand_3_out);
  nand nand_2 (nand_2_out, A2, not_1_out);
  nand nand_3 (nand_3_out, A0, nor_1_out);
  not not_1 (not_1_out, A0);
  nor nor_1 (nor_1_out, A1, A2, A3);
  nand nand_4 (b, or_1_out, or_2_out, or_3_out, nand_5_out);
  or or_1 (or_1_out, A2, A3);
  or or_2 (or_2_out, A1, A2);
  or or_3 (or_3_out, A1, A0);
  nand nand_5 (nand_5_out, A1, not_2_out, A0);
  not not_2 (not_2_out, A3);
  and and_2 (c, nand_6_out, or_4_out);
  nand nand_6 (nand_6_out, A2, A3);
  or or_4 (or_4_out, not_3_out, A2, A0);
  not not_3 (not_3_out, A1);
  or or_5 (d, xnor_1_out, and_5_out);
  xnor xnor_1 (xnor_1_out, and_3_out, A0);
  and and_3 (and_3_out, not_3_out, A2);
  and and_4 (e, not_1_out, or_6_out);
  and and_5 (and_5_out, A1, not_4_out);
  not not_4 (not_4_out, A2);
  or or_6 (or_6_out, not_4_out, A1);
  and and_6 (and_6_out, nand_7_out, A2);
  nand nand_7 (nand_7_out, A1, A0);
  or or_7 (f, and_6_out, nor_2_out, and_7_out);
  nor nor_2 (nor_2_out, A1, A0);
  and and_7 (and_7_out, not_3_out, A3);
  and and_8 (g, or_8_out, nand_8_out);
  or or_8 (or_8_out, A1, A2, A3);
  nand nand_8 (nand_8_out, A1, A2, A0);
endmodule

module \报警器  (
  input  QD,
  input  QC,
  input  QB,
  input  QA,
  input  CPu,
  output warn
);

  and and_1 (warn, QD, QC, QB, QA, CPu);
endmodule

module \报警电路  (
  input  CPu,
  input  CLR,
  input  CPd
);

  wire and_1_out, and_2_out, nand_1_out, or_1_out, \四位二进制可逆计数器_1_qa , \四位二进制可逆计数器_1_qb , \四位二进制可逆计数器_1_qc ,
       \四位二进制可逆计数器_1_qd , \报警器_1_warn ;

  or or_1 (or_1_out, \四位二进制可逆计数器_1_qa , \四位二进制可逆计数器_1_qb , \四位二进制可逆计数器_1_qc , \四位二进制可逆计数器_1_qd );
  and and_1 (and_1_out, or_1_out, CPd);
  nand nand_1 (nand_1_out, \四位二进制可逆计数器_1_qa , \四位二进制可逆计数器_1_qb , \四位二进制可逆计数器_1_qc , \四位二进制可逆计数器_1_qd );
  and and_2 (and_2_out, nand_1_out, CPu);
  \四位二进制可逆计数器  \u_四位二进制可逆计数器_1  (
    .CPu(and_2_out), .CPd(and_1_out), .CLR(CLR), .QA(\四位二进制可逆计数器_1_qa ), .QB(\四位二进制可逆计数器_1_qb ),
    .QC(\四位二进制可逆计数器_1_qc ), .QD(\四位二进制可逆计数器_1_qd ));
  \报警器  \u_报警器_1  (
    .QD(\四位二进制可逆计数器_1_qd ), .QC(\四位二进制可逆计数器_1_qc ), .QB(\四位二进制可逆计数器_1_qb ), .QA(\四位二进制可逆计数器_1_qa ),
    .CPu(CPu), .warn(\报警器_1_warn ));
  LED led_1 (.in(\报警器_1_warn ));
endmodule

module test1 (
  input  in_1,
  input  in_2,
  input  in_3,
  output out_4,
  output out_5,
  output out_6,
  output out_7
);

  \四位二进制可逆计数器  \u_四位二进制可逆计数器_1  (.CPu(in_1), .CPd(in_3), .CLR(in_2), .QA(out_7), .QB(out_6), .QC(out_5), .QD(out_4));
endmodule

module \七段数码显示管显示电路  (
  input  in_1,
  input  in_2,
  input  in_3,
  input  in_4,
  input  in_5,
  input  in_6,
  input  in_7,
  input  in_8
);

  wire \七段译码器_1_a , \七段译码器_1_b , \七段译码器_1_c , \七段译码器_1_d , \七段译码器_1_e , \七段译码器_1_f , \七段译码器_1_g ,
       \七段译码器_2_a , \七段译码器_2_b , \七段译码器_2_c , \七段译码器_2_d , \七段译码器_2_e , \七段译码器_2_f , \七段译码器_2_g ;

  \七段译码器  \u_七段译码器_1  (
    .a(\七段译码器_1_a ), .b(\七段译码器_1_b ), .c(\七段译码器_1_c ), .d(\七段译码器_1_d ), .e(\七段译码器_1_e ), .f(\七段译码器_1_f ),
    .g(\七段译码器_1_g ), .A3(in_1), .A2(in_2), .A1(in_3), .A0(in_4));
  _7_Segment_Display u_7_segment_display_1 (
    .g(\七段译码器_1_g ), .f(\七段译码器_1_f ), .a(\七段译码器_1_a ), .b(\七段译码器_1_b ), .e(\七段译码器_1_e ), .d(\七段译码器_1_d ),
    .c(\七段译码器_1_c ));  // open: dp
  _7_Segment_Display u_7_segment_display_2 (
    .g(\七段译码器_2_g ), .f(\七段译码器_2_f ), .a(\七段译码器_2_a ), .b(\七段译码器_2_b ), .e(\七段译码器_2_e ), .d(\七段译码器_2_d ),
    .c(\七段译码器_2_c ));  // open: dp
  \七段译码器  \u_七段译码器_2  (
    .a(\七段译码器_2_a ), .b(\七段译码器_2_b ), .c(\七段译码器_2_c ), .d(\七段译码器_2_d ), .e(\七段译码器_2_e ), .f(\七段译码器_2_f ),
    .g(\七段译码器_2_g ), .A3(in_5), .A2(in_6), .A1(in_7), .A0(in_8));
endmodule

module \门禁  (
  input  CPu,
  input  CLR,
  input  CPd
);

  wire and_1_out, and_2_out, nand_1_out, or_1_out, \七段译码器_1_a , \七段译码器_1_b , \七段译码器_1_c , \七段译码器_1_d ,
       \七段译码器_1_e , \七段译码器_1_f , \七段译码器_1_g , \七段译码器_2_a , \七段译码器_2_b , \七段译码器_2_c , \七段译码器_2_d ,
       \七段译码器_2_e , \七段译码器_2_f , \七段译码器_2_g , \二进制转8421bcd_1_s11 , \二进制转8421bcd_1_s12 , \二进制转8421bcd_1_s13 ,
       \二进制转8421bcd_1_s14 , \二进制转8421bcd_1_s21 , \二进制转8421bcd_1_s22 , \二进制转8421bcd_1_s23 ,
       \二进制转8421bcd_1_s24 , \四位二进制可逆计数器_1_qa , \四位二进制可逆计数器_1_qb , \四位二进制可逆计数器_1_qc , \四位二进制可逆计数器_1_qd ,
       \报警器_1_warn ;

  or or_1 (or_1_out, \四位二进制可逆计数器_1_qa , \四位二进制可逆计数器_1_qb , \四位二进制可逆计数器_1_qc , \四位二进制可逆计数器_1_qd );
  \七段译码器  \u_七段译码器_1  (
    .a(\七段译码器_1_a ), .b(\七段译码器_1_b ), .c(\七段译码器_1_c ), .d(\七段译码器_1_d ), .e(\七段译码器_1_e ), .f(\七段译码器_1_f ),
    .g(\七段译码器_1_g ), .A3(\二进制转8421bcd_1_s24 ), .A2(\二进制转8421bcd_1_s23 ), .A1(\二进制转8421bcd_1_s22 ),
    .A0(\二进制转8421bcd_1_s21 ));
  and and_1 (and_1_out, or_1_out, CPd);
  nand nand_1 (nand_1_out, \四位二进制可逆计数器_1_qa , \四位二进制可逆计数器_1_qb , \四位二进制可逆计数器_1_qc , \四位二进制可逆计数器_1_qd );
  and and_2 (and_2_out, nand_1_out, CPu);
  _7_Segment_Display u_7_segment_display_1 (
    .g(\七段译码器_1_g ), .f(\七段译码器_1_f ), .a(\七段译码器_1_a ), .b(\七段译码器_1_b ), .e(\七段译码器_1_e ), .d(\七段译码器_1_d ),
    .c(\七段译码器_1_c ));  // open: dp
  \二进制转8421BCD  \u_二进制转8421bcd_1  (
    .S24(\二进制转8421bcd_1_s24 ), .S23(\二进制转8421bcd_1_s23 ), .S22(\二进制转8421bcd_1_s22 ),
    .S21(\二进制转8421bcd_1_s21 ), .S14(\二进制转8421bcd_1_s14 ), .S13(\二进制转8421bcd_1_s13 ),
    .S12(\二进制转8421bcd_1_s12 ), .S11(\二进制转8421bcd_1_s11 ), .QD(\四位二进制可逆计数器_1_qd ), .QC(\四位二进制可逆计数器_1_qc ),
    .QB(\四位二进制可逆计数器_1_qb ), .QA(\四位二进制可逆计数器_1_qa ));
  _7_Segment_Display u_7_segment_display_2 (
    .g(\七段译码器_2_g ), .f(\七段译码器_2_f ), .a(\七段译码器_2_a ), .b(\七段译码器_2_b ), .e(\七段译码器_2_e ), .d(\七段译码器_2_d ),
    .c(\七段译码器_2_c ));  // open: dp
  \四位二进制可逆计数器  \u_四位二进制可逆计数器_1  (
    .CPu(and_2_out), .CPd(and_1_out), .CLR(CLR), .QA(\四位二进制可逆计数器_1_qa ), .QB(\四位二进制可逆计数器_1_qb ),
    .QC(\四位二进制可逆计数器_1_qc ), .QD(\四位二进制可逆计数器_1_qd ));
  \七段译码器  \u_七段译码器_2  (
    .a(\七段译码器_2_a ), .b(\七段译码器_2_b ), .c(\七段译码器_2_c ), .d(\七段译码器_2_d ), .e(\七段译码器_2_e ), .f(\七段译码器_2_f ),
    .g(\七段译码器_2_g ), .A3(\二进制转8421bcd_1_s14 ), .A2(\二进制转8421bcd_1_s13 ), .A1(\二进制转8421bcd_1_s12 ),
    .A0(\二进制转8421bcd_1_s11 ));
  \报警器  \u_报警器_1  (
    .QD(\四位二进制可逆计数器_1_qd ), .QC(\四位二进制可逆计数器_1_qc ), .QB(\四位二进制可逆计数器_1_qb ), .QA(\四位二进制可逆计数器_1_qa ),
    .CPu(CPu), .warn(\报警器_1_warn ));
  LED led_1 (.in(\报警器_1_warn ));
endmodule
