// Logisim project 数字钟.circ as structural Verilog: 19 circuits, main circuit 60进制计数器
module \_60进制计数器  (
  input  CPu,
  input  Adj,
  input  CPd,
  input  CLR,
  output out_5,
  output out_6,
  output out_7,
  output out_8,
  output out_9,
  output out_10,
  output out_11,
  output out_12,
  output Qcc
);

  wire and_1_out, or_1_out, \模6计数器_1_进位 , \模10计数器_1_借位 , \模10计数器_1_进位 ;

  or or_1 (or_1_out, out_12, out_11, out_10, out_9, out_8, out_7, out_6, out_5);
  and and_1 (and_1_out, or_1_out, Adj, CPd);
  \模10计数器  \u_模10计数器_1  (
    .CPu(CPu), .CPd(and_1_out), .\进位 (\模10计数器_1_进位 ), .out_4(out_5), .out_5(out_6), .out_6(out_7),
    .out_7(out_8), .\借位 (\模10计数器_1_借位 ), .CLR(CLR));
  \模6计数器  \u_模6计数器_1  (
    .CLR(CLR), .CPu(\模10计数器_1_进位 ), .CPd(\模10计数器_1_借位 ), .\进位 (\模6计数器_1_进位 ), .out_4(out_9), .out_5(out_10),
    .out_6(out_11), .out_7(out_12));  // open: 借位
  not not_1 (Qcc, \模6计数器_1_进位 );
endmodule

module \模6计数器  (
  input  CLR,
  input  CPu,
  input  CPd,
  output out_4,
  output out_5,
  output out_6,
  output out_7,
  output \借位 ,
  output \进位 
);

  wire and_2_out, nor_1_out, or_1_out;

  or or_1 (or_1_out, CLR, \进位 );
  \四位二进制计数器  \u_四位二进制计数器_1  (
    .CPu(CPu), .CPd(CPd), .QA(out_7), .QB(out_6), .QC(out_5), .QD(out_4), .Q(\借位 ), .Q3(1'b1), .Q2(1'b0),
    .Q4(1'b0), .Q1(1'b1), .CLR(or_1_out));
  and and_1 (\借位 , out_4, out_5, out_6, out_7);
  and and_2 (and_2_out, out_5, out_6);
  nor nor_1 (nor_1_out, out_4, out_7);
  and and_3 (\进位 , and_2_out, nor_1_out);
endmodule

module \四位二进制计数器  (
  input  CPu,
  input  CPd,
  input  CLR,
  input  Q4,
  input  Q3,
  input  Q2,
  input  Q1,
  input  Q,
  output QA,
  output QB,
  output QC,
  output QD
);

  wire and_1_out, and_2_out, and_3_out, and_4_out, and_5_out, and_6_out, buffer_1_out, buffer_2_out, D1_qn,
       D2_qn, D3_qn, demultiplexer_1_out0, demultiplexer_1_out1, demultiplexer_2_out0, demultiplexer_2_out1,
       demultiplexer_3_out0, demultiplexer_3_out1, demultiplexer_4_out0, demultiplexer_4_out1, or_1_out,
       or_2_out, or_3_out, or_4_out, or_5_out, xor_1_out, xor_2_out, xor_3_out, xor_4_out;

  buf buffer_1 (buffer_1_out, CPu);
  buf buffer_2 (buffer_2_out, CPd);
  or or_1 (or_1_out, CPu, CPd);
  xor xor_1 (xor_1_out, buffer_1_out, buffer_2_out, QA);
  and and_1 (and_1_out, QA, buffer_1_out);
  and and_2 (and_2_out, QB, QA, buffer_1_out);
  and and_3 (and_3_out, QC, QB, QA, buffer_1_out);
  and and_4 (and_4_out, buffer_2_out, D1_qn, D2_qn, D3_qn);
  and and_5 (and_5_out, buffer_2_out, D1_qn, D2_qn);
  and and_6 (and_6_out, buffer_2_out, D1_qn);
  xor xor_2 (xor_2_out, and_1_out, and_6_out, QB);
  xor xor_3 (xor_3_out, and_2_out, and_5_out, QC);
  xor xor_4 (xor_4_out, and_3_out, and_4_out, QD);
  D_Flip_Flop #(.trigger("falling")) D1 (
    .clk(or_1_out), .D(xor_1_out), .Q(QA), .Qn(D1_qn), .preset(demultiplexer_4_out1), .reset(or_5_out));  // open: en
  D_Flip_Flop #(.trigger("falling")) D2 (
    .clk(or_1_out), .D(xor_2_out), .Q(QB), .Qn(D2_qn), .preset(demultiplexer_3_out1), .reset(or_4_out));  // open: en
  D_Flip_Flop #(.trigger("falling")) D3 (
    .clk(or_1_out), .D(xor_3_out), .Q(QC), .Qn(D3_qn), .preset(demultiplexer_2_out1), .reset(or_3_out));  // open: en
  D_Flip_Flop #(.trigger("falling")) D4 (
    .clk(or_1_out), .D(xor_4_out), .Q(QD), .preset(demultiplexer_1_out1), .reset(or_2_out));  // open: Qn, en
  or or_2 (or_2_out, CLR, demultiplexer_1_out0);
  Demultiplexer #(.disabled(0), .enable("false")) demultiplexer_1 (
    .out0(demultiplexer_1_out0), .out1(demultiplexer_1_out1), .in(Q), .sel(Q4));
  or or_3 (or_3_out, CLR, demultiplexer_2_out0);
  Demultiplexer #(.disabled(0), .enable("false")) demultiplexer_2 (
    .out0(demultiplexer_2_out0), .out1(demultiplexer_2_out1), .in(Q), .sel(Q3));
  or or_4 (or_4_out, CLR, demultiplexer_3_out0);
  Demultiplexer #(.disabled(0), .enable("false")) demultiplexer_3 (
    .out0(demultiplexer_3_out0), .out1(demultiplexer_3_out1), .in(Q), .sel(Q2));
  or or_5 (or_5_out, CLR, demultiplexer_4_out0);
  Demultiplexer #(.disabled(0), .enable("false")) demultiplexer_4 (
    .out0(demultiplexer_4_out0), .out1(demultiplexer_4_out1), .in(Q), .sel(Q1));
endmodule

module \模10计数器  (
  input  CLR,
  input  CPu,
  input  CPd,
  output out_4,
  output out_5,
  output out_6,
  output out_7,
  output \借位 ,
  output \进位 
);

  wire and_2_out, nor_1_out, or_1_out;

  or or_1 (or_1_out, CLR, \进位 );
  \四位二进制计数器  \u_四位二进制计数器_1  (
    .CPu(CPu), .CPd(CPd), .QA(out_7), .QB(out_6), .QC(out_5), .QD(out_4), .Q(\借位 ), .Q3(1'b0), .Q2(1'b0),
    .Q4(1'b1), .Q1(1'b1), .CLR(or_1_out));
  and and_1 (\借位 , out_4, out_5, out_6, out_7);
  and and_2 (and_2_out, out_4, out_6);
  nor nor_1 (nor_1_out, out_5, out_7);
  and and_3 (\进位 , and_2_out, nor_1_out);
endmodule

module \_12_24进制计数器  (
  input  Set,
  input  CPu,
  input  Adj,
  input  CPd,
  input  CLR,
  output out_6,
  output out_7,
  output out_8,
  output out_9,
  output out_10,
  output out_11,
  output out_12,
  output out_13,
  output Qcc
);

  wire and_1_out, and_2_out, multiplexer_1_out, or_1_out;

  \_60进制计数器  \u_60进制计数器_1  (
    .CPu(CPu), .Adj(Adj), .CPd(CPd), .CLR(or_1_out), .out_5(out_10), .out_6(out_11), .out_7(out_12),
    .out_8(out_13), .out_9(out_6), .out_10(out_7), .out_11(out_8), .out_12(out_9));  // open: Qcc
  and and_1 (and_1_out, out_9, out_12);
  and and_2 (and_2_out, out_8, out_11);
  or or_1 (or_1_out, multiplexer_1_out, CLR);
  Multiplexer #(.disabled(0), .enable("false")) multiplexer_1 (
    .in0(and_1_out), .in1(and_2_out), .out(multiplexer_1_out), .sel(Set));
  not not_1 (Qcc, multiplexer_1_out);
endmodule

module LED (
  input  TT,
  input  AM_FM,
  output [4:0] out_3,
  output [4:0] out_4,
  output [4:0] out_5,
  output [4:0] out_6
);

  wire [19:0] multiplexer_2_out;

  Multiplexer #(.width(20), .disabled(0), .enable("false")) multiplexer_1 (
    .in0({20{1'b0}}), .in1(multiplexer_2_out), .out({out_3, out_4, out_5, out_6}), .sel(TT));
  Multiplexer #(.width(20), .disabled(0), .enable("false")) multiplexer_2 (
    .in0(20'hfca1), .in1(20'h87e90), .out(multiplexer_2_out), .sel(AM_FM));
endmodule

module LED_test (
  input  in_1,
  input  in_2
);

  wire [4:0] led_1_out_3, led_1_out_4, led_1_out_5, led_1_out_6;

  DotMatrix #(.matrixcols(4), .matrixrows(5)) dotmatrix_1 (
    .col0(led_1_out_3), .col1(led_1_out_4), .col2(led_1_out_5), .col3(led_1_out_6));
  LED led_1 (
    .TT(in_2), .AM_FM(in_1), .out_3(led_1_out_3), .out_4(led_1_out_4), .out_5(led_1_out_5),
    .out_6(led_1_out_6));
endmodule

module \整点报时  (
  input  [3:0] \分2 ,
  input  [3:0] \分1 ,
  input  [3:0] \秒2 ,
  output out_4
);

  wire and_1_out, nor_1_out;

  and and_1 (and_1_out, \分2 [0], \分2 [2], \分1 [0], \分1 [3], \秒2 [0], \秒2 [2]);
  nor nor_1 (nor_1_out, \分1 [2], \秒2 [1], \秒2 [3], \分1 [1], \分2 [3], \分2 [1]);
  and and_2 (out_4, and_1_out, nor_1_out);
endmodule

module \脉冲产生器  (
  input  _8Hz,
  output _1Hz
);

  wire not_1_out, \模8计数器进位_1_进位 ;

  \模8计数器进位  \u_模8计数器进位_1  (.CPu(_8Hz), .\进位 (\模8计数器进位_1_进位 ));
  D_Flip_Flop d_ff_1 (.clk(\模8计数器进位_1_进位 ), .D(not_1_out), .Q(_1Hz));  // open: Qn, preset, en, reset
  not not_1 (not_1_out, _1Hz);
endmodule

module \模8计数器进位  (
  input  CPu,
  output \进位 
);

  \四位二进制计数器  \u_四位二进制计数器_1  (
    .CPu(CPu), .CPd(1'b0), .QD(\进位 ), .Q(1'b0), .Q3(1'b0), .Q2(1'b0), .Q4(1'b0), .Q1(1'b0), .CLR(\进位 ));  // open: QA, QB, QC
endmodule

module \数字钟_8421码设置闹钟  (
  input  [3:0] in_1,
  input  [3:0] in_2,
  input  [3:0] in_3,
  input  [3:0] in_4,
  input  CLR,
  input  CPu,
  input  CPd,
  input  CP,
  input  Adj1,
  input  Adj0,
  input  Set,
  output \报时 ,
  output [3:0] \时2 ,
  output [3:0] \时1 ,
  output [4:0] LED3,
  output [4:0] LED2,
  output [3:0] \秒2 ,
  output [3:0] \秒1 ,
  output [3:0] \分2 ,
  output [3:0] \分1 ,
  output \闹钟 ,
  output [4:0] LED1,
  output [4:0] LED0
);

  wire d_ff_1_q, multiplexer_1_out, multiplexer_2_out, \n12_24进制计数器_1_qcc , \n60进制计数器_1_qcc ,
       \n60进制计数器_2_qcc , not_1_out, not_2_out, not_3_out, not_4_out, not_5_out, \脉冲产生器_1__1hz ;

  \脉冲产生器  \u_脉冲产生器_1  (._8Hz(CP), ._1Hz(\脉冲产生器_1__1hz ));
  \_60进制计数器  \u_60进制计数器_1  (
    .CPu(\脉冲产生器_1__1hz ), .Adj(1'b0), .CPd(1'b0), .CLR(CLR), .Qcc(\n60进制计数器_1_qcc ), .out_5(\秒1 [3]),
    .out_6(\秒1 [2]), .out_7(\秒1 [1]), .out_8(\秒1 [0]), .out_9(\秒2 [3]), .out_10(\秒2 [2]), .out_11(\秒2 [1]),
    .out_12(\秒2 [0]));
  not not_1 (not_1_out, \n60进制计数器_1_qcc );
  Multiplexer #(.enable("false")) multiplexer_1 (.in0(not_1_out), .in1(CPu), .out(multiplexer_1_out), .sel(Adj1));
  not not_2 (not_2_out, \n60进制计数器_2_qcc );
  \_60进制计数器  \u_60进制计数器_2  (
    .CPu(multiplexer_1_out), .Adj(Adj1), .CPd(CPd), .CLR(CLR), .Qcc(\n60进制计数器_2_qcc ), .out_5(\分1 [3]),
    .out_6(\分1 [2]), .out_7(\分1 [1]), .out_8(\分1 [0]), .out_9(\分2 [3]), .out_10(\分2 [2]), .out_11(\分2 [1]),
    .out_12(\分2 [0]));
  Multiplexer #(.enable("false")) multiplexer_2 (.in0(not_2_out), .in1(CPu), .out(multiplexer_2_out), .sel(Adj0));
  \整点报时  \u_整点报时_1  (.out_4(\报时 ), .\分2 (\分2 ), .\分1 (\分1 ), .\秒2 (\秒2 ));
  \_12_24进制计数器  \u_12_24进制计数器_1  (
    .CPu(multiplexer_2_out), .Adj(Adj0), .CPd(CPd), .Qcc(\n12_24进制计数器_1_qcc ), .CLR(CLR), .out_6(\时2 [3]),
    .out_7(\时2 [2]), .out_8(\时2 [1]), .out_9(\时2 [0]), .out_10(\时1 [3]), .out_11(\时1 [2]), .out_12(\时1 [1]),
    .out_13(\时1 [0]), .Set(Set));
  not not_3 (not_3_out, \n12_24进制计数器_1_qcc );
  \闹钟  \u_闹钟_1  (
    .\时2 (\时2 ), .\时1 (\时1 ), .\分2 (\分2 ), .\分1 (\分1 ), .\闹钟 (\闹钟 ), .\秒2 (\秒2 ), .\时2设 (in_1), .\时1设 (in_2),
    .\分2设 (in_3), .\分1设 (in_4));
  not not_4 (not_4_out, d_ff_1_q);
  LED led_1 (.TT(not_5_out), .AM_FM(d_ff_1_q), .out_3(LED3), .out_4(LED2), .out_5(LED1), .out_6(LED0));
  D_Flip_Flop d_ff_1 (.clk(not_3_out), .D(not_4_out), .Q(d_ff_1_q));  // open: Qn, preset, en, reset
  not not_5 (not_5_out, Set);
endmodule

module \七段译码器  (
  input  A3,
  input  A2,
  input  A1,
  input  A0,
  output a,
  output b,
  output c,
  output d,
  output e,
  output f,
  output g
);

  wire and_3_out, and_5_out, and_6_out, and_7_out, nand_1_out, nand_2_out, nand_3_out, nand_5_out,
       nand_6_out, nand_7_out, nand_8_out, nor_1_out, nor_2_out, not_1_out, not_2_out, not_3_out, not_4_out,
       or_1_out, or_2_out, or_3_out, or_4_out, or_6_out, or_8_out, xnor_1_out;

  nand nand_1 (nand_1_out, A3, A1);
  and and_1 (a, nand_1_out, nand_2_out, nand_3_out);
  nand nand_2 (nand_2_out, A2, not_1_out);
  nand nand_3 (nand_3_out, A0, nor_1_out);
  not not_1 (not_1_out, A0);
  nor nor_1 (nor_1_out, A1, A2, A3);
  nand nand_4 (b, or_1_out, or_2_out, or_3_out, nand_5_out);
  or or_1 (or_1_out, A2, A3);
  or or_2 (or_2_out, A1, A2);
  or or_3 (or_3_out, A1, A0);
  nand nand_5 (nand_5_out, A1, not_2_out, A0);
  not not_2 (not_2_out, A3);
  and and_2 (c, nand_6_out, or_4_out);
  nand nand_6 (nand_6_out, A2, A3);
  or or_4 (or_4_out, not_3_out, A2, A0);
  not not_3 (not_3_out, A1);
  or or_5 (d, xnor_1_out, and_5_out);
  xnor xnor_1 (xnor_1_out, and_3_out, A0);
  and and_3 (and_3_out, not_3_out, A2);
  and and_4 (e, not_1_out, or_6_out);
  and and_5 (and_5_out, A1, not_4_out);
  not not_4 (not_4_out, A2);
  or or_6 (or_6_out, not_4_out, A1);
  and and_6 (and_6_out, nand_7_out, A2);
  nand nand_7 (nand_7_out, A1, A0);
  or or_7 (f, and_6_out, nor_2_out, and_7_out);
  nor nor_2 (nor_2_out, A1, A0);
  and and_7 (and_7_out, not_3_out, A3);
  and and_8 (g, or_8_out, nand_8_out);
  or or_8 (or_8_out, A1, A2, A3);
  nand nand_8 (nand_8_out, A1, A2, A0);
endmodule

module \数字钟_显示管设置闹钟  (
  input  Adj0,
  input  Adj1,
  input  CP,
  input  CLR,
  input  \闹钟时控制 ,
  input  \闹钟清零 ,
  input  \闹钟分控制 ,
  input  CPu,
  input  CPd,
  input  Set,
  output [4:0] out_11,
  output [4:0] out_12,
  output [4:0] out_13,
  output [4:0] out_14,
  output [3:0] out_15,
  output [3:0] out_16,
  output [3:0] out_17,
  output [3:0] out_18,
  output [3:0] out_19,
  output [3:0] out_20,
  output \报时 ,
  output \闹钟 ,
  output [3:0] \时2设 ,
  output [3:0] \时1设 ,
  output [3:0] \分2设 ,
  output [3:0] \分1设 
);

  wire and_1_out, and_2_out, and_3_out, and_4_out;

  \数字钟_8421码设置闹钟  \u_数字钟_8421码设置闹钟_1  (
    .CP(CP), .CLR(CLR), .\报时 (\报时 ), .\秒2 (out_19), .\秒1 (out_20), .LED3(out_11), .LED2(out_12),
    .LED1(out_13), .LED0(out_14), .CPu(CPu), .Adj1(Adj1), .CPd(CPd), .Adj0(Adj0), .Set(Set), .\分2 (out_17),
    .\分1 (out_18), .\时2 (out_15), .\时1 (out_16), .\闹钟 (\闹钟 ), .in_1(\时2设 ), .in_3(\分2设 ), .in_2(\时1设 ),
    .in_4(\分1设 ));
  and and_1 (and_1_out, CPu, \闹钟时控制 );
  and and_2 (and_2_out, CPd, \闹钟时控制 );
  and and_3 (and_3_out, CPu, \闹钟分控制 );
  and and_4 (and_4_out, CPd, \闹钟分控制 );
  \_12_24进制计数器  \u_12_24进制计数器_1  (
    .CPu(and_1_out), .Adj(1'b1), .CPd(and_2_out), .CLR(\闹钟清零 ), .out_6(\时2设 [3]), .out_7(\时2设 [2]),
    .out_8(\时2设 [1]), .out_9(\时2设 [0]), .out_10(\时1设 [3]), .out_11(\时1设 [2]), .out_12(\时1设 [1]),
    .out_13(\时1设 [0]), .Set(Set));  // open: Qcc
  \_60进制计数器  \u_60进制计数器_1  (
    .CPu(and_3_out), .Adj(1'b1), .CPd(and_4_out), .CLR(\闹钟清零 ), .out_5(\分1设 [3]), .out_6(\分1设 [2]),
    .out_7(\分1设 [1]), .out_8(\分1设 [0]), .out_9(\分2设 [3]), .out_10(\分2设 [2]), .out_11(\分2设 [1]),
    .out_12(\分2设 [0]));  // open: Qcc
endmodule

module \闹钟  (
  input  [3:0] \时2设 ,
  input  [3:0] \时2 ,
  input  [3:0] \时1设 ,
  input  [3:0] \时1 ,
  input  [3:0] \分2设 ,
  input  [3:0] \分2 ,
  input  [3:0] \分1设 ,
  input  [3:0] \分1 ,
  input  [3:0] \秒2 ,
  output \闹钟 
);

  wire comparator_1_eq, comparator_2_eq, comparator_3_eq, comparator_4_eq, comparator_5_eq;

  Comparator #(.width(4)) comparator_1 (.a(\时2设 ), .b(\时2 ), .eq(comparator_1_eq));  // open: gt, lt
  Comparator #(.width(4)) comparator_2 (.a(\时1设 ), .b(\时1 ), .eq(comparator_2_eq));  // open: gt, lt
  Comparator #(.width(4)) comparator_3 (.a(\分2设 ), .b(\分2 ), .eq(comparator_3_eq));  // open: gt, lt
  Comparator #(.width(4)) comparator_4 (.a(\分1设 ), .b(\分1 ), .eq(comparator_4_eq));  // open: gt, lt
  Comparator #(.width(4)) comparator_5 (.a(4'b0000), .b(\秒2 ), .eq(comparator_5_eq));  // open: gt, lt
  and and_1 (\闹钟 , comparator_1_eq, comparator_2_eq, comparator_3_eq, comparator_4_eq, comparator_5_eq);
endmodule

module \数字钟  (
  input  in_1,
  input  in_2,
  input  in_3,
  input  in_4,
  input  in_5,
  input  in_6,
  input  in_7,
  input  in_8,
  input  in_9
);

  wire clock_1_out, \数字钟_显示管设置闹钟_1_报时 , \数字钟_显示管设置闹钟_1_闹钟 ;
  wire [3:0] \数字钟_显示管设置闹钟_1_out_15 , \数字钟_显示管设置闹钟_1_out_16 , \数字钟_显示管设置闹钟_1_out_17 , \数字钟_显示管设置闹钟_1_out_18 ,
       \数字钟_显示管设置闹钟_1_out_19 , \数字钟_显示管设置闹钟_1_out_20 , \数字钟_显示管设置闹钟_1_分1设 , \数字钟_显示管设置闹钟_1_分2设 ,
       \数字钟_显示管设置闹钟_1_时1设 , \数字钟_显示管设置闹钟_1_时2设 ;
  wire [4:0] \数字钟_显示管设置闹钟_1_out_11 , \数字钟_显示管设置闹钟_1_out_12 , \数字钟_显示管设置闹钟_1_out_13 , \数字钟_显示管设置闹钟_1_out_14 ;

  DotMatrix #(.matrixcols(4), .matrixrows(5)) dotmatrix_1 (
    .col0(\数字钟_显示管设置闹钟_1_out_11 ), .col1(\数字钟_显示管设置闹钟_1_out_12 ), .col2(\数字钟_显示管设置闹钟_1_out_13 ),
    .col3(\数字钟_显示管设置闹钟_1_out_14 ));
  Clock clock_1 (.out(clock_1_out));
  Hex_Digit_Display hex_digit_display_1 (.value(\数字钟_显示管设置闹钟_1_out_16 ));  // open: dp
  Hex_Digit_Display hex_digit_display_2 (.value(\数字钟_显示管设置闹钟_1_out_15 ));  // open: dp
  Hex_Digit_Display hex_digit_display_3 (.value(\数字钟_显示管设置闹钟_1_out_17 ));  // open: dp
  Hex_Digit_Display hex_digit_display_4 (.value(\数字钟_显示管设置闹钟_1_out_19 ));  // open: dp
  Hex_Digit_Display hex_digit_display_5 (.value(\数字钟_显示管设置闹钟_1_out_18 ));  // open: dp
  \数字钟_显示管设置闹钟  \u_数字钟_显示管设置闹钟_1  (
    .Adj0(in_1), .Adj1(in_2), .\闹钟清零 (in_7), .\报时 (\数字钟_显示管设置闹钟_1_报时 ), .\闹钟 (\数字钟_显示管设置闹钟_1_闹钟 ),
    .out_11(\数字钟_显示管设置闹钟_1_out_11 ), .out_12(\数字钟_显示管设置闹钟_1_out_12 ), .out_13(\数字钟_显示管设置闹钟_1_out_13 ),
    .out_14(\数字钟_显示管设置闹钟_1_out_14 ), .out_15(\数字钟_显示管设置闹钟_1_out_15 ), .out_16(\数字钟_显示管设置闹钟_1_out_16 ),
    .out_17(\数字钟_显示管设置闹钟_1_out_17 ), .out_18(\数字钟_显示管设置闹钟_1_out_18 ), .out_19(\数字钟_显示管设置闹钟_1_out_19 ),
    .out_20(\数字钟_显示管设置闹钟_1_out_20 ), .\时2设 (\数字钟_显示管设置闹钟_1_时2设 ), .\时1设 (\数字钟_显示管设置闹钟_1_时1设 ),
    .\分2设 (\数字钟_显示管设置闹钟_1_分2设 ), .\分1设 (\数字钟_显示管设置闹钟_1_分1设 ), .CPu(in_3), .CPd(in_4), .Set(in_5), .CLR(in_6),
    .CP(clock_1_out), .\闹钟时控制 (in_8), .\闹钟分控制 (in_9));
  Hex_Digit_Display hex_digit_display_6 (.value(\数字钟_显示管设置闹钟_1_out_20 ));  // open: dp
  LED_part led_1 (.in(\数字钟_显示管设置闹钟_1_报时 ));
  LED_part led_2 (.in(\数字钟_显示管设置闹钟_1_闹钟 ));
  Hex_Digit_Display hex_digit_display_7 (.value(\数字钟_显示管设置闹钟_1_时1设 ));  // open: dp
  Hex_Digit_Display hex_digit_display_8 (.value(\数字钟_显示管设置闹钟_1_时2设 ));  // open: dp
  Hex_Digit_Display hex_digit_display_9 (.value(\数字钟_显示管设置闹钟_1_分2设 ));  // open: dp
  Hex_Digit_Display hex_digit_display_10 (.value(\数字钟_显示管设置闹钟_1_分1设 ));  // open: dp
endmodule

module \_60进制计数器test  (
  input  in_1,
  input  in_2,
  input  in_3,
  input  in_4
);

  wire [3:0] \n60进制计数器_1_out_8 , \n60进制计数器_1_out_12 ;

  Hex_Digit_Display hex_digit_display_1 (.value(\n60进制计数器_1_out_12 ));  // open: dp
  Hex_Digit_Display hex_digit_display_2 (.value(\n60进制计数器_1_out_8 ));  // open: dp
  \_60进制计数器  \u_60进制计数器_1  (
    .CPu(in_1), .Adj(in_2), .CPd(in_3), .CLR(in_4), .out_5(\n60进制计数器_1_out_8 [3]),
    .out_6(\n60进制计数器_1_out_8 [2]), .out_7(\n60进制计数器_1_out_8 [1]), .out_8(\n60进制计数器_1_out_8 [0]),
    .out_9(\n60进制计数器_1_out_12 [3]), .out_10(\n60进制计数器_1_out_12 [2]), .out_11(\n60进制计数器_1_out_12 [1]),
    .out_12(\n60进制计数器_1_out_12 [0]));  // open: Qcc
endmodule

module \_12_24进制计数器test  (
  input  in_1,
  input  in_2,
  input  in_3,
  input  in_4,
  input  in_5
);

  wire [3:0] \n12_24进制计数器_1_out_9 , \n12_24进制计数器_1_out_13 ;

  Hex_Digit_Display hex_digit_display_1 (.value(\n12_24进制计数器_1_out_9 ));  // open: dp
  Hex_Digit_Display hex_digit_display_2 (.value(\n12_24进制计数器_1_out_13 ));  // open: dp
  \_12_24进制计数器  \u_12_24进制计数器_1  (
    .CPu(in_1), .Adj(in_2), .CPd(in_3), .CLR(in_4), .out_6(\n12_24进制计数器_1_out_9 [3]),
    .out_7(\n12_24进制计数器_1_out_9 [2]), .out_8(\n12_24进制计数器_1_out_9 [1]), .out_9(\n12_24进制计数器_1_out_9 [0]),
    .out_10(\n12_24进制计数器_1_out_13 [3]), .out_11(\n12_24进制计数器_1_out_13 [2]),
    .out_12(\n12_24进制计数器_1_out_13 [1]), .out_13(\n12_24进制计数器_1_out_13 [0]), .Set(in_5));  // open: Qcc
endmodule

module \整点报时test  (
  input  [3:0] in_1,
  input  [3:0] in_2,
  input  [3:0] in_3
);

  wire \整点报时_1_out_4 ;

  \整点报时  \u_整点报时_1  (.out_4(\整点报时_1_out_4 ), .\分2 (in_1), .\分1 (in_2), .\秒2 (in_3));
  LED_part led_1 (.in(\整点报时_1_out_4 ));
endmodule

module \闹钟test  (
  input  [3:0] in_1,
  input  [3:0] in_2,
  input  [3:0] in_3,
  input  [3:0] in_4,
  input  [3:0] in_5,
  input  [3:0] in_6,
  input  [3:0] in_7,
  input  [3:0] in_8,
  input  [3:0] in_9
);

  wire \闹钟_1_闹钟 ;

  \闹钟  \u_闹钟_1  (
    .\时2 (in_1), .\时1 (in_2), .\分2 (in_3), .\分1 (in_4), .\闹钟 (\闹钟_1_闹钟 ), .\秒2 (in_5), .\时2设 (in_6),
    .\时1设 (in_7), .\分2设 (in_8), .\分1设 (in_9));
  LED_part led_1 (.in(\闹钟_1_闹钟 ));
endmodule
