// Logisim project Fibonacci.circ as structural Verilog: 6 circuits, main circuit main
module main (
  input  [5:0] in_1,
  input  in_2
);

  wire clock_1_out, controller_1_clk, controller_1_clr, controller_1_n_i_1, controller_1_start;
  wire [3:0] display_1_a0, display_1_a1, display_1_a2, display_1_a3, display_1_a4, display_1_a5,
       display_1_a6, display_1_a7, display_1_a8, display_1_a9;
  wire [31:0] fibo_1_fi;

  Clock clock_1 (.out(clock_1_out));
  controller controller_1 (
    .clear(in_2), .clock(clock_1_out), .start(controller_1_start), .N(in_1), .clr(controller_1_clr),
    .n_i_1(controller_1_n_i_1), .clk(controller_1_clk));
  Fibo fibo_1 (
    .start(controller_1_start), .n_i_1(controller_1_n_i_1), .clr(controller_1_clr), .Fi(fibo_1_fi),
    .clk(controller_1_clk));
  Hex_Digit_Display hex_digit_display_1 (.value(display_1_a8));  // open: dp
  Hex_Digit_Display hex_digit_display_2 (.value(display_1_a9));  // open: dp
  display display_1 (
    .Fi(fibo_1_fi), .a0(display_1_a0), .a1(display_1_a1), .a2(display_1_a2), .a3(display_1_a3),
    .a4(display_1_a4), .a5(display_1_a5), .a6(display_1_a6), .a7(display_1_a7), .a8(display_1_a8),
    .a9(display_1_a9));
  Hex_Digit_Display hex_digit_display_3 (.value(display_1_a7));  // open: dp
  Hex_Digit_Display hex_digit_display_4 (.value(display_1_a6));  // open: dp
  Hex_Digit_Display hex_digit_display_5 (.value(display_1_a5));  // open: dp
  Hex_Digit_Display hex_digit_display_6 (.value(display_1_a3));  // open: dp
  Hex_Digit_Display hex_digit_display_7 (.value(display_1_a4));  // open: dp
  Hex_Digit_Display hex_digit_display_8 (.value(display_1_a2));  // open: dp
  Hex_Digit_Display hex_digit_display_9 (.value(display_1_a0));  // open: dp
  Hex_Digit_Display hex_digit_display_10 (.value(display_1_a1));  // open: dp
endmodule

module sqrX (
  input  [31:0] a,
  input  [31:0] b,
  input  [31:0] c,
  input  [31:0] d,
  output [31:0] a1,
  output [31:0] b1,
  output [31:0] c1,
  output [31:0] d1
);

  wire [31:0] multiplier_1_out, multiplier_2_out, multiplier_3_out, multiplier_4_out, multiplier_5_out,
       multiplier_6_out, multiplier_7_out;

  Multiplier #(.width(32)) multiplier_1 (.a(a), .b(a), .out(multiplier_1_out));  // open: cin, cout
  Multiplier #(.width(32)) multiplier_2 (.a(b), .b(c), .out(multiplier_2_out));  // open: cin, cout
  Multiplier #(.width(32)) multiplier_3 (.a(a), .b(b), .out(multiplier_3_out));  // open: cin, cout
  Multiplier #(.width(32)) multiplier_4 (.a(b), .b(d), .out(multiplier_4_out));  // open: cin, cout
  Multiplier #(.width(32)) multiplier_5 (.a(a), .b(c), .out(multiplier_5_out));  // open: cin, cout
  Multiplier #(.width(32)) multiplier_6 (.a(c), .b(d), .out(multiplier_6_out));  // open: cin, cout
  Multiplier #(.width(32)) multiplier_7 (.a(d), .b(d), .out(multiplier_7_out));  // open: cin, cout
  Adder #(.width(32)) adder_1 (.a(multiplier_1_out), .b(multiplier_2_out), .out(a1));  // open: cin, cout
  Adder #(.width(32)) adder_2 (.a(multiplier_3_out), .b(multiplier_4_out), .out(b1));  // open: cin, cout
  Adder #(.width(32)) adder_3 (.a(multiplier_5_out), .b(multiplier_6_out), .out(c1));  // open: cin, cout
  Adder #(.width(32)) adder_4 (.a(multiplier_7_out), .b(multiplier_2_out), .out(d1));  // open: cin, cout
endmodule

module sqrX_A (
  input  [31:0] a,
  input  [31:0] b,
  input  [31:0] c,
  input  [31:0] d,
  output [31:0] a2,
  output [31:0] b2,
  output [31:0] c2,
  output [31:0] d2
);

  wire [31:0] sqrx_1_a1, sqrx_1_b1;

  sqrX sqrx_1 (.a(a), .b(b), .c(c), .d(d), .a1(sqrx_1_a1), .b1(sqrx_1_b1), .c1(a2), .d1(c2));
  Adder #(.width(32)) adder_1 (.a(sqrx_1_a1), .b(sqrx_1_b1), .out(b2));  // open: cin, cout
  Adder #(.width(32)) adder_2 (.a(a2), .b(c2), .out(d2));  // open: cin, cout
endmodule

module Fibo (
  input  start,
  input  n_i_1,
  input  clr,
  input  clk,
  output [31:0] Fi
);

  wire [31:0] multiplexer_1_out, multiplexer_2_out, multiplexer_3_out, multiplexer_4_out, multiplexer_5_out,
       multiplexer_6_out, multiplexer_7_out, multiplexer_8_out, register_1_q, register_3_q, register_4_q,
       sqrx_1_a1, sqrx_1_b1, sqrx_1_c1, sqrx_1_d1, sqrx_a_1_a2, sqrx_a_1_b2, sqrx_a_1_c2, sqrx_a_1_d2;

  Multiplexer #(.width(32), .enable("false")) multiplexer_1 (
    .in0({32{1'b0}}), .in1(multiplexer_5_out), .out(multiplexer_1_out), .sel(start));
  Multiplexer #(.width(32), .enable("false")) multiplexer_2 (
    .in0(32'h1), .in1(multiplexer_6_out), .out(multiplexer_2_out), .sel(start));
  Multiplexer #(.width(32), .enable("false")) multiplexer_3 (
    .in0(32'h1), .in1(multiplexer_7_out), .out(multiplexer_3_out), .sel(start));
  Multiplexer #(.width(32), .enable("false")) multiplexer_4 (
    .in0(32'h1), .in1(multiplexer_8_out), .out(multiplexer_4_out), .sel(start));
  Register #(.width(32)) register_1 (.D(multiplexer_1_out), .Q(register_1_q), .clk(clk), .clr(clr));  // open: en
  Register #(.width(32)) register_2 (.D(multiplexer_2_out), .Q(Fi), .clk(clk), .clr(clr));  // open: en
  Register #(.width(32)) register_3 (.D(multiplexer_3_out), .Q(register_3_q), .clk(clk), .clr(clr));  // open: en
  Register #(.width(32)) register_4 (.D(multiplexer_4_out), .Q(register_4_q), .clk(clk), .clr(clr));  // open: en
  sqrX sqrx_1 (
    .a(register_1_q), .b(Fi), .c(register_3_q), .d(register_4_q), .a1(sqrx_1_a1), .b1(sqrx_1_b1),
    .c1(sqrx_1_c1), .d1(sqrx_1_d1));
  sqrX_A sqrx_a_1 (
    .a(register_1_q), .b(Fi), .c(register_3_q), .d(register_4_q), .a2(sqrx_a_1_a2), .b2(sqrx_a_1_b2),
    .c2(sqrx_a_1_c2), .d2(sqrx_a_1_d2));
  Multiplexer #(.width(32), .enable("false")) multiplexer_5 (
    .in0(sqrx_1_a1), .in1(sqrx_a_1_a2), .out(multiplexer_5_out), .sel(n_i_1));
  Multiplexer #(.width(32), .enable("false")) multiplexer_6 (
    .in0(sqrx_1_b1), .in1(sqrx_a_1_b2), .out(multiplexer_6_out), .sel(n_i_1));
  Multiplexer #(.width(32), .enable("false")) multiplexer_7 (
    .in0(sqrx_1_c1), .in1(sqrx_a_1_c2), .out(multiplexer_7_out), .sel(n_i_1));
  Multiplexer #(.width(32), .enable("false")) multiplexer_8 (
    .in0(sqrx_1_d1), .in1(sqrx_a_1_d2), .out(multiplexer_8_out), .sel(n_i_1));
endmodule

module controller (
  input  [5:0] N,
  input  clear,
  input  clock,
  output start,
  output clr,
  output n_i_1,
  output clk
);

  wire comparator_1_gt, shift_register_1_out, shift_register_1_q5;
  wire [7:0] counter_1_q;

  Shift_Register #(.length(7)) shift_register_1 (
    .shift(1'b1), .in(1'b0), .clk(clock), .out(shift_register_1_out), .load(clear), .clr(1'b0), .d0(N[0]),
    .d1(N[1]), .d2(N[2]), .d3(N[3]), .d4(N[4]), .d5(N[5]), .q5(shift_register_1_q5), .d6(1'b0));  // open: q0, q1, q2, q3, q4, q6
  Counter counter_1 (.count(clock), .Q(counter_1_q), .clk(clock), .clr(clear));  // open: load, D, carry
  Comparator comparator_1 (.a(counter_1_q), .b(8'h5), .gt(comparator_1_gt));  // open: eq, lt
  D_Flip_Flop d_ff_1 (.clk(clear), .D(1'b0), .Q(start), .preset(shift_register_1_out));  // open: Qn, en, reset
  Multiplexer #(.enable("false")) multiplexer_1 (.in0(clock), .in1(1'b0), .out(clk), .sel(comparator_1_gt));
  and and_1 (n_i_1, start, shift_register_1_q5);

  assign clr = clear;
endmodule

module display (
  input  [31:0] Fi,
  output [3:0] a0,
  output [3:0] a1,
  output [3:0] a2,
  output [3:0] a3,
  output [3:0] a4,
  output [3:0] a5,
  output [3:0] a6,
  output [3:0] a7,
  output [3:0] a8,
  output [3:0] a9
);

  wire [31:0] divider_1_out, divider_2_out, divider_3_out, divider_4_out, divider_5_out, divider_6_out,
       divider_7_out, divider_8_out, divider_9_out;
  wire [31:4] divider_1_rem, divider_2_rem, divider_3_rem, divider_4_rem, divider_5_rem, divider_6_rem,
       divider_7_rem, divider_8_rem, divider_9_rem, divider_10_rem;

  Divider #(.width(32)) divider_1 (.a(Fi), .b(32'ha), .out(divider_1_out), .rem({divider_1_rem, a0}));  // open: upper
  Divider #(.width(32)) divider_2 (
    .a(divider_1_out), .b(32'ha), .out(divider_2_out), .rem({divider_2_rem, a1}));  // open: upper
  Divider #(.width(32)) divider_3 (
    .a(divider_2_out), .b(32'ha), .out(divider_3_out), .rem({divider_3_rem, a2}));  // open: upper
  Divider #(.width(32)) divider_4 (
    .a(divider_3_out), .b(32'ha), .out(divider_4_out), .rem({divider_4_rem, a3}));  // open: upper
  Divider #(.width(32)) divider_5 (
    .a(divider_4_out), .b(32'ha), .out(divider_5_out), .rem({divider_5_rem, a4}));  // open: upper
  Divider #(.width(32)) divider_6 (
    .a(divider_5_out), .b(32'ha), .out(divider_6_out), .rem({divider_6_rem, a5}));  // open: upper
  Divider #(.width(32)) divider_7 (
    .a(divider_6_out), .b(32'ha), .out(divider_7_out), .rem({divider_7_rem, a6}));  // open: upper
  Divider #(.width(32)) divider_8 (
    .a(divider_7_out), .b(32'ha), .out(divider_8_out), .rem({divider_8_rem, a7}));  // open: upper
  Divider #(.width(32)) divider_9 (
    .a(divider_8_out), .b(32'ha), .out(divider_9_out), .rem({divider_9_rem, a8}));  // open: upper
  Divider #(.width(32)) divider_10 (.a(divider_9_out), .b(32'ha), .rem({divider_10_rem, a9}));  // open: out, upper
endmodule
